// Logisim project cpu24.circ as structural Verilog: 34 circuits, main circuit ◇单周期MIPS
module \单周期MIPS  (
  output RegWrite,
  output MemWrite,
  output [31:0] PC,
  output [31:0] IR,
  output [31:0] RDin,
  output [31:0] MDin,
  output [31:0] out_7
);

  wire and_1_out, and_2_out, BEQ, BLTZ, BNE, CLK, comparator_1_eq, comparator_2_eq, EN, Go, IR1, IR2, IR3,
       JAL, JMP, JR, LB, LUI, multiplexer_1_out, multiplexer_16_out, not_1_out, not_2_out, not_3_out, Pause,
       SignedExt, syscall, tunnel, W1, W2, W3, \单周期硬布线控制器_1_alu_src , \单周期硬布线控制器_1_memtoreg ,
       \单周期硬布线控制器_1_regdst ;
  wire [3:0] \单周期硬布线控制器_1_alu_op ;
  wire [4:0] multiplexer_2_out, multiplexer_3_out, multiplexer_4_out, multiplexer_6_out, multiplexer_7_out,
       multiplexer_10_out;
  wire [7:0] multiplexer_15_out;
  wire [15:0] \总周期数 ;
  wire [31:0] a0, adder_2_out, bit_extender_1_out, bit_extender_2_out, bit_extender_3_out, BLTZ_result,
       JRaddr, \j型指令转跳地址判断器_1_out_12 , multiplexer_5_out, multiplexer_9_out, multiplexer_12_out,
       multiplexer_14_out, multiplexer_17_out, PC_4, ram_1_data, shifter_1_out, v0;

  Clock #(.highDuration(1), .lowDuration(1)) clock_1 (.out(CLK));
  Button _1 (.out(IR1));
  Button _2 (.out(IR2));
  Button _3 (.out(IR3));
  // Probe on \j型指令转跳地址判断器_1_out_12 
  Button \u_继续运行  (.out(Go));
  LED #(.active("true")) led_1 (.in(W1));
  LED #(.active("true")) led_2 (.in(W2));
  LED #(.active("true")) led_3 (.in(W3));
  not not_1 (not_1_out, Pause);
  Counter #(.width(16), .max('hffff), .ongoal("wrap"), .trigger("rising"), .behavior("old")) counter_1 (
    .count(not_1_out), .Q(\总周期数 ), .clk(CLK), .clr(1'b0));  // open: load, D, carry, preset
  Register #(.width(32), .trigger("rising"), .Select("low")) u_PC (
    .D(\j型指令转跳地址判断器_1_out_12 ), .en(not_1_out), .Q(PC), .clk(CLK), .clr(1'b0));
  \J型指令转跳地址判断器  \j型指令转跳地址判断器_1  (
    .JR(JR), .JMP(JMP), .BNE(BNE), .in_2(tunnel), .BEQ(BEQ), .JAL(JAL), .BLTZ(multiplexer_1_out),
    .out_12(\j型指令转跳地址判断器_1_out_12 ), .PC_4(PC_4), .BNE_BEQ_BLTZaddr(adder_2_out),
    .J_JALaddr({PC[31:28], IR[25:0], 2'b00}), .JRaddr(JRaddr));  // open: 转跳信号灯
  Hex_Digit_Display hex_digit_display_1 (.value(out_7[31:28]));  // open: dp
  Adder #(.width(32)) adder_1 (.a(PC), .b(32'h4), .out(PC_4));  // open: cin, cout
  Multiplexer #(.select(1), .width(1), .disabled("Z"), .enable("false")) multiplexer_1 (
    .in0(1'b0), .in1(BLTZ), .out(multiplexer_1_out), .sel(comparator_1_eq));
  Comparator #(.width(32), .mode("unsigned")) comparator_1 (
    .a(BLTZ_result), .b(32'h1), .eq(comparator_1_eq));  // open: gt, lt
  Hex_Digit_Display hex_digit_display_2 (.value(out_7[23:20]));  // open: dp
  Hex_Digit_Display hex_digit_display_3 (.value(out_7[27:24]));  // open: dp
  // Probe on PC_4
  // Probe on JRaddr
  Hex_Digit_Display hex_digit_display_4 (.value(out_7[19:16]));  // open: dp
  Hex_Digit_Display hex_digit_display_5 (.value(out_7[15:12]));  // open: dp
  // Probe on IR
  ROM #(.addrWidth(10), .dataWidth(32), .Select("high")) rom_1 (.addr(PC[11:2]), .data(IR));
  // Probe on {PC[31:28], IR[25:0], 2'b00}
  Hex_Digit_Display hex_digit_display_6 (.value(out_7[11:8]));  // open: dp
  Hex_Digit_Display hex_digit_display_7 (.value(out_7[7:4]));  // open: dp
  // Probe on \总周期数 
  // Probe on IR[25:21]
  // Probe on IR[20:16]
  // Probe on IR[15:11]
  // Probe on IR[10:6]
  Hex_Digit_Display hex_digit_display_8 (.value(out_7[3:0]));  // open: dp
  // Probe on \总周期数 
  \单周期硬布线控制器  \u_单周期硬布线控制器_1  (
    .ALU_OP(\单周期硬布线控制器_1_alu_op ), .MemToReg(\单周期硬布线控制器_1_memtoreg ), .MemWrite(MemWrite),
    .ALU_SRC(\单周期硬布线控制器_1_alu_src ), .RegWrite(RegWrite), .SysCALL(syscall), .SignedExt(SignedExt),
    .RegDst(\单周期硬布线控制器_1_regdst ), .JR(JR), .JMP(JMP), .Beq(BEQ), .JAL(JAL), .Bne(BNE), .LUI(LUI),
    .BLTZ(BLTZ), .LB(LB), .IR(IR));  // open: ERET, 关中断, 开中断
  assign bit_extender_1_out = {{16{IR[15]}}, IR[15:0]};  // Bit_Extender bit_extender_1
  assign bit_extender_2_out = {{16{1'b0}}, IR[15:0]};  // Bit_Extender bit_extender_2
  // Probe on adder_2_out
  Multiplexer #(.select(1), .width(5), .disabled("Z"), .enable("false")) multiplexer_2 (
    .in0(IR[25:21]), .in1({5{1'b1}}), .out(multiplexer_2_out), .sel(JR));
  Multiplexer #(.select(1), .width(5), .disabled("Z"), .enable("false")) multiplexer_3 (
    .in0(IR[20:16]), .in1(5'b00100), .out(multiplexer_3_out), .sel(syscall));
  Multiplexer #(.select(1), .width(5), .disabled("Z"), .enable("false")) multiplexer_4 (
    .in0(IR[20:16]), .in1(IR[15:11]), .out(multiplexer_4_out), .sel(\单周期硬布线控制器_1_regdst ));
  Multiplexer #(.select(1), .width(32), .disabled("Z"), .enable("false")) multiplexer_5 (
    .in0(bit_extender_1_out), .in1(bit_extender_2_out), .out(multiplexer_5_out), .sel(SignedExt));
  Multiplexer #(.select(1), .width(5), .disabled("Z"), .enable("false")) multiplexer_6 (
    .in0(multiplexer_2_out), .in1(5'b00010), .out(multiplexer_6_out), .sel(syscall));
  Multiplexer #(.select(1), .width(5), .disabled("Z"), .enable("false")) multiplexer_7 (
    .in0(multiplexer_4_out), .in1({5{1'b1}}), .out(multiplexer_7_out), .sel(JAL));
  // Probe on RDin
  // Probe on multiplexer_5_out
  Multiplexer #(.select(1), .width(32), .disabled("Z"), .enable("false")) multiplexer_8 (
    .in0(multiplexer_12_out), .in1(PC_4), .out(RDin), .sel(JAL));
  // Probe on JRaddr
  MIPS_Regifile mips_regifile_1 (
    .Din(RDin), .Clk(CLK), .R1(JRaddr), .R2(MDin), .WE(RegWrite), .W_num(multiplexer_7_out),
    .R1_num(multiplexer_6_out), .R2_num(multiplexer_3_out));
  // Probe on MDin
  Multiplexer #(.select(1), .width(32), .disabled("Z"), .enable("false")) multiplexer_9 (
    .in0(MDin), .in1(multiplexer_5_out), .out(multiplexer_9_out), .sel(\单周期硬布线控制器_1_alu_src ));
  Shifter #(.width(32), .shift("ll")) shifter_1 (.in(multiplexer_5_out), .\dist (5'b00010), .out(shifter_1_out));
  Multiplexer #(.select(1), .width(5), .disabled("Z"), .enable("false")) multiplexer_10 (
    .in0(IR[10:6]), .in1(5'b10000), .out(multiplexer_10_out), .sel(LUI));
  Adder #(.width(32)) adder_2 (.a(shifter_1_out), .b(PC_4), .out(adder_2_out));  // open: cin, cout
  // Probe on \单周期硬布线控制器_1_alu_op 
  MIPS_ALU mips_alu_1 (
    .X(JRaddr), .Y(multiplexer_9_out), .AluOP(\单周期硬布线控制器_1_alu_op ), .Equal(tunnel), .Result(BLTZ_result),
    .shamt(multiplexer_10_out));  // open: Result_2
  Multiplexer #(.select(1), .width(32), .disabled("Z"), .enable("false")) multiplexer_11 (
    .in0({32{1'b0}}), .in1(JRaddr), .out(v0), .sel(syscall));
  // Probe on BLTZ_result
  Multiplexer #(.select(1), .width(32), .disabled("Z"), .enable("false")) multiplexer_12 (
    .in0(multiplexer_14_out), .in1(bit_extender_3_out), .out(multiplexer_12_out), .sel(LB));
  and and_1 (and_1_out, MemWrite, not_2_out);
  Multiplexer #(.select(1), .width(32), .disabled("Z"), .enable("false")) multiplexer_13 (
    .in0({32{1'b0}}), .in1(MDin), .out(a0), .sel(syscall));
  RAM #(.addrWidth(10), .dataWidth(32), .bus("separate"), .Select("high")) ram_1 (
    .addr({2'b00, BLTZ_result[9:2]}), .din(MDin), .data(ram_1_data), .str(and_1_out), .clk(CLK),
    .ld(not_2_out), .clr(1'b0));  // open: sel
  not not_2 (not_2_out, syscall);
  Multiplexer #(.select(1), .width(32), .disabled("Z"), .enable("false")) multiplexer_14 (
    .in0(BLTZ_result), .in1(ram_1_data), .out(multiplexer_14_out), .sel(\单周期硬布线控制器_1_memtoreg ));
  Multiplexer #(.select(2), .width(8), .disabled("Z"), .enable("false")) multiplexer_15 (
    .in0(multiplexer_14_out[7:0]), .in1(multiplexer_14_out[15:8]), .in2(multiplexer_14_out[23:16]),
    .in3(multiplexer_14_out[31:24]), .out(multiplexer_15_out), .sel(BLTZ_result[1:0]));
  Comparator #(.width(32), .mode("unsigned")) comparator_2 (.a(v0), .b(32'ha), .eq(comparator_2_eq));  // open: gt, lt
  not not_3 (not_3_out, comparator_2_eq);
  assign bit_extender_3_out = {{24{multiplexer_15_out[7]}}, multiplexer_15_out};  // Bit_Extender bit_extender_3
  Multiplexer #(.select(1), .width(1), .disabled("Z"), .enable("false")) multiplexer_16 (
    .in0(1'b0), .in1(Go), .out(multiplexer_16_out), .sel(comparator_2_eq));
  xor xor_1 (Pause, comparator_2_eq, multiplexer_16_out);
  not not_4 (EN, Pause);
  and and_2 (and_2_out, syscall, not_3_out);
  Multiplexer #(.select(1), .width(32), .disabled("Z"), .enable("false")) multiplexer_17 (
    .in0(out_7), .in1(a0), .out(multiplexer_17_out), .sel(and_2_out));
  Register #(.width(32), .trigger("rising"), .Select("low")) register_1 (
    .D(multiplexer_17_out), .Q(out_7), .clk(CLK));  // open: en, clr

  // Other names for the same wires on the sheet: LB取数据地址低2位[1:0] = BLTZ_result[1:0];
  //   Jaddr[31:2] = {PC[31:28], IR[25:0]}; shamt[4:0] = IR[10:6]; LedData[31:0] = out_7; R1[31:0] = JRaddr;
  //   R2[31:0] = MDin

  // Notes on the sheet:
  //   中断源
  //   中断等待指示
  //   总复位信号应将除ROM以外所有存储组件全部清零
  //   SLTIU：rt<---(rs<imm)
  //   指令存储器
  //   数码管输出
  //   指令字
  //   contents of rom_1 (hex, n*v repeats v):
  //   20110001 8000c05 20110001 20120002 20130003 8000c09 20110001 20120002 20130003 8000c0d 20110001
  //   20120002 20130003 8000c11 20110001 20120002 20130003 c000cf6 20100001 20110001 118fc0 112020
  //   20020022 c 118882 12200001 8000c15 112020 20020022 c 20110001 118880 112020 20020022 c 12200001
  //   8000c1f 20110001 118fc0 112020 20020022 c 1188c3 112020 20020022 c 118903 112020 20020022 c 118903
  //   112020 20020022 c 118903 112020 20020022 c 118903 112020 20020022 c 118903 112020 20020022 c 118903
  //   112020 20020022 c 118903 112020 20020022 c 20100001 109fc0 139fc3 8021 2012000c 24160003 26100001
  //   3210000f 20080008 20090001 139900 2709825 132020 20020022 c 1094022 1500fff9 22100001 2018000f
  //   2188024 108700 20080008 20090001 139902 2709825 132021 20020022 c 1094022 1500fff9 108702 2c9b022
  //   12c00001 8000c50 4020 1084027 84400 3508ffff 82021 20020022 c 2010ffff 20110000 ae300000 22100001
  //   22310004 ae300000 22100001 22310004 ae300000 22100001 22310004 ae300000 22100001 22310004 ae300000
  //   22100001 22310004 ae300000 22100001 22310004 ae300000 22100001 22310004 ae300000 22100001 22310004
  //   ae300000 22100001 22310004 ae300000 22100001 22310004 ae300000 22100001 22310004 ae300000 22100001
  //   22310004 ae300000 22100001 22310004 ae300000 22100001 22310004 ae300000 22100001 22310004 ae300000
  //   22100001 22310004 22100001 8020 2011003c 8e130000 8e340000 274402a 11000002 ae330000 ae140000
  //   2231fffc 1611fff8 102020 20020022 c 22100004 2011003c 1611fff2 2002000a c 200b0008 3c11fedc 3631ffff
  //   112020 20020022 c 3c11ba98 112020 c 3c117654 112020 c 3c113210 112020 c 216bffff 1560fff0 2002000a c
  //   2008ffff 20090000 20111997 112020 20020022 c 2288820 2e291949 1120fffa 2002000a c 20090000 200b0010
  //   34118483 20120404 118c00 129400 36318281 22520404 ad310000 2328820 21290004 216bffff 1560fffb
  //   200b0020 20090000 81310000 112020 20020022 c 21290001 216bffff 1560fff9 2002000a c 2011fff1 112020
  //   20020022 c 22310001 620fffb 2002000a c 20100000 22100001 102020 20020022 c 22100002 102020 20020022
  //   c 22100003 102020 20020022 c 22100004 102020 20020022 c 22100005 102020 20020022 c 22100006 102020
  //   20020022 c 22100007 102020 20020022 c 22100008 102020 20020022 20020022 c 3e00008
  //   数码管输出应该用寄存器锁存，否则显示数据只能一闪而过
  //   JMP
  //   JR
  //   rs
  //   rt
  //   rd
  //   imm
  //   BLTZ：和BNE、BEQ类似，imm左移两位作为偏移量加当前地址，当且仅当ALU比较结果为1时work。ALU的B口默认为寄存器$0==0，验证正确
  //   Beq
  //   Bne
  //   LB
  //   MemToReg
  //   MemWrite
  //   AluOP
  //   AluSrcB
  //   RegWrite
  //   JAL
  //   RegDst
  //   Syscall
  //   $a0
  //   $v0
  //   为方便自动评测，需要输出PC，IR，寄存器文件写入端口RDin，内存写入端口MDin等信号
  //   SignedExt到底有啥用？？
  //   LUI：imm左移16位，送入rt对应寄存器，验证正确
  //   LB：数据寄存器地址：base+imm，取出数据后根据地址低两位选择八位数据，扩展成32位
endmodule

module \单周期MIPS_单级中断  (
  input  IR1,
  input  IR2,
  input  IR3,
  output RegWrite,
  output MemWrite,
  output [31:0] PC,
  output [31:0] IR,
  output [31:0] RDin,
  output [31:0] MDin,
  output [31:0] LedData
);

  wire _1_out, \_1号中断清零信号 , _2_out, \_2号中断清零信号 , _3_out, \_3号中断清零信号 , and_6_out, and_7_out, BEQ, BLTZ, BNE,
       CLK, comparator_1_eq, comparator_2_eq, comparator_3_eq, comparator_4_eq, comparator_5_eq,
       comparator_6_eq, demultiplexer_1_out1, demultiplexer_1_out2, demultiplexer_1_out3, EN, ERET, Go, IE,
       IR1_t, IR2_t, IR3_t, IRA, IRB, IRC, JAL, JMP, JR, LB, LUI, multiplexer_4_out, multiplexer_18_out,
       not_1_out, or_5_out, Pause, priority_encoder_1_gs, SignedExt, syscall, tunnel, W1, W2, W3, \中断信号 ,
       \中断信息记录信号 , \中断按键参考电路_1__1号与中断屏蔽位与 , \中断按键参考电路_1__2号与中断屏蔽位与 , \中断按键参考电路_1__3号与中断屏蔽位与 , \中断清零信号 ,
       \单周期硬布线控制器_1_alu_src , \单周期硬布线控制器_1_memtoreg , \单周期硬布线控制器_1_regdst ;
  wire [1:0] multiplexer_3_out, priority_encoder_1_out, \中断编号 ;
  wire [3:0] \单周期硬布线控制器_1_alu_op ;
  wire [4:0] multiplexer_5_out, multiplexer_6_out, multiplexer_7_out, multiplexer_8_out, multiplexer_9_out,
       multiplexer_14_out;
  wire [7:0] multiplexer_19_out;
  wire [15:0] \总周期数 ;
  wire [31:0] a0, adder_2_out, bit_extender_1_out, bit_extender_2_out, bit_extender_3_out, BLTZ_result, EPC,
       JRaddr, multiplexer_1_out, multiplexer_2_out, multiplexer_10_out, multiplexer_12_out,
       multiplexer_16_out, multiplexer_17_out, multiplexer_20_out, PC_4, ram_1_data, shifter_1_out, v0,
       \正常程序地址 ;

  Clock #(.highDuration(1), .lowDuration(1)) clock_1 (.out(CLK));
  Button _1 (.out(_1_out));
  Button _2 (.out(_2_out));
  Button _3 (.out(_3_out));
  Button \u_继续运行  (.out(Go));
  LED #(.active("true")) led_1 (.in(W1));
  LED #(.active("true")) led_2 (.in(W2));
  LED #(.active("true")) led_3 (.in(W3));
  and and_1 (\_1号中断清零信号 , demultiplexer_1_out1, ERET);
  and and_2 (\_2号中断清零信号 , demultiplexer_1_out2, ERET);
  and and_3 (\_3号中断清零信号 , demultiplexer_1_out3, ERET);
  Hex_Digit_Display hex_digit_display_1 (.value(LedData[31:28]));  // open: dp
  \中断按键参考电路  \u_中断按键参考电路_1  (
    .\_1号同步清零信号 (\_1号中断清零信号 ), .\_1号中断 (IR1_t), .CLK(CLK), .\_1号中断等待指示灯 (W1), .\_2号中断 (IR2_t),
    .\_2号中断等待指示灯 (W2), .\_3号中断 (IR3_t), .\_3号中断等待指示灯 (W3), .\_2号同步清零信号 (\_2号中断清零信号 ),
    .\_3号同步清零信号 (\_3号中断清零信号 ), .\_1号与中断屏蔽位与 (\中断按键参考电路_1__1号与中断屏蔽位与 ),
    .\_2号与中断屏蔽位与 (\中断按键参考电路_1__2号与中断屏蔽位与 ), .\_3号与中断屏蔽位与 (\中断按键参考电路_1__3号与中断屏蔽位与 ));
  Hex_Digit_Display hex_digit_display_2 (.value(LedData[23:20]));  // open: dp
  Hex_Digit_Display hex_digit_display_3 (.value(LedData[27:24]));  // open: dp
  Multiplexer #(.select(1), .width(32), .disabled("Z"), .enable("false")) multiplexer_1 (
    .in0(\正常程序地址 ), .in1(EPC), .out(multiplexer_1_out), .sel(ERET));
  Priority_Encoder #(.select(2), .disabled("Z")) priority_encoder_1 (
    .in0(1'b0), .in1(\中断按键参考电路_1__1号与中断屏蔽位与 ), .in2(\中断按键参考电路_1__2号与中断屏蔽位与 ), .in3(\中断按键参考电路_1__3号与中断屏蔽位与 ),
    .out(priority_encoder_1_out), .gs(priority_encoder_1_gs));  // open: en_out, en_in
  Hex_Digit_Display hex_digit_display_4 (.value(LedData[19:16]));  // open: dp
  Hex_Digit_Display hex_digit_display_5 (.value(LedData[15:12]));  // open: dp
  Demultiplexer #(.select(2), .width(1), .tristate("false"), .disabled("Z"), .enable("false")) demultiplexer_1 (
    .out1(demultiplexer_1_out1), .out2(demultiplexer_1_out2), .out3(demultiplexer_1_out3), .in(1'b1),
    .sel(\中断编号 ));  // open: out0
  Multiplexer #(.select(2), .width(32), .disabled("Z"), .enable("false")) multiplexer_2 (
    .in0(multiplexer_1_out), .in1(32'h30ac), .in2(32'h3150), .in3(32'h31f4), .out(multiplexer_2_out),
    .sel(multiplexer_3_out));
  Multiplexer #(.select(1), .width(2), .disabled("Z"), .enable("false")) multiplexer_3 (
    .in0(2'b00), .in1(priority_encoder_1_out), .out(multiplexer_3_out), .sel(\中断信息记录信号 ));
  and and_4 (\中断信号 , priority_encoder_1_gs, ~IE);  // AND_Gate
  Hex_Digit_Display hex_digit_display_6 (.value(LedData[11:8]));  // open: dp
  Hex_Digit_Display hex_digit_display_7 (.value(LedData[7:4]));  // open: dp
  // Probe on \总周期数 
  // Probe on multiplexer_2_out
  Hex_Digit_Display hex_digit_display_8 (.value(LedData[3:0]));  // open: dp
  // Probe on \总周期数 
  Register #(.width(2), .trigger("rising"), .Select("low")) \u_中断编号  (
    .D(multiplexer_3_out), .en(\中断信息记录信号 ), .Q(\中断编号 ), .clk(CLK));  // open: clr
  or or_1 (\中断清零信号 , \_1号中断清零信号 , \_2号中断清零信号 , \_3号中断清零信号 );
  // Probe on \正常程序地址 
  or or_2 (IR1_t, IR1, IRA);
  and and_5 (\中断信息记录信号 , \中断信号 , ~\中断清零信号 );  // AND_Gate
  Counter #(.width(16), .max('hffff), .ongoal("wrap"), .trigger("rising"), .behavior("old")) counter_1 (
    .count(EN), .Q(\总周期数 ), .clk(CLK), .clr(1'b0));  // open: load, D, carry, preset
  Register #(.width(32), .trigger("rising"), .Select("low")) u_PC (
    .D(multiplexer_2_out), .en(EN), .Q(PC), .clk(CLK), .clr(1'b0));
  \J型指令转跳地址判断器  \j型指令转跳地址判断器_1  (
    .JR(JR), .JMP(JMP), .BNE(BNE), .in_2(tunnel), .BEQ(BEQ), .JAL(JAL), .BLTZ(multiplexer_4_out),
    .out_12(\正常程序地址 ), .PC_4(PC_4), .BNE_BEQ_BLTZaddr(adder_2_out), .J_JALaddr({PC[31:28], IR[25:0], 2'b00}),
    .JRaddr(JRaddr));  // open: 转跳信号灯
  Multiplexer #(.select(1), .width(1), .disabled("Z"), .enable("false")) multiplexer_4 (
    .in0(1'b0), .in1(BLTZ), .out(multiplexer_4_out), .sel(comparator_1_eq));
  Comparator #(.width(32), .mode("unsigned")) comparator_1 (
    .a(BLTZ_result), .b(32'h1), .eq(comparator_1_eq));  // open: gt, lt
  or or_3 (IR2_t, IR2, IRB);
  Adder #(.width(32)) adder_1 (.a(PC), .b(32'h4), .out(PC_4));  // open: cin, cout
  // Probe on PC_4
  // Probe on JRaddr
  LED #(.active("true")) led_4 (.in(ERET));
  ROM #(.addrWidth(10), .dataWidth(32), .Select("high")) rom_1 (.addr(PC[11:2]), .data(IR));
  or or_4 (IR3_t, IR3, IRC);
  // Probe on IR
  // Probe on IR[25:21]
  // Probe on IR[10:6]
  // Probe on {PC[31:28], IR[25:0], 2'b00}
  \单周期硬布线控制器  \u_单周期硬布线控制器_1  (
    .ALU_OP(\单周期硬布线控制器_1_alu_op ), .MemToReg(\单周期硬布线控制器_1_memtoreg ), .MemWrite(MemWrite),
    .ALU_SRC(\单周期硬布线控制器_1_alu_src ), .RegWrite(RegWrite), .SysCALL(syscall), .SignedExt(SignedExt),
    .RegDst(\单周期硬布线控制器_1_regdst ), .JR(JR), .JMP(JMP), .Beq(BEQ), .JAL(JAL), .Bne(BNE), .LUI(LUI),
    .BLTZ(BLTZ), .LB(LB), .ERET(ERET), .IR(IR));  // open: 关中断, 开中断
  // Probe on IR[20:16]
  // Probe on IR[15:11]
  // Probe on adder_2_out
  Multiplexer #(.select(1), .width(5), .disabled("Z"), .enable("false")) multiplexer_5 (
    .in0(IR[25:21]), .in1({5{1'b1}}), .out(multiplexer_5_out), .sel(JR));
  Multiplexer #(.select(1), .width(5), .disabled("Z"), .enable("false")) multiplexer_6 (
    .in0(IR[20:16]), .in1(IR[15:11]), .out(multiplexer_6_out), .sel(\单周期硬布线控制器_1_regdst ));
  assign bit_extender_1_out = {{16{IR[15]}}, IR[15:0]};  // Bit_Extender bit_extender_1
  assign bit_extender_2_out = {{16{1'b0}}, IR[15:0]};  // Bit_Extender bit_extender_2
  Multiplexer #(.select(1), .width(5), .disabled("Z"), .enable("false")) multiplexer_7 (
    .in0(multiplexer_5_out), .in1(5'b00010), .out(multiplexer_7_out), .sel(syscall));
  Multiplexer #(.select(1), .width(5), .disabled("Z"), .enable("false")) multiplexer_8 (
    .in0(IR[20:16]), .in1(5'b00100), .out(multiplexer_8_out), .sel(syscall));
  Multiplexer #(.select(1), .width(5), .disabled("Z"), .enable("false")) multiplexer_9 (
    .in0(multiplexer_6_out), .in1({5{1'b1}}), .out(multiplexer_9_out), .sel(JAL));
  Multiplexer #(.select(1), .width(32), .disabled("Z"), .enable("false")) multiplexer_10 (
    .in0(bit_extender_1_out), .in1(bit_extender_2_out), .out(multiplexer_10_out), .sel(SignedExt));
  // Probe on RDin
  Multiplexer #(.select(1), .width(32), .disabled("Z"), .enable("false")) multiplexer_11 (
    .in0(multiplexer_16_out), .in1(PC_4), .out(RDin), .sel(JAL));
  MIPS_Regifile mips_regifile_1 (
    .Din(RDin), .Clk(CLK), .R1(JRaddr), .R2(MDin), .WE(RegWrite), .W_num(multiplexer_9_out),
    .R1_num(multiplexer_7_out), .R2_num(multiplexer_8_out));
  // Probe on multiplexer_10_out
  // Probe on PC_4
  Register #(.width(1), .trigger("rising"), .Select("low")) u_IE (
    .D(\中断信号 ), .en(\中断信息记录信号 ), .Q(IE), .clk(CLK), .clr(ERET));
  // Probe on JRaddr
  // Probe on MDin
  Shifter #(.width(32), .shift("ll")) shifter_1 (.in(multiplexer_10_out), .\dist (5'b00010), .out(shifter_1_out));
  Multiplexer #(.select(1), .width(32), .disabled("Z"), .enable("false")) multiplexer_12 (
    .in0(MDin), .in1(multiplexer_10_out), .out(multiplexer_12_out), .sel(\单周期硬布线控制器_1_alu_src ));
  Adder #(.width(32)) adder_2 (.a(shifter_1_out), .b(PC_4), .out(adder_2_out));  // open: cin, cout
  Multiplexer #(.select(1), .width(32), .disabled("Z"), .enable("false")) multiplexer_13 (
    .in0({32{1'b0}}), .in1(JRaddr), .out(v0), .sel(syscall));
  Register #(.width(32), .trigger("rising"), .Select("low")) u_EPC (
    .D(\正常程序地址 ), .en(\中断信息记录信号 ), .Q(EPC), .clk(CLK));  // open: clr
  // Probe on \单周期硬布线控制器_1_alu_op 
  MIPS_ALU mips_alu_1 (
    .X(JRaddr), .Y(multiplexer_12_out), .AluOP(\单周期硬布线控制器_1_alu_op ), .Equal(tunnel), .Result(BLTZ_result),
    .shamt(multiplexer_14_out));  // open: Result_2
  Multiplexer #(.select(1), .width(5), .disabled("Z"), .enable("false")) multiplexer_14 (
    .in0(IR[10:6]), .in1(5'b10000), .out(multiplexer_14_out), .sel(LUI));
  // Probe on multiplexer_16_out
  Multiplexer #(.select(1), .width(32), .disabled("Z"), .enable("false")) multiplexer_15 (
    .in0({32{1'b0}}), .in1(MDin), .out(a0), .sel(syscall));
  // Probe on BLTZ_result
  Multiplexer #(.select(1), .width(32), .disabled("Z"), .enable("false")) multiplexer_16 (
    .in0(multiplexer_17_out), .in1(bit_extender_3_out), .out(multiplexer_16_out), .sel(LB));
  and and_6 (and_6_out, MemWrite, EN);
  Comparator #(.width(32), .mode("unsigned")) comparator_2 (.a(v0), .b(32'ha), .eq(comparator_2_eq));  // open: gt, lt
  not not_1 (not_1_out, comparator_2_eq);
  Multiplexer #(.select(1), .width(32), .disabled("Z"), .enable("false")) multiplexer_17 (
    .in0(BLTZ_result), .in1(ram_1_data), .out(multiplexer_17_out), .sel(\单周期硬布线控制器_1_memtoreg ));
  RAM #(.addrWidth(10), .dataWidth(32), .bus("separate"), .Select("high")) ram_1 (
    .addr({2'b00, BLTZ_result[9:2]}), .din(MDin), .data(ram_1_data), .str(and_6_out), .clk(CLK), .ld(EN),
    .clr(1'b0));  // open: sel
  // Probe on multiplexer_17_out
  // Probe on bit_extender_3_out
  xor xor_1 (Pause, comparator_2_eq, multiplexer_18_out);
  Multiplexer #(.select(1), .width(1), .disabled("Z"), .enable("false")) multiplexer_18 (
    .in0(1'b0), .in1(Go), .out(multiplexer_18_out), .sel(comparator_2_eq));
  Multiplexer #(.select(2), .width(8), .disabled("Z"), .enable("false")) multiplexer_19 (
    .in0(multiplexer_17_out[7:0]), .in1(multiplexer_17_out[15:8]), .in2(multiplexer_17_out[23:16]),
    .in3(multiplexer_17_out[31:24]), .out(multiplexer_19_out), .sel(BLTZ_result[1:0]));
  not not_2 (EN, Pause);
  assign bit_extender_3_out = {{24{multiplexer_19_out[7]}}, multiplexer_19_out};  // Bit_Extender bit_extender_3
  and and_7 (and_7_out, syscall, not_1_out);
  Comparator #(.width(16), .mode("twosComplement")) comparator_3 (
    .a(16'h23b), .b(\总周期数 ), .eq(comparator_3_eq));  // open: gt, lt
  Comparator #(.width(16), .mode("twosComplement")) comparator_4 (
    .a(\总周期数 ), .b(16'h1), .eq(comparator_4_eq));  // open: gt, lt
  Comparator #(.width(16), .mode("twosComplement")) comparator_5 (
    .a(\总周期数 ), .b(16'h4), .eq(comparator_5_eq));  // open: gt, lt
  Comparator #(.width(16), .mode("twosComplement")) comparator_6 (
    .a(\总周期数 ), .b(16'h7), .eq(comparator_6_eq));  // open: gt, lt
  Register #(.width(32), .trigger("rising"), .Select("low")) register_1 (
    .D(multiplexer_20_out), .Q(LedData), .clk(CLK));  // open: en, clr
  Multiplexer #(.select(1), .width(32), .disabled("Z"), .enable("false")) multiplexer_20 (
    .in0(LedData), .in1(a0), .out(multiplexer_20_out), .sel(and_7_out));
  or or_5 (or_5_out, comparator_3_eq, comparator_4_eq);
  assign IRA = or_5_out ? ~CLK : 1'bz;  // Controlled_Inverter controlled_inverter_1
  assign IRB = comparator_5_eq ? ~CLK : 1'bz;  // Controlled_Inverter controlled_inverter_2
  assign IRC = comparator_6_eq ? ~CLK : 1'bz;  // Controlled_Inverter controlled_inverter_3
  Pull_Resistor #(.pull(0)) pull_resistor_1 (.node(IRA));
  Pull_Resistor #(.pull(0)) pull_resistor_2 (.node(IRB));
  Pull_Resistor #(.pull(0)) pull_resistor_3 (.node(IRC));

  // Other names for the same wires on the sheet: LB取数据地址低2位[1:0] = BLTZ_result[1:0];
  //   Jaddr[31:2] = {PC[31:28], IR[25:0]}; shamt[4:0] = IR[10:6]; R1[31:0] = JRaddr; R2[31:0] = MDin

  // Notes on the sheet:
  //   中断源
  //   中断等待指示
  //   总复位信号应将除ROM以外所有存储组件全部清零
  //   数码管输出
  //   数码管输出应该用寄存器锁存，否则显示数据只能一闪而过
  //   指令存储器
  //   指令字
  //   contents of rom_1 (hex, n*v repeats v):
  //   201d07d0 20100001 109fc0 139fc3 8021 2012000c 24160008 26100001 3210000f 20080008 20090001 139900
  //   2709825 132020 20020022 c 1094022 1500fff9 22100001 2018000f 2188024 108700 20080008 20090001 139902
  //   2709825 132021 20020022 c 1094022 1500fff9 108702 2c9b022 12c00001 8000c07 4020 1084027 84400
  //   3508ffff 82021 20020022 c 8000c01 afa20000 23bd0004 afa40000 23bd0004 afb00000 23bd0004 afb30000
  //   23bd0004 afb40000 23bd0004 afb50000 23bd0004 afb60000 23bd0004 20160001 20140003 20150001 168020
  //   108100 2149825 132020 20020022 c 1600fffa 295a022 1680fff7 23bdfffc 8fb60000 23bdfffc 8fb50000
  //   23bdfffc 8fb40000 23bdfffc 8fb30000 23bdfffc 8fb00000 23bdfffc 8fa40000 23bdfffc 8fa20000 42000018
  //   afa20000 23bd0004 afa40000 23bd0004 afb00000 23bd0004 afb30000 23bd0004 afb40000 23bd0004 afb50000
  //   23bd0004 afb60000 23bd0004 20160002 20140003 20150001 168020 108100 2149825 132020 20020022 c
  //   1600fffa 295a022 1680fff7 23bdfffc 8fb60000 23bdfffc 8fb50000 23bdfffc 8fb40000 23bdfffc 8fb30000
  //   23bdfffc 8fb00000 23bdfffc 8fa40000 23bdfffc 8fa20000 42000018 afa20000 23bd0004 afa40000 23bd0004
  //   afb00000 23bd0004 afb30000 23bd0004 afb40000 23bd0004 afb50000 23bd0004 afb60000 23bd0004 20160003
  //   20140003 20150001 168020 108100 2149825 132020 20020022 c 1600fffa 295a022 1680fff7 23bdfffc
  //   8fb60000 23bdfffc 8fb50000 23bdfffc 8fb40000 23bdfffc 8fb30000 23bdfffc 8fb00000 23bdfffc 8fa40000
  //   23bdfffc 8fa20000 42000018
  //   JMP
  //   JR
  //   rs
  //   rt
  //   rd
  //   imm
  //   Beq
  //   Bne
  //   LB
  //   AluOP
  //   AluSrcB
  //   RegWrite
  //   JAL
  //   RegDst
  //   Syscall
  //   MemToReg
  //   MemWrite
  //   $a0
  //   为方便自动评测，需要输出PC，IR，寄存器堆写如数据RDin
  //   $v0
  //   RAM写使能MemWrite、RAM写入数据MDin等信号
  //   LUI：imm左移16位，送入rt对应寄存器，验证正确
  //   单级中断测试信号
endmodule

module \单周期MIPS_多级中断  (
  input  IR1,
  input  IR2,
  input  IR3,
  output RegWrite,
  output MemWrite,
  output [31:0] PC,
  output [31:0] IR,
  output [31:0] RDin,
  output [31:0] MDin,
  output [31:0] LedData
);

  wire _1, \_1号中断清零信号 , _2, \_2号中断清零信号 , _3, \_3号中断清零信号 , and_4_out, and_5_out, and_8_out, and_9_out, BEQ,
       BLTZ, BNE, CLK, comparator_1_gt, comparator_2_gt, comparator_3_eq, comparator_4_eq, comparator_5_eq,
       comparator_6_eq, comparator_7_eq, comparator_8_eq, comparator_9_eq, demultiplexer_1_out1,
       demultiplexer_1_out2, demultiplexer_1_out3, EN, ERET, Go, IE, IR1_t, IR2_t, IR3_t, IRA, IRB, IRC, JAL,
       JMP, JR, LB, LUI, multiplexer_4_out, multiplexer_18_out, not_1_out, or_5_out, or_6_out, or_7_out,
       or_8_out, or_9_out, Pause, priority_encoder_1_gs, SignedExt, syscall, tunnel, W1, W2, W3, \中断信号 ,
       \中断信息记录信号 , \中断清零信号 , \关中断 , \单周期硬布线控制器_1_alu_src , \单周期硬布线控制器_1_memtoreg , \单周期硬布线控制器_1_regdst ,
       \开中断 ;
  wire [1:0] multiplexer_3_out, priority_encoder_1_out, \中断编号 ;
  wire [3:0] \单周期硬布线控制器_1_alu_op ;
  wire [4:0] multiplexer_5_out, multiplexer_6_out, multiplexer_7_out, multiplexer_8_out, multiplexer_9_out,
       multiplexer_14_out;
  wire [7:0] multiplexer_19_out;
  wire [15:0] \总周期数 ;
  wire [31:0] a0, adder_2_out, bit_extender_1_out, bit_extender_2_out, bit_extender_3_out, BLTZ_result, EPC,
       JRaddr, multiplexer_1_out, multiplexer_2_out, multiplexer_10_out, multiplexer_12_out,
       multiplexer_16_out, multiplexer_17_out, multiplexer_20_out, PC_4, ram_1_data, shifter_1_out, v0,
       \正常程序地址 ;

  Clock #(.highDuration(1), .lowDuration(1)) clock_1 (.out(CLK));
  Button u__1 ();  // open: out
  Button u__2 ();  // open: out
  Button u__3 ();  // open: out
  Button \u_继续运行  (.out(Go));
  LED #(.active("true")) led_1 (.in(W1));
  LED #(.active("true")) led_2 (.in(W2));
  LED #(.active("true")) led_3 (.in(W3));
  and and_1 (\_1号中断清零信号 , demultiplexer_1_out1, \开中断 );
  and and_2 (\_2号中断清零信号 , demultiplexer_1_out2, \开中断 );
  and and_3 (\_3号中断清零信号 , demultiplexer_1_out3, \开中断 );
  \中断按键参考电路  \u_中断按键参考电路_1  (
    .\_1号同步清零信号 (\_1号中断清零信号 ), .\_1号中断 (IR1_t), .CLK(CLK), .\_1号中断等待指示灯 (W1), .\_2号中断 (IR2_t),
    .\_2号中断等待指示灯 (W2), .\_3号中断 (IR3_t), .\_3号中断等待指示灯 (W3), .\_2号同步清零信号 (\_2号中断清零信号 ),
    .\_3号同步清零信号 (\_3号中断清零信号 ), .\_1号与中断屏蔽位与 (_1), .\_2号与中断屏蔽位与 (_2), .\_3号与中断屏蔽位与 (_3));
  Comparator #(.width(2), .mode("unsigned")) comparator_1 (
    .a(\中断编号 ), .b(2'b01), .gt(comparator_1_gt));  // open: eq, lt
  Comparator #(.width(2), .mode("unsigned")) comparator_2 (
    .a(\中断编号 ), .b(2'b10), .gt(comparator_2_gt));  // open: eq, lt
  Hex_Digit_Display hex_digit_display_1 (.value(LedData[31:28]));  // open: dp
  and and_4 (and_4_out, _1, ~comparator_1_gt);  // AND_Gate
  and and_5 (and_5_out, _2, ~comparator_2_gt);  // AND_Gate
  Hex_Digit_Display hex_digit_display_2 (.value(LedData[27:24]));  // open: dp
  Hex_Digit_Display hex_digit_display_3 (.value(LedData[23:20]));  // open: dp
  Multiplexer #(.select(1), .width(32), .disabled("Z"), .enable("false")) multiplexer_1 (
    .in0(\正常程序地址 ), .in1(EPC), .out(multiplexer_1_out), .sel(ERET));
  Priority_Encoder #(.select(2), .disabled("Z")) priority_encoder_1 (
    .in0(1'b0), .in1(and_4_out), .in2(and_5_out), .in3(_3), .out(priority_encoder_1_out),
    .gs(priority_encoder_1_gs));  // open: en_out, en_in
  Hex_Digit_Display hex_digit_display_4 (.value(LedData[19:16]));  // open: dp
  Hex_Digit_Display hex_digit_display_5 (.value(LedData[15:12]));  // open: dp
  Demultiplexer #(.select(2), .width(1), .tristate("false"), .disabled("Z"), .enable("false")) demultiplexer_1 (
    .out1(demultiplexer_1_out1), .out2(demultiplexer_1_out2), .out3(demultiplexer_1_out3), .in(1'b1),
    .sel(\中断编号 ));  // open: out0
  // Probe on \中断编号 
  Multiplexer #(.select(2), .width(32), .disabled("Z"), .enable("false")) multiplexer_2 (
    .in0(multiplexer_1_out), .in1(32'h30ac), .in2(32'h3158), .in3(32'h3204), .out(multiplexer_2_out),
    .sel(multiplexer_3_out));
  Multiplexer #(.select(1), .width(2), .disabled("Z"), .enable("false")) multiplexer_3 (
    .in0(2'b00), .in1(priority_encoder_1_out), .out(multiplexer_3_out), .sel(\中断信息记录信号 ));
  and and_6 (\中断信号 , priority_encoder_1_gs, ~IE, ~\开中断 );  // AND_Gate
  Hex_Digit_Display hex_digit_display_6 (.value(LedData[7:4]));  // open: dp
  Hex_Digit_Display hex_digit_display_7 (.value(LedData[11:8]));  // open: dp
  // Probe on \总周期数 
  // Probe on multiplexer_2_out
  Hex_Digit_Display hex_digit_display_8 (.value(LedData[3:0]));  // open: dp
  // Probe on \总周期数 
  \EPC硬件堆栈  \epc硬件堆栈_1  (.\地址 (\正常程序地址 ), .\写入信号_不含ERET (\中断信息记录信号 ), .\EPC堆栈 (EPC), .eret(ERET), .CLK(CLK));
  \中断序号记录堆栈  \u_中断序号记录堆栈_1  (
    .\地址 (multiplexer_3_out), .\写入信号_不含ERET (\中断信息记录信号 ), .\EPC堆栈 (\中断编号 ), .eret(ERET), .CLK(CLK));
  or or_1 (\中断清零信号 , \_1号中断清零信号 , \_2号中断清零信号 , \_3号中断清零信号 );
  // Probe on \正常程序地址 
  or or_2 (IR1_t, IR1, IRA);
  and and_7 (\中断信息记录信号 , \中断信号 , ~\中断清零信号 );  // AND_Gate
  Counter #(.width(16), .max('hffff), .ongoal("wrap"), .trigger("rising"), .behavior("old")) counter_1 (
    .count(EN), .Q(\总周期数 ), .clk(CLK), .clr(1'b0));  // open: load, D, carry, preset
  Register #(.width(32), .trigger("rising"), .Select("low")) u_PC (
    .D(multiplexer_2_out), .en(EN), .Q(PC), .clk(CLK), .clr(1'b0));
  \J型指令转跳地址判断器  \j型指令转跳地址判断器_1  (
    .JR(JR), .JMP(JMP), .BNE(BNE), .in_2(tunnel), .BEQ(BEQ), .JAL(JAL), .BLTZ(multiplexer_4_out),
    .out_12(\正常程序地址 ), .PC_4(PC_4), .BNE_BEQ_BLTZaddr(adder_2_out), .J_JALaddr({PC[31:28], IR[25:0], 2'b00}),
    .JRaddr(JRaddr));  // open: 转跳信号灯
  Multiplexer #(.select(1), .width(1), .disabled("Z"), .enable("false")) multiplexer_4 (
    .in0(1'b0), .in1(BLTZ), .out(multiplexer_4_out), .sel(comparator_3_eq));
  Comparator #(.width(32), .mode("unsigned")) comparator_3 (
    .a(BLTZ_result), .b(32'h1), .eq(comparator_3_eq));  // open: gt, lt
  or or_3 (IR2_t, IR2, IRB);
  Adder #(.width(32)) adder_1 (.a(PC), .b(32'h4), .out(PC_4));  // open: cin, cout
  // Probe on PC_4
  // Probe on JRaddr
  LED #(.active("true")) led_4 (.in(ERET));
  ROM #(.addrWidth(10), .dataWidth(32), .Select("high")) rom_1 (.addr(PC[11:2]), .data(IR));
  or or_4 (IR3_t, IR3, IRC);
  // Probe on IR[25:21]
  // Probe on IR[10:6]
  // Probe on {PC[31:28], IR[25:0], 2'b00}
  \单周期硬布线控制器  \u_单周期硬布线控制器_1  (
    .ALU_OP(\单周期硬布线控制器_1_alu_op ), .MemToReg(\单周期硬布线控制器_1_memtoreg ), .MemWrite(MemWrite),
    .ALU_SRC(\单周期硬布线控制器_1_alu_src ), .RegWrite(RegWrite), .SysCALL(syscall), .SignedExt(SignedExt),
    .RegDst(\单周期硬布线控制器_1_regdst ), .JR(JR), .JMP(JMP), .Beq(BEQ), .JAL(JAL), .Bne(BNE), .LUI(LUI),
    .BLTZ(BLTZ), .LB(LB), .ERET(ERET), .IR(IR), .\关中断 (\关中断 ), .\开中断 (\开中断 ));
  // Probe on IR[20:16]
  // Probe on IR[15:11]
  // Probe on adder_2_out
  Multiplexer #(.select(1), .width(5), .disabled("Z"), .enable("false")) multiplexer_5 (
    .in0(IR[25:21]), .in1({5{1'b1}}), .out(multiplexer_5_out), .sel(JR));
  Multiplexer #(.select(1), .width(5), .disabled("Z"), .enable("false")) multiplexer_6 (
    .in0(IR[20:16]), .in1(IR[15:11]), .out(multiplexer_6_out), .sel(\单周期硬布线控制器_1_regdst ));
  assign bit_extender_1_out = {{16{IR[15]}}, IR[15:0]};  // Bit_Extender bit_extender_1
  assign bit_extender_2_out = {{16{1'b0}}, IR[15:0]};  // Bit_Extender bit_extender_2
  Multiplexer #(.select(1), .width(5), .disabled("Z"), .enable("false")) multiplexer_7 (
    .in0(multiplexer_5_out), .in1(5'b00010), .out(multiplexer_7_out), .sel(syscall));
  Multiplexer #(.select(1), .width(5), .disabled("Z"), .enable("false")) multiplexer_8 (
    .in0(IR[20:16]), .in1(5'b00100), .out(multiplexer_8_out), .sel(syscall));
  Multiplexer #(.select(1), .width(5), .disabled("Z"), .enable("false")) multiplexer_9 (
    .in0(multiplexer_6_out), .in1({5{1'b1}}), .out(multiplexer_9_out), .sel(JAL));
  Multiplexer #(.select(1), .width(32), .disabled("Z"), .enable("false")) multiplexer_10 (
    .in0(bit_extender_1_out), .in1(bit_extender_2_out), .out(multiplexer_10_out), .sel(SignedExt));
  // Probe on RDin
  Multiplexer #(.select(1), .width(32), .disabled("Z"), .enable("false")) multiplexer_11 (
    .in0(multiplexer_16_out), .in1(PC_4), .out(RDin), .sel(JAL));
  or or_5 (or_5_out, \关中断 , \中断信号 );
  or or_6 (or_6_out, \中断信息记录信号 , \关中断 );
  MIPS_Regifile mips_regifile_1 (
    .Din(RDin), .Clk(CLK), .R1(JRaddr), .R2(MDin), .WE(RegWrite), .W_num(multiplexer_9_out),
    .R1_num(multiplexer_7_out), .R2_num(multiplexer_8_out));
  // Probe on multiplexer_10_out
  // Probe on PC_4
  Register #(.width(1), .trigger("rising"), .Select("low")) u_IE (
    .D(or_5_out), .en(or_6_out), .Q(IE), .clk(CLK), .clr(or_7_out));
  or or_7 (or_7_out, ERET, \开中断 );
  // Probe on JRaddr
  // Probe on MDin
  Shifter #(.width(32), .shift("ll")) shifter_1 (.in(multiplexer_10_out), .\dist (5'b00010), .out(shifter_1_out));
  Multiplexer #(.select(1), .width(32), .disabled("Z"), .enable("false")) multiplexer_12 (
    .in0(MDin), .in1(multiplexer_10_out), .out(multiplexer_12_out), .sel(\单周期硬布线控制器_1_alu_src ));
  Adder #(.width(32)) adder_2 (.a(shifter_1_out), .b(PC_4), .out(adder_2_out));  // open: cin, cout
  Multiplexer #(.select(1), .width(32), .disabled("Z"), .enable("false")) multiplexer_13 (
    .in0({32{1'b0}}), .in1(JRaddr), .out(v0), .sel(syscall));
  // Probe on \单周期硬布线控制器_1_alu_op 
  MIPS_ALU mips_alu_1 (
    .X(JRaddr), .Y(multiplexer_12_out), .AluOP(\单周期硬布线控制器_1_alu_op ), .Equal(tunnel), .Result(BLTZ_result),
    .shamt(multiplexer_14_out));  // open: Result_2
  Multiplexer #(.select(1), .width(5), .disabled("Z"), .enable("false")) multiplexer_14 (
    .in0(IR[10:6]), .in1(5'b10000), .out(multiplexer_14_out), .sel(LUI));
  // Probe on multiplexer_16_out
  Multiplexer #(.select(1), .width(32), .disabled("Z"), .enable("false")) multiplexer_15 (
    .in0({32{1'b0}}), .in1(MDin), .out(a0), .sel(syscall));
  // Probe on BLTZ_result
  Multiplexer #(.select(1), .width(32), .disabled("Z"), .enable("false")) multiplexer_16 (
    .in0(multiplexer_17_out), .in1(bit_extender_3_out), .out(multiplexer_16_out), .sel(LB));
  and and_8 (and_8_out, MemWrite, EN);
  Comparator #(.width(32), .mode("unsigned")) comparator_4 (.a(v0), .b(32'ha), .eq(comparator_4_eq));  // open: gt, lt
  not not_1 (not_1_out, comparator_4_eq);
  Multiplexer #(.select(1), .width(32), .disabled("Z"), .enable("false")) multiplexer_17 (
    .in0(BLTZ_result), .in1(ram_1_data), .out(multiplexer_17_out), .sel(\单周期硬布线控制器_1_memtoreg ));
  RAM #(.addrWidth(10), .dataWidth(32), .bus("separate"), .Select("high")) ram_1 (
    .addr({2'b00, BLTZ_result[9:2]}), .din(MDin), .data(ram_1_data), .str(and_8_out), .clk(CLK), .ld(EN),
    .clr(1'b0));  // open: sel
  // Probe on multiplexer_17_out
  // Probe on bit_extender_3_out
  xor xor_1 (Pause, comparator_4_eq, multiplexer_18_out);
  Multiplexer #(.select(1), .width(1), .disabled("Z"), .enable("false")) multiplexer_18 (
    .in0(1'b0), .in1(Go), .out(multiplexer_18_out), .sel(comparator_4_eq));
  Multiplexer #(.select(2), .width(8), .disabled("Z"), .enable("false")) multiplexer_19 (
    .in0(multiplexer_17_out[7:0]), .in1(multiplexer_17_out[15:8]), .in2(multiplexer_17_out[23:16]),
    .in3(multiplexer_17_out[31:24]), .out(multiplexer_19_out), .sel(BLTZ_result[1:0]));
  not not_2 (EN, Pause);
  assign bit_extender_3_out = {{24{multiplexer_19_out[7]}}, multiplexer_19_out};  // Bit_Extender bit_extender_3
  and and_9 (and_9_out, syscall, not_1_out);
  Comparator #(.width(16), .mode("twosComplement")) comparator_5 (
    .a(\总周期数 ), .b(16'h7), .eq(comparator_5_eq));  // open: gt, lt
  Comparator #(.width(16), .mode("twosComplement")) comparator_6 (
    .a(\总周期数 ), .b(16'h241), .eq(comparator_6_eq));  // open: gt, lt
  Multiplexer #(.select(1), .width(32), .disabled("Z"), .enable("false")) multiplexer_20 (
    .in0(LedData), .in1(a0), .out(multiplexer_20_out), .sel(and_9_out));
  Register #(.width(32), .trigger("rising"), .Select("low")) register_1 (
    .D(multiplexer_20_out), .Q(LedData), .clk(CLK));  // open: en, clr
  Comparator #(.width(16), .mode("twosComplement")) comparator_7 (
    .a(16'h258), .b(\总周期数 ), .eq(comparator_7_eq));  // open: gt, lt
  or or_8 (or_8_out, comparator_7_eq, comparator_8_eq);
  Comparator #(.width(16), .mode("twosComplement")) comparator_8 (
    .a(\总周期数 ), .b(16'h1), .eq(comparator_8_eq));  // open: gt, lt
  Comparator #(.width(16), .mode("twosComplement")) comparator_9 (
    .a(\总周期数 ), .b(16'h4), .eq(comparator_9_eq));  // open: gt, lt
  or or_9 (or_9_out, comparator_5_eq, comparator_6_eq);
  Pull_Resistor #(.pull(0)) pull_resistor_1 (.node(IRA));
  assign IRA = or_8_out ? ~CLK : 1'bz;  // Controlled_Inverter controlled_inverter_1
  Pull_Resistor #(.pull(0)) pull_resistor_2 (.node(IRB));
  assign IRB = comparator_9_eq ? ~CLK : 1'bz;  // Controlled_Inverter controlled_inverter_2
  Pull_Resistor #(.pull(0)) pull_resistor_3 (.node(IRC));
  assign IRC = or_9_out ? ~CLK : 1'bz;  // Controlled_Inverter controlled_inverter_3

  // Other names for the same wires on the sheet: LB取数据地址低2位[1:0] = BLTZ_result[1:0];
  //   Jaddr[31:2] = {PC[31:28], IR[25:0]}; shamt[4:0] = IR[10:6]; R1[31:0] = JRaddr; R2[31:0] = MDin

  // Notes on the sheet:
  //   中断源
  //   中断等待指示
  //   总复位信号应将除ROM以外所有存储组件全部清零
  //   数码管输出
  //   数码管输出应该用寄存器锁存，否则显示数据只能一闪而过
  //   指令存储器
  //   指令字
  //   contents of rom_1 (hex, n*v repeats v):
  //   201d07d0 20100001 109fc0 139fc3 8021 2012000c 24160008 26100001 3210000f 20080008 20090001 139900
  //   2709825 132020 20020022 c 1094022 1500fff9 22100001 2018000f 2188024 108700 20080008 20090001 139902
  //   2709825 132021 20020022 c 1094022 1500fff9 108702 2c9b022 12c00001 8000c07 4020 1084027 84400
  //   3508ffff 82021 20020022 c 8000c01 afa20000 23bd0004 afa40000 23bd0004 afb00000 23bd0004 afb30000
  //   23bd0004 afb40000 23bd0004 afb50000 23bd0004 afb60000 23bd0004 40000000 20160001 20140003 20150001
  //   168020 108100 2149825 132020 20020022 c 1600fffa 295a022 1680fff7 40800000 23bdfffc 8fb60000
  //   23bdfffc 8fb50000 23bdfffc 8fb40000 23bdfffc 8fb30000 23bdfffc 8fb00000 23bdfffc 8fa40000 23bdfffc
  //   8fa20000 42000018 afa20000 23bd0004 afa40000 23bd0004 afb00000 23bd0004 afb30000 23bd0004 afb40000
  //   23bd0004 afb50000 23bd0004 afb60000 23bd0004 40000000 20160002 20140003 20150001 168020 108100
  //   2149825 132020 20020022 c 1600fffa 295a022 1680fff7 40800000 23bdfffc 8fb60000 23bdfffc 8fb50000
  //   23bdfffc 8fb40000 23bdfffc 8fb30000 23bdfffc 8fb00000 23bdfffc 8fa40000 23bdfffc 8fa20000 42000018
  //   afa20000 23bd0004 afa40000 23bd0004 afb00000 23bd0004 afb30000 23bd0004 afb40000 23bd0004 afb50000
  //   23bd0004 afb60000 23bd0004 40000000 20160003 20140003 20150001 168020 108100 2149825 132020 20020022
  //   c 1600fffa 295a022 1680fff7 40800000 23bdfffc 8fb60000 23bdfffc 8fb50000 23bdfffc 8fb40000 23bdfffc
  //   8fb30000 23bdfffc 8fb00000 23bdfffc 8fa40000 23bdfffc 8fa20000 42000018
  //   JMP
  //   JR
  //   rs
  //   rt
  //   rd
  //   imm
  //   Beq
  //   Bne
  //   LB
  //   AluOP
  //   AluSrcB
  //   RegWrite
  //   JAL
  //   RegDst
  //   Syscall
  //   MemToReg
  //   MemWrite
  //   $a0
  //   为方便自动评测，需要输出PC，IR，寄存器堆写如数据RDin
  //   $v0
  //   RAM写使能MemWrite、RAM写入数据MDin等信号
  //   LUI：imm左移16位，送入rt对应寄存器，验证正确
endmodule

module \EPC硬件堆栈  (
  input  eret,
  input  [31:0] \地址 ,
  input  \写入信号_不含ERET ,
  input  CLK,
  output [31:0] \EPC堆栈 
);

  wire or_1_out;
  wire [31:0] EPC_2_q, EPC_3_q, multiplexer_1_out, multiplexer_2_out, multiplexer_3_out;

  Register #(.width(32), .trigger("rising"), .Select("low")) EPC (
    .D(multiplexer_1_out), .en(or_1_out), .Q(\EPC堆栈 ), .clk(CLK));  // open: clr
  Multiplexer #(.select(1), .width(32), .disabled("Z"), .enable("false")) multiplexer_1 (
    .in0(\地址 ), .in1(EPC_2_q), .out(multiplexer_1_out), .sel(eret));
  or or_1 (or_1_out, \写入信号_不含ERET , eret);
  Multiplexer #(.select(1), .width(32), .disabled("Z"), .enable("false")) multiplexer_2 (
    .in0(\EPC堆栈 ), .in1(EPC_3_q), .out(multiplexer_2_out), .sel(eret));
  Register #(.width(32), .trigger("rising"), .Select("low")) EPC_2 (
    .D(multiplexer_2_out), .en(or_1_out), .Q(EPC_2_q), .clk(CLK));  // open: clr
  Multiplexer #(.select(1), .width(32), .disabled("Z"), .enable("false")) multiplexer_3 (
    .in0(EPC_2_q), .in1({32{1'b0}}), .out(multiplexer_3_out), .sel(eret));
  Register #(.width(32), .trigger("rising"), .Select("low")) EPC_3 (
    .D(multiplexer_3_out), .en(or_1_out), .Q(EPC_3_q), .clk(CLK));  // open: clr

  // Other names for the same wires on the sheet: EPC[31:0] = \EPC堆栈 
endmodule

module \中断序号记录堆栈  (
  input  eret,
  input  [1:0] \地址 ,
  input  \写入信号_不含ERET ,
  input  CLK,
  output [1:0] \EPC堆栈 
);

  wire or_1_out;
  wire [1:0] EPC_2_q, EPC_3_q, multiplexer_1_out, multiplexer_2_out, multiplexer_3_out;

  Register #(.width(2), .trigger("rising"), .Select("low")) EPC (
    .D(multiplexer_1_out), .en(or_1_out), .Q(\EPC堆栈 ), .clk(CLK));  // open: clr
  Multiplexer #(.select(1), .width(2), .disabled("Z"), .enable("false")) multiplexer_1 (
    .in0(\地址 ), .in1(EPC_2_q), .out(multiplexer_1_out), .sel(eret));
  or or_1 (or_1_out, \写入信号_不含ERET , eret);
  Multiplexer #(.select(1), .width(2), .disabled("Z"), .enable("false")) multiplexer_2 (
    .in0(\EPC堆栈 ), .in1(EPC_3_q), .out(multiplexer_2_out), .sel(eret));
  Register #(.width(2), .trigger("rising"), .Select("low")) EPC_2 (
    .D(multiplexer_2_out), .en(or_1_out), .Q(EPC_2_q), .clk(CLK));  // open: clr
  Multiplexer #(.select(1), .width(2), .disabled("Z"), .enable("false")) multiplexer_3 (
    .in0(EPC_2_q), .in1(2'b00), .out(multiplexer_3_out), .sel(eret));
  Register #(.width(2), .trigger("rising"), .Select("low")) EPC_3 (
    .D(multiplexer_3_out), .en(or_1_out), .Q(EPC_3_q), .clk(CLK));  // open: clr

  // Other names for the same wires on the sheet: EPC[1:0] = \EPC堆栈 
endmodule

module \中断按键参考电路  (
  input  \_1号同步清零信号 ,
  input  CLK,
  input  \_1号中断 ,
  input  \_2号同步清零信号 ,
  input  \_2号中断 ,
  input  \_3号同步清零信号 ,
  input  \_3号中断 ,
  output \_1号与中断屏蔽位与 ,
  output \_1号中断等待指示灯 ,
  output \_2号与中断屏蔽位与 ,
  output \_2号中断等待指示灯 ,
  output \_3号与中断屏蔽位与 ,
  output \_3号中断等待指示灯 
);

  wire and_1_out, and_2_out, and_3_out, d_ff_1_q, d_ff_2_q, d_ff_3_q, or_4_out, or_5_out, or_6_out;

  or or_1 (\_1号中断等待指示灯 , \_1号与中断屏蔽位与 , d_ff_1_q);
  or or_2 (\_2号中断等待指示灯 , \_2号与中断屏蔽位与 , d_ff_2_q);
  or or_3 (\_3号中断等待指示灯 , \_3号与中断屏蔽位与 , d_ff_3_q);
  D_Flip_Flop #(.trigger("rising"), .Pre_Clr_Positions("LEGACY"), .NegatePresetClear("false"), .enable("true"), .NewFFLayout("false")) d_ff_1 (
    .clk(\_1号中断 ), .D(1'b1), .Q(d_ff_1_q), .reset(\_1号与中断屏蔽位与 ));  // open: Qn, preset, en
  D_Flip_Flop #(.trigger("rising"), .Pre_Clr_Positions("LEGACY"), .NegatePresetClear("false"), .enable("true"), .NewFFLayout("false")) d_ff_2 (
    .clk(\_2号中断 ), .D(1'b1), .Q(d_ff_2_q), .reset(\_2号与中断屏蔽位与 ));  // open: Qn, preset, en
  D_Flip_Flop #(.trigger("rising"), .Pre_Clr_Positions("LEGACY"), .NegatePresetClear("false"), .enable("true"), .NewFFLayout("false")) d_ff_3 (
    .clk(\_3号中断 ), .D(1'b1), .Q(d_ff_3_q), .reset(\_3号与中断屏蔽位与 ));  // open: Qn, preset, en
  or or_4 (or_4_out, d_ff_1_q, \_1号与中断屏蔽位与 );
  or or_5 (or_5_out, d_ff_2_q, \_2号与中断屏蔽位与 );
  or or_6 (or_6_out, d_ff_3_q, \_3号与中断屏蔽位与 );
  and and_1 (and_1_out, or_4_out, ~\_1号同步清零信号 );  // AND_Gate
  and and_2 (and_2_out, or_5_out, ~\_2号同步清零信号 );  // AND_Gate
  and and_3 (and_3_out, or_6_out, ~\_3号同步清零信号 );  // AND_Gate
  D_Flip_Flop #(.trigger("rising"), .Pre_Clr_Positions("LEGACY"), .NegatePresetClear("false"), .enable("true"), .NewFFLayout("false")) IR1 (
    .clk(CLK), .D(and_1_out), .Q(\_1号与中断屏蔽位与 ));  // open: Qn, preset, en, reset
  D_Flip_Flop #(.trigger("rising"), .Pre_Clr_Positions("LEGACY"), .NegatePresetClear("false"), .enable("true"), .NewFFLayout("false")) IR2 (
    .clk(CLK), .D(and_2_out), .Q(\_2号与中断屏蔽位与 ));  // open: Qn, preset, en, reset
  D_Flip_Flop #(.trigger("rising"), .Pre_Clr_Positions("LEGACY"), .NegatePresetClear("false"), .enable("true"), .NewFFLayout("false")) IR3 (
    .clk(CLK), .D(and_3_out), .Q(\_3号与中断屏蔽位与 ));  // open: Qn, preset, en, reset

  // Other names for the same wires on the sheet: _1号位 = \_1号与中断屏蔽位与 ; _2号位 = \_2号与中断屏蔽位与 ; _3号位 = \_3号与中断屏蔽位与 

  // Notes on the sheet:
  //   中断信号采样参考电路
endmodule

// 单周期硬布线控制器
module \单周期硬布线控制器  (
  input  [31:0] IR,
  output [3:0] ALU_OP,
  output MemToReg,
  output MemWrite,
  output ALU_SRC,
  output RegWrite,
  output SysCALL,
  output SignedExt,
  output RegDst,
  output Beq,
  output Bne,
  output JR,
  output JMP,
  output JAL,
  output LUI,
  output BLTZ,
  output LB,
  output ERET,
  output \关中断 ,
  output \开中断 
);

  Comparator #(.width(32), .mode("twosComplement")) comparator_1 (.a(IR), .b(32'h42000018), .eq(ERET));  // open: gt, lt
  Comparator #(.width(32), .mode("twosComplement")) comparator_2 (
    .a(IR), .b(32'h40800000), .eq(\关中断 ));  // open: gt, lt
  Comparator #(.width(32), .mode("twosComplement")) comparator_3 (
    .a(IR), .b(32'h40000000), .eq(\开中断 ));  // open: gt, lt
  \运算控制器自动生成  \u_运算控制器自动生成_1  (
    .OP0(IR[26]), .OP1(IR[27]), .OP2(IR[28]), .OP3(IR[29]), .OP4(IR[30]), .OP5(IR[31]), .F0(IR[0]),
    .F1(IR[1]), .F2(IR[2]), .F3(IR[3]), .F4(IR[4]), .F5(IR[5]), .S0(ALU_OP[0]), .S1(ALU_OP[1]),
    .S2(ALU_OP[2]), .S3(ALU_OP[3]));
  \控制信号自动生成  \u_控制信号自动生成_1  (
    .OP0(IR[26]), .OP1(IR[27]), .OP2(IR[28]), .MemToReg(MemToReg), .OP3(IR[29]), .OP4(IR[30]), .OP5(IR[31]),
    .MemWrite(MemWrite), .F0(IR[0]), .F1(IR[1]), .F2(IR[2]), .F3(IR[3]), .F4(IR[4]), .F5(IR[5]),
    .ALU_SRC(ALU_SRC), .RegWrite(RegWrite), .SysCALL(SysCALL), .SignedExt(SignedExt), .RegDst(RegDst),
    .BEQ(Beq), .BNE(Bne), .JR(JR), .JUMP(JMP), .JAL(JAL), .LUI(LUI), .BLTZ(BLTZ), .LB(LB));

  // Other names for the same wires on the sheet: FUNC[5:0] = IR[5:0]; OP_CODE[5:0] = IR[31:26]

  // Notes on the sheet:
  //   Func
  //   控制信号生成，产生数据通路需要的其他控制信号
  //   运算器控制器，根据指令生成运算器功能选择信号
endmodule

// 修改的硬布线控制器
module \修改的单周期硬布线控制器  (
  input  [5:0] OP,
  input  [5:0] Func,
  output [3:0] ALU_OP,
  output MemToReg,
  output MemWrite,
  output ALU_SRC,
  output RegWrite,
  output SysCALL,
  output SignedExt,
  output RegDst,
  output Beq,
  output Bne,
  output JR,
  output JMP,
  output JAL,
  output LUI,
  output BLTZ,
  output LB,
  output ERET
);

  Comparator #(.width(6), .mode("twosComplement")) comparator_1 (.a(OP), .b(6'b010000), .eq(ERET));  // open: gt, lt
  \运算控制器自动生成  \u_运算控制器自动生成_1  (
    .OP0(OP[0]), .OP1(OP[1]), .OP2(OP[2]), .OP3(OP[3]), .OP4(OP[4]), .OP5(OP[5]), .F0(Func[0]), .F1(Func[1]),
    .F2(Func[2]), .F3(Func[3]), .F4(Func[4]), .F5(Func[5]), .S0(ALU_OP[0]), .S1(ALU_OP[1]), .S2(ALU_OP[2]),
    .S3(ALU_OP[3]));
  \控制信号自动生成  \u_控制信号自动生成_1  (
    .OP0(OP[0]), .OP1(OP[1]), .OP2(OP[2]), .MemToReg(MemToReg), .OP3(OP[3]), .OP4(OP[4]), .OP5(OP[5]),
    .MemWrite(MemWrite), .F0(Func[0]), .F1(Func[1]), .F2(Func[2]), .F3(Func[3]), .F4(Func[4]), .F5(Func[5]),
    .ALU_SRC(ALU_SRC), .RegWrite(RegWrite), .SysCALL(SysCALL), .SignedExt(SignedExt), .RegDst(RegDst),
    .BEQ(Beq), .BNE(Bne), .JR(JR), .JUMP(JMP), .JAL(JAL), .LUI(LUI), .BLTZ(BLTZ), .LB(LB));

  // Other names for the same wires on the sheet: OP_CODE[5:0] = OP

  // Notes on the sheet:
  //   运算器控制器，根据指令生成运算器功能选择信号
endmodule

// 运算器控制器
module \运算控制器自动生成  (
  input  OP0,
  input  OP1,
  input  OP2,
  input  OP3,
  input  OP4,
  input  OP5,
  input  F0,
  input  F1,
  input  F2,
  input  F3,
  input  F4,
  input  F5,
  output S0,
  output S1,
  output S2,
  output S3
);

  wire and_1_out, and_2_out, and_3_out, and_4_out, and_5_out, and_6_out, and_7_out, and_8_out, and_9_out,
       and_10_out, and_11_out, and_12_out, and_13_out, and_14_out, and_15_out, and_16_out, and_17_out,
       and_18_out, and_19_out, and_20_out, and_21_out, and_22_out, and_23_out, and_24_out, and_25_out,
       and_26_out, and_27_out, and_28_out, and_29_out, and_30_out, and_31_out, and_32_out, and_33_out,
       and_34_out, and_35_out, and_36_out, and_37_out, and_38_out, and_39_out, and_40_out, and_41_out,
       not_1_out, not_2_out, not_3_out, not_4_out, not_5_out, not_6_out, not_7_out, not_8_out, not_9_out,
       not_10_out, not_11_out, not_12_out, not_13_out, not_14_out, not_15_out, not_16_out, not_17_out,
       not_18_out, not_19_out, not_20_out, not_21_out, not_22_out, not_23_out, not_24_out, not_25_out,
       not_26_out, not_27_out, not_28_out, not_29_out, not_30_out, not_31_out, not_32_out, not_33_out,
       not_34_out, not_35_out, not_36_out, not_37_out, not_38_out, not_39_out, not_40_out, not_41_out,
       not_42_out, not_43_out, not_44_out, not_45_out, not_46_out, not_47_out, not_48_out, not_49_out,
       not_50_out, not_51_out, not_52_out, not_53_out, not_54_out, not_55_out, not_56_out, not_57_out,
       not_58_out, not_59_out, not_60_out, not_61_out, not_62_out, not_63_out, not_64_out, not_65_out,
       not_66_out, not_67_out, not_68_out, not_69_out, not_70_out, not_71_out, not_72_out, not_73_out,
       not_74_out, not_75_out, not_76_out, not_77_out, not_78_out, not_79_out, not_80_out, not_81_out,
       not_82_out, not_83_out, not_84_out, not_85_out, not_86_out, not_87_out, not_88_out, not_89_out,
       not_90_out, not_91_out, not_92_out, not_93_out, not_94_out, not_95_out, not_96_out, not_97_out,
       not_98_out, not_99_out, not_100_out, not_101_out, not_102_out, not_103_out, not_104_out, not_105_out,
       not_106_out, not_107_out, not_108_out, not_109_out, not_110_out, not_111_out, not_112_out,
       not_113_out, not_114_out, not_115_out, not_116_out, not_117_out, not_118_out, not_119_out,
       not_120_out, not_121_out, not_122_out, not_123_out, not_124_out, not_125_out, not_126_out,
       not_127_out, not_128_out, not_129_out, not_130_out, not_131_out, not_132_out, not_133_out,
       not_134_out, not_135_out, not_136_out, not_137_out, not_138_out, not_139_out, not_140_out,
       not_141_out, not_142_out, not_143_out, not_144_out, not_145_out, not_146_out, not_147_out,
       not_148_out, not_149_out, not_150_out, not_151_out, not_152_out, not_153_out, not_154_out,
       not_155_out, not_156_out, not_157_out, not_158_out, not_159_out, not_160_out, not_161_out,
       not_162_out, not_163_out, not_164_out, not_165_out, not_166_out, not_167_out, not_168_out,
       not_169_out, not_170_out, not_171_out, not_172_out, not_173_out, not_174_out, not_175_out,
       not_176_out, not_177_out, not_178_out, not_179_out, not_180_out, not_181_out, not_182_out,
       not_183_out, not_184_out, not_185_out, not_186_out, not_187_out, not_188_out, not_189_out,
       not_190_out, not_191_out, not_192_out, not_193_out, not_194_out, not_195_out, not_196_out,
       not_197_out, not_198_out, not_199_out, not_200_out, not_201_out, not_202_out, not_203_out,
       not_204_out, not_205_out, not_206_out, not_207_out, not_208_out, not_209_out, not_210_out,
       not_211_out, not_212_out, not_213_out, not_214_out, not_215_out, not_216_out, not_217_out,
       not_218_out, not_219_out, not_220_out, not_221_out, not_222_out, not_223_out, not_224_out,
       not_225_out, not_226_out, not_227_out, not_228_out, not_229_out, not_230_out, not_231_out,
       not_232_out, not_233_out, not_234_out, not_235_out, not_236_out, not_237_out, not_238_out,
       not_239_out, not_240_out, not_241_out, not_242_out, not_243_out, not_244_out, not_245_out,
       not_246_out, not_247_out, not_248_out, not_249_out, not_250_out, not_251_out, not_252_out,
       not_253_out, not_254_out, not_255_out, not_256_out, not_257_out, not_258_out, not_259_out,
       not_260_out, not_261_out, not_262_out, not_263_out, not_264_out, not_265_out, not_266_out, not_267_out;

  not not_1 (not_1_out, OP5);
  not not_2 (not_2_out, OP4);
  not not_3 (not_3_out, OP3);
  not not_4 (not_4_out, OP2);
  not not_5 (not_5_out, OP1);
  not not_6 (not_6_out, OP0);
  not not_7 (not_7_out, F5);
  not not_8 (not_8_out, F4);
  not not_9 (not_9_out, F3);
  not not_10 (not_10_out, F2);
  not not_11 (not_11_out, OP5);
  not not_12 (not_12_out, OP4);
  not not_13 (not_13_out, OP3);
  not not_14 (not_14_out, OP2);
  not not_15 (not_15_out, OP1);
  not not_16 (not_16_out, OP0);
  not not_17 (not_17_out, F4);
  not not_18 (not_18_out, F3);
  not not_19 (not_19_out, F2);
  not not_20 (not_20_out, F1);
  not not_21 (not_21_out, F0);
  not not_22 (not_22_out, OP5);
  not not_23 (not_23_out, OP4);
  not not_24 (not_24_out, OP3);
  not not_25 (not_25_out, OP2);
  not not_26 (not_26_out, OP1);
  not not_27 (not_27_out, OP0);
  not not_28 (not_28_out, F4);
  not not_29 (not_29_out, F3);
  not not_30 (not_30_out, F2);
  not not_31 (not_31_out, F1);
  not not_32 (not_32_out, OP5);
  not not_33 (not_33_out, OP4);
  not not_34 (not_34_out, OP3);
  not not_35 (not_35_out, OP2);
  not not_36 (not_36_out, OP1);
  not not_37 (not_37_out, OP0);
  not not_38 (not_38_out, F4);
  not not_39 (not_39_out, F3);
  not not_40 (not_40_out, F1);
  not not_41 (not_41_out, F0);
  not not_42 (not_42_out, OP5);
  not not_43 (not_43_out, OP4);
  not not_44 (not_44_out, OP3);
  not not_45 (not_45_out, OP2);
  not not_46 (not_46_out, OP1);
  not not_47 (not_47_out, OP0);
  not not_48 (not_48_out, F4);
  not not_49 (not_49_out, F2);
  not not_50 (not_50_out, F0);
  not not_51 (not_51_out, OP5);
  not not_52 (not_52_out, OP4);
  not not_53 (not_53_out, OP2);
  not not_54 (not_54_out, OP1);
  not not_55 (not_55_out, OP0);
  not not_56 (not_56_out, OP5);
  not not_57 (not_57_out, OP4);
  not not_58 (not_58_out, OP1);
  not not_59 (not_59_out, OP0);
  not not_60 (not_60_out, OP5);
  not not_61 (not_61_out, OP4);
  not not_62 (not_62_out, OP2);
  not not_63 (not_63_out, OP1);
  not not_64 (not_64_out, OP5);
  not not_65 (not_65_out, OP4);
  not not_66 (not_66_out, OP2);
  not not_67 (not_67_out, OP0);
  not not_68 (not_68_out, OP4);
  not not_69 (not_69_out, OP3);
  not not_70 (not_70_out, OP2);
  not not_71 (not_71_out, OP4);
  not not_72 (not_72_out, OP2);
  not not_73 (not_73_out, OP4);
  not not_74 (not_74_out, OP3);
  not not_75 (not_75_out, OP2);
  not not_76 (not_76_out, OP1);
  not not_77 (not_77_out, OP0);
  not not_78 (not_78_out, OP5);
  not not_79 (not_79_out, OP4);
  not not_80 (not_80_out, OP3);
  not not_81 (not_81_out, OP2);
  not not_82 (not_82_out, OP1);
  not not_83 (not_83_out, OP5);
  not not_84 (not_84_out, OP4);
  not not_85 (not_85_out, OP3);
  not not_86 (not_86_out, OP2);
  not not_87 (not_87_out, OP1);
  not not_88 (not_88_out, OP0);
  not not_89 (not_89_out, F5);
  not not_90 (not_90_out, F4);
  not not_91 (not_91_out, F3);
  not not_92 (not_92_out, F2);
  not not_93 (not_93_out, F0);
  not not_94 (not_94_out, OP5);
  not not_95 (not_95_out, OP4);
  not not_96 (not_96_out, OP3);
  not not_97 (not_97_out, OP2);
  not not_98 (not_98_out, OP1);
  not not_99 (not_99_out, OP0);
  not not_100 (not_100_out, F4);
  not not_101 (not_101_out, F3);
  not not_102 (not_102_out, F2);
  not not_103 (not_103_out, F0);
  not not_104 (not_104_out, OP5);
  not not_105 (not_105_out, OP4);
  not not_106 (not_106_out, OP3);
  not not_107 (not_107_out, OP2);
  not not_108 (not_108_out, OP1);
  not not_109 (not_109_out, OP0);
  not not_110 (not_110_out, F4);
  not not_111 (not_111_out, F3);
  not not_112 (not_112_out, F1);
  not not_113 (not_113_out, F0);
  not not_114 (not_114_out, OP5);
  not not_115 (not_115_out, OP4);
  not not_116 (not_116_out, OP3);
  not not_117 (not_117_out, OP2);
  not not_118 (not_118_out, OP1);
  not not_119 (not_119_out, OP0);
  not not_120 (not_120_out, F4);
  not not_121 (not_121_out, F3);
  not not_122 (not_122_out, OP5);
  not not_123 (not_123_out, OP4);
  not not_124 (not_124_out, OP3);
  not not_125 (not_125_out, OP2);
  not not_126 (not_126_out, OP1);
  not not_127 (not_127_out, OP0);
  not not_128 (not_128_out, F4);
  not not_129 (not_129_out, F2);
  not not_130 (not_130_out, F0);
  not not_131 (not_131_out, OP5);
  not not_132 (not_132_out, OP4);
  not not_133 (not_133_out, OP1);
  not not_134 (not_134_out, OP0);
  not not_135 (not_135_out, OP5);
  not not_136 (not_136_out, OP4);
  not not_137 (not_137_out, OP2);
  not not_138 (not_138_out, OP0);
  not not_139 (not_139_out, OP5);
  not not_140 (not_140_out, OP4);
  not not_141 (not_141_out, OP3);
  not not_142 (not_142_out, OP2);
  not not_143 (not_143_out, OP1);
  not not_144 (not_144_out, OP5);
  not not_145 (not_145_out, OP4);
  not not_146 (not_146_out, OP3);
  not not_147 (not_147_out, OP2);
  not not_148 (not_148_out, OP1);
  not not_149 (not_149_out, OP0);
  not not_150 (not_150_out, F4);
  not not_151 (not_151_out, F3);
  not not_152 (not_152_out, F2);
  not not_153 (not_153_out, F1);
  not not_154 (not_154_out, F0);
  not not_155 (not_155_out, OP5);
  not not_156 (not_156_out, OP4);
  not not_157 (not_157_out, OP3);
  not not_158 (not_158_out, OP2);
  not not_159 (not_159_out, OP1);
  not not_160 (not_160_out, OP0);
  not not_161 (not_161_out, F4);
  not not_162 (not_162_out, F3);
  not not_163 (not_163_out, F2);
  not not_164 (not_164_out, F1);
  not not_165 (not_165_out, OP5);
  not not_166 (not_166_out, OP4);
  not not_167 (not_167_out, OP3);
  not not_168 (not_168_out, OP2);
  not not_169 (not_169_out, OP1);
  not not_170 (not_170_out, OP0);
  not not_171 (not_171_out, F4);
  not not_172 (not_172_out, F3);
  not not_173 (not_173_out, F2);
  not not_174 (not_174_out, F0);
  not not_175 (not_175_out, OP5);
  not not_176 (not_176_out, OP4);
  not not_177 (not_177_out, OP3);
  not not_178 (not_178_out, OP2);
  not not_179 (not_179_out, OP1);
  not not_180 (not_180_out, OP0);
  not not_181 (not_181_out, F4);
  not not_182 (not_182_out, F3);
  not not_183 (not_183_out, F1);
  not not_184 (not_184_out, F0);
  not not_185 (not_185_out, OP5);
  not not_186 (not_186_out, OP4);
  not not_187 (not_187_out, OP3);
  not not_188 (not_188_out, OP2);
  not not_189 (not_189_out, OP1);
  not not_190 (not_190_out, OP0);
  not not_191 (not_191_out, F4);
  not not_192 (not_192_out, F2);
  not not_193 (not_193_out, OP5);
  not not_194 (not_194_out, OP4);
  not not_195 (not_195_out, OP2);
  not not_196 (not_196_out, OP1);
  not not_197 (not_197_out, OP0);
  not not_198 (not_198_out, OP5);
  not not_199 (not_199_out, OP4);
  not not_200 (not_200_out, OP1);
  not not_201 (not_201_out, OP0);
  not not_202 (not_202_out, OP5);
  not not_203 (not_203_out, OP4);
  not not_204 (not_204_out, OP2);
  not not_205 (not_205_out, OP1);
  not not_206 (not_206_out, OP4);
  not not_207 (not_207_out, OP3);
  not not_208 (not_208_out, OP2);
  not not_209 (not_209_out, OP4);
  not not_210 (not_210_out, OP2);
  not not_211 (not_211_out, OP5);
  not not_212 (not_212_out, OP4);
  not not_213 (not_213_out, OP2);
  not not_214 (not_214_out, OP4);
  not not_215 (not_215_out, OP3);
  not not_216 (not_216_out, OP2);
  not not_217 (not_217_out, OP1);
  not not_218 (not_218_out, OP0);
  not not_219 (not_219_out, OP5);
  not not_220 (not_220_out, OP4);
  not not_221 (not_221_out, OP3);
  not not_222 (not_222_out, OP2);
  not not_223 (not_223_out, OP1);
  not not_224 (not_224_out, OP0);
  not not_225 (not_225_out, F4);
  not not_226 (not_226_out, F3);
  not not_227 (not_227_out, F1);
  not not_228 (not_228_out, OP5);
  not not_229 (not_229_out, OP4);
  not not_230 (not_230_out, OP3);
  not not_231 (not_231_out, OP2);
  not not_232 (not_232_out, OP1);
  not not_233 (not_233_out, OP0);
  not not_234 (not_234_out, F4);
  not not_235 (not_235_out, F3);
  not not_236 (not_236_out, OP5);
  not not_237 (not_237_out, OP4);
  not not_238 (not_238_out, OP3);
  not not_239 (not_239_out, OP2);
  not not_240 (not_240_out, OP1);
  not not_241 (not_241_out, OP0);
  not not_242 (not_242_out, F4);
  not not_243 (not_243_out, F2);
  not not_244 (not_244_out, F0);
  not not_245 (not_245_out, OP5);
  not not_246 (not_246_out, OP4);
  not not_247 (not_247_out, OP3);
  not not_248 (not_248_out, OP2);
  not not_249 (not_249_out, OP1);
  not not_250 (not_250_out, OP0);
  not not_251 (not_251_out, F4);
  not not_252 (not_252_out, F2);
  not not_253 (not_253_out, OP5);
  not not_254 (not_254_out, OP4);
  not not_255 (not_255_out, OP2);
  not not_256 (not_256_out, OP0);
  not not_257 (not_257_out, OP5);
  not not_258 (not_258_out, OP4);
  not not_259 (not_259_out, OP1);
  not not_260 (not_260_out, OP5);
  not not_261 (not_261_out, OP4);
  not not_262 (not_262_out, OP2);
  not not_263 (not_263_out, OP5);
  not not_264 (not_264_out, OP4);
  not not_265 (not_265_out, OP3);
  not not_266 (not_266_out, OP2);
  not not_267 (not_267_out, OP1);
  and and_1 (and_1_out, not_1_out, not_2_out, not_3_out, not_4_out, not_5_out, not_6_out, not_7_out, not_8_out, not_9_out, not_10_out, F1, F0);
  and and_2 (and_2_out, not_11_out, not_12_out, not_13_out, not_14_out, not_15_out, not_16_out, F5, not_17_out, not_18_out, not_19_out, not_20_out, not_21_out);
  and and_3 (and_3_out, not_22_out, not_23_out, not_24_out, not_25_out, not_26_out, not_27_out, F5, not_28_out, not_29_out, not_30_out, not_31_out, F0);
  and and_4 (and_4_out, not_32_out, not_33_out, not_34_out, not_35_out, not_36_out, not_37_out, F5, not_38_out, not_39_out, F2, not_40_out, not_41_out);
  and and_5 (and_5_out, not_42_out, not_43_out, not_44_out, not_45_out, not_46_out, not_47_out, F5, not_48_out, F3, not_49_out, F1, not_50_out);
  and and_6 (and_6_out, not_51_out, not_52_out, OP3, not_53_out, not_54_out, not_55_out);
  and and_7 (and_7_out, not_56_out, not_57_out, OP3, OP2, not_58_out, not_59_out);
  and and_8 (and_8_out, not_60_out, not_61_out, OP3, not_62_out, not_63_out, OP0);
  and and_9 (and_9_out, not_64_out, not_65_out, OP3, not_66_out, OP1, not_67_out);
  and and_10 (and_10_out, OP5, not_68_out, not_69_out, not_70_out, OP1, OP0);
  and and_11 (and_11_out, OP5, not_71_out, OP3, not_72_out, OP1, OP0);
  and and_12 (and_12_out, OP5, not_73_out, not_74_out, not_75_out, not_76_out, not_77_out);
  and and_13 (and_13_out, not_78_out, not_79_out, not_80_out, not_81_out, not_82_out, OP0);
  and and_14 (and_14_out, not_83_out, not_84_out, not_85_out, not_86_out, not_87_out, not_88_out, not_89_out, not_90_out, not_91_out, not_92_out, F1, not_93_out);
  and and_15 (and_15_out, not_94_out, not_95_out, not_96_out, not_97_out, not_98_out, not_99_out, F5, not_100_out, not_101_out, not_102_out, F1, not_103_out);
  and and_16 (and_16_out, not_104_out, not_105_out, not_106_out, not_107_out, not_108_out, not_109_out, F5, not_110_out, not_111_out, F2, not_112_out, not_113_out);
  and and_17 (and_17_out, not_114_out, not_115_out, not_116_out, not_117_out, not_118_out, not_119_out, F5, not_120_out, not_121_out, F2, F1, F0);
  and and_18 (and_18_out, not_122_out, not_123_out, not_124_out, not_125_out, not_126_out, not_127_out, F5, not_128_out, F3, not_129_out, F1, not_130_out);
  and and_19 (and_19_out, not_131_out, not_132_out, OP3, OP2, not_133_out, not_134_out);
  and and_20 (and_20_out, not_135_out, not_136_out, OP3, not_137_out, OP1, not_138_out);
  and and_21 (and_21_out, not_139_out, not_140_out, not_141_out, not_142_out, not_143_out, OP0);
  and and_22 (and_22_out, not_144_out, not_145_out, not_146_out, not_147_out, not_148_out, not_149_out, F5, not_150_out, not_151_out, not_152_out, not_153_out, not_154_out);
  and and_23 (and_23_out, not_155_out, not_156_out, not_157_out, not_158_out, not_159_out, not_160_out, F5, not_161_out, not_162_out, not_163_out, not_164_out, F0);
  and and_24 (and_24_out, not_165_out, not_166_out, not_167_out, not_168_out, not_169_out, not_170_out, F5, not_171_out, not_172_out, not_173_out, F1, not_174_out);
  and and_25 (and_25_out, not_175_out, not_176_out, not_177_out, not_178_out, not_179_out, not_180_out, F5, not_181_out, not_182_out, F2, not_183_out, not_184_out);
  and and_26 (and_26_out, not_185_out, not_186_out, not_187_out, not_188_out, not_189_out, not_190_out, F5, not_191_out, F3, not_192_out, F1, F0);
  and and_27 (and_27_out, not_193_out, not_194_out, OP3, not_195_out, not_196_out, not_197_out);
  and and_28 (and_28_out, not_198_out, not_199_out, OP3, OP2, not_200_out, not_201_out);
  and and_29 (and_29_out, not_202_out, not_203_out, OP3, not_204_out, not_205_out, OP0);
  and and_30 (and_30_out, OP5, not_206_out, not_207_out, not_208_out, OP1, OP0);
  and and_31 (and_31_out, OP5, not_209_out, OP3, not_210_out, OP1, OP0);
  and and_32 (and_32_out, not_211_out, not_212_out, OP3, not_213_out, OP1, OP0);
  and and_33 (and_33_out, OP5, not_214_out, not_215_out, not_216_out, not_217_out, not_218_out);
  and and_34 (and_34_out, not_219_out, not_220_out, not_221_out, not_222_out, not_223_out, not_224_out, F5, not_225_out, not_226_out, F2, not_227_out, F0);
  and and_35 (and_35_out, not_228_out, not_229_out, not_230_out, not_231_out, not_232_out, not_233_out, F5, not_234_out, not_235_out, F2, F1, F0);
  and and_36 (and_36_out, not_236_out, not_237_out, not_238_out, not_239_out, not_240_out, not_241_out, F5, not_242_out, F3, not_243_out, F1, not_244_out);
  and and_37 (and_37_out, not_245_out, not_246_out, not_247_out, not_248_out, not_249_out, not_250_out, F5, not_251_out, F3, not_252_out, F1, F0);
  and and_38 (and_38_out, not_253_out, not_254_out, OP3, not_255_out, OP1, not_256_out);
  and and_39 (and_39_out, not_257_out, not_258_out, OP3, OP2, not_259_out, OP0);
  and and_40 (and_40_out, not_260_out, not_261_out, OP3, not_262_out, OP1, OP0);
  and and_41 (and_41_out, not_263_out, not_264_out, not_265_out, not_266_out, not_267_out, OP0);
  or or_1 (S1, and_14_out, and_15_out, and_16_out, and_17_out, and_18_out, and_19_out, and_20_out, and_21_out);
  or or_2 (S3, and_34_out, and_35_out, and_36_out, and_37_out, and_38_out, and_39_out, and_40_out, and_41_out);
  or or_3 (S0, and_1_out, and_2_out, and_3_out, and_4_out, and_5_out, and_6_out, and_7_out, and_8_out, and_9_out, and_10_out, and_11_out, and_12_out, and_13_out);
  or or_4 (S2, and_22_out, and_23_out, and_24_out, and_25_out, and_26_out, and_27_out, and_28_out, and_29_out, and_30_out, and_31_out, and_32_out, and_33_out);
endmodule

// 控制信号生成
module \控制信号自动生成  (
  input  OP0,
  input  OP1,
  input  OP2,
  input  OP3,
  input  OP4,
  input  OP5,
  input  F0,
  input  F1,
  input  F2,
  input  F3,
  input  F4,
  input  F5,
  output MemToReg,
  output MemWrite,
  output ALU_SRC,
  output RegWrite,
  output SysCALL,
  output SignedExt,
  output RegDst,
  output BEQ,
  output BNE,
  output JR,
  output JUMP,
  output JAL,
  output LUI,
  output BLTZ,
  output LB
);

  wire and_1_out, and_2_out, and_4_out, and_5_out, and_6_out, and_7_out, and_8_out, and_9_out, and_10_out,
       and_11_out, and_12_out, and_13_out, and_14_out, and_15_out, and_16_out, and_17_out, and_18_out,
       and_21_out, and_22_out, and_23_out, and_24_out, and_25_out, and_29_out, and_30_out, not_1_out,
       not_2_out, not_3_out, not_4_out, not_5_out, not_6_out, not_7_out, not_8_out, not_9_out, not_10_out,
       not_11_out, not_12_out, not_13_out, not_14_out, not_15_out, not_16_out, not_17_out, not_18_out,
       not_19_out, not_20_out, not_21_out, not_22_out, not_23_out, not_24_out, not_25_out, not_26_out,
       not_27_out, not_28_out, not_29_out, not_30_out, not_31_out, not_32_out, not_33_out, not_34_out,
       not_35_out, not_36_out, not_37_out, not_38_out, not_39_out, not_40_out, not_41_out, not_42_out,
       not_43_out, not_44_out, not_45_out, not_46_out, not_47_out, not_48_out, not_49_out, not_50_out,
       not_51_out, not_52_out, not_53_out, not_54_out, not_55_out, not_56_out, not_57_out, not_58_out,
       not_59_out, not_60_out, not_61_out, not_62_out, not_63_out, not_64_out, not_65_out, not_66_out,
       not_67_out, not_68_out, not_69_out, not_70_out, not_71_out, not_72_out, not_73_out, not_74_out,
       not_75_out, not_76_out, not_77_out, not_78_out, not_79_out, not_80_out, not_81_out, not_82_out,
       not_83_out, not_84_out, not_85_out, not_86_out, not_87_out, not_88_out, not_89_out, not_90_out,
       not_91_out, not_92_out, not_93_out, not_94_out, not_95_out, not_96_out, not_97_out, not_98_out,
       not_99_out, not_100_out, not_101_out, not_102_out, not_103_out, not_104_out, not_105_out, not_106_out,
       not_107_out, not_108_out, not_109_out, not_110_out, not_111_out, not_112_out, not_113_out,
       not_114_out, not_115_out, not_116_out, not_117_out, not_118_out, not_119_out, not_120_out,
       not_121_out, not_122_out, not_123_out, not_124_out, not_125_out, not_126_out, not_127_out,
       not_128_out, not_129_out, not_130_out, not_131_out, not_132_out, not_133_out, not_134_out,
       not_135_out, not_136_out, not_137_out, not_138_out, not_139_out, not_140_out, not_141_out,
       not_142_out, not_143_out, not_144_out, not_145_out, not_146_out, not_147_out, not_148_out,
       not_149_out, not_150_out, not_151_out, not_152_out, not_153_out, not_154_out, not_155_out,
       not_156_out, not_157_out, not_158_out, not_159_out, not_160_out, not_161_out, not_162_out,
       not_163_out, not_164_out, not_165_out, not_166_out, not_167_out, not_168_out, not_169_out,
       not_170_out, not_171_out, not_172_out, not_173_out, not_174_out, not_175_out, not_176_out,
       not_177_out, not_178_out, not_179_out, not_180_out, not_181_out, not_182_out, not_183_out,
       not_184_out, not_185_out, not_186_out, not_187_out, not_188_out, not_189_out;

  not not_1 (not_1_out, OP0);
  not not_2 (not_2_out, OP1);
  not not_3 (not_3_out, OP2);
  not not_4 (not_4_out, OP3);
  not not_5 (not_5_out, OP4);
  not not_6 (not_6_out, OP2);
  not not_7 (not_7_out, OP3);
  not not_8 (not_8_out, OP4);
  not not_9 (not_9_out, OP2);
  not not_10 (not_10_out, OP4);
  not not_11 (not_11_out, OP0);
  not not_12 (not_12_out, OP1);
  not not_13 (not_13_out, OP2);
  not not_14 (not_14_out, OP3);
  not not_15 (not_15_out, OP4);
  not not_16 (not_16_out, OP1);
  not not_17 (not_17_out, OP4);
  not not_18 (not_18_out, OP5);
  not not_19 (not_19_out, OP2);
  not not_20 (not_20_out, OP4);
  not not_21 (not_21_out, OP5);
  not not_22 (not_22_out, OP4);
  not not_23 (not_23_out, OP5);
  not not_24 (not_24_out, OP2);
  not not_25 (not_25_out, OP4);
  not not_26 (not_26_out, OP0);
  not not_27 (not_27_out, OP1);
  not not_28 (not_28_out, OP2);
  not not_29 (not_29_out, OP3);
  not not_30 (not_30_out, OP4);
  not not_31 (not_31_out, F0);
  not not_32 (not_32_out, F2);
  not not_33 (not_33_out, F3);
  not not_34 (not_34_out, F4);
  not not_35 (not_35_out, OP0);
  not not_36 (not_36_out, OP1);
  not not_37 (not_37_out, OP2);
  not not_38 (not_38_out, OP3);
  not not_39 (not_39_out, OP4);
  not not_40 (not_40_out, F1);
  not not_41 (not_41_out, F3);
  not not_42 (not_42_out, F4);
  not not_43 (not_43_out, OP0);
  not not_44 (not_44_out, OP1);
  not not_45 (not_45_out, OP2);
  not not_46 (not_46_out, OP3);
  not not_47 (not_47_out, OP4);
  not not_48 (not_48_out, F2);
  not not_49 (not_49_out, F3);
  not not_50 (not_50_out, F4);
  not not_51 (not_51_out, F5);
  not not_52 (not_52_out, OP0);
  not not_53 (not_53_out, OP1);
  not not_54 (not_54_out, OP2);
  not not_55 (not_55_out, OP3);
  not not_56 (not_56_out, OP4);
  not not_57 (not_57_out, F2);
  not not_58 (not_58_out, F4);
  not not_59 (not_59_out, OP0);
  not not_60 (not_60_out, OP1);
  not not_61 (not_61_out, OP2);
  not not_62 (not_62_out, OP3);
  not not_63 (not_63_out, OP4);
  not not_64 (not_64_out, F3);
  not not_65 (not_65_out, F4);
  not not_66 (not_66_out, OP0);
  not not_67 (not_67_out, OP1);
  not not_68 (not_68_out, OP2);
  not not_69 (not_69_out, OP3);
  not not_70 (not_70_out, OP4);
  not not_71 (not_71_out, OP1);
  not not_72 (not_72_out, OP4);
  not not_73 (not_73_out, OP5);
  not not_74 (not_74_out, OP2);
  not not_75 (not_75_out, OP4);
  not not_76 (not_76_out, OP5);
  not not_77 (not_77_out, OP4);
  not not_78 (not_78_out, OP5);
  not not_79 (not_79_out, OP2);
  not not_80 (not_80_out, OP3);
  not not_81 (not_81_out, OP4);
  not not_82 (not_82_out, OP0);
  not not_83 (not_83_out, OP1);
  not not_84 (not_84_out, OP2);
  not not_85 (not_85_out, OP3);
  not not_86 (not_86_out, OP4);
  not not_87 (not_87_out, OP5);
  not not_88 (not_88_out, F0);
  not not_89 (not_89_out, F1);
  not not_90 (not_90_out, F4);
  not not_91 (not_91_out, F5);
  not not_92 (not_92_out, OP5);
  not not_93 (not_93_out, OP4);
  not not_94 (not_94_out, OP1);
  not not_95 (not_95_out, OP0);
  not not_96 (not_96_out, OP1);
  not not_97 (not_97_out, OP2);
  not not_98 (not_98_out, OP3);
  not not_99 (not_99_out, OP4);
  not not_100 (not_100_out, OP5);
  not not_101 (not_101_out, F0);
  not not_102 (not_102_out, F2);
  not not_103 (not_103_out, F3);
  not not_104 (not_104_out, F4);
  not not_105 (not_105_out, OP0);
  not not_106 (not_106_out, OP1);
  not not_107 (not_107_out, OP2);
  not not_108 (not_108_out, OP3);
  not not_109 (not_109_out, OP4);
  not not_110 (not_110_out, OP5);
  not not_111 (not_111_out, F1);
  not not_112 (not_112_out, F3);
  not not_113 (not_113_out, F4);
  not not_114 (not_114_out, OP0);
  not not_115 (not_115_out, OP1);
  not not_116 (not_116_out, OP2);
  not not_117 (not_117_out, OP3);
  not not_118 (not_118_out, OP4);
  not not_119 (not_119_out, OP5);
  not not_120 (not_120_out, F2);
  not not_121 (not_121_out, F3);
  not not_122 (not_122_out, F4);
  not not_123 (not_123_out, F5);
  not not_124 (not_124_out, OP0);
  not not_125 (not_125_out, OP1);
  not not_126 (not_126_out, OP2);
  not not_127 (not_127_out, OP3);
  not not_128 (not_128_out, OP4);
  not not_129 (not_129_out, OP5);
  not not_130 (not_130_out, F2);
  not not_131 (not_131_out, F4);
  not not_132 (not_132_out, OP0);
  not not_133 (not_133_out, OP1);
  not not_134 (not_134_out, OP2);
  not not_135 (not_135_out, OP3);
  not not_136 (not_136_out, OP4);
  not not_137 (not_137_out, OP5);
  not not_138 (not_138_out, F3);
  not not_139 (not_139_out, F4);
  not not_140 (not_140_out, OP0);
  not not_141 (not_141_out, OP1);
  not not_142 (not_142_out, OP3);
  not not_143 (not_143_out, OP4);
  not not_144 (not_144_out, OP5);
  not not_145 (not_145_out, OP1);
  not not_146 (not_146_out, OP3);
  not not_147 (not_147_out, OP4);
  not not_148 (not_148_out, OP5);
  not not_149 (not_149_out, OP0);
  not not_150 (not_150_out, OP1);
  not not_151 (not_151_out, OP2);
  not not_152 (not_152_out, OP3);
  not not_153 (not_153_out, OP4);
  not not_154 (not_154_out, OP5);
  not not_155 (not_155_out, F0);
  not not_156 (not_156_out, F1);
  not not_157 (not_157_out, F2);
  not not_158 (not_158_out, F4);
  not not_159 (not_159_out, F5);
  not not_160 (not_160_out, OP0);
  not not_161 (not_161_out, OP2);
  not not_162 (not_162_out, OP3);
  not not_163 (not_163_out, OP4);
  not not_164 (not_164_out, OP5);
  not not_165 (not_165_out, F0);
  not not_166 (not_166_out, F1);
  not not_167 (not_167_out, F2);
  not not_168 (not_168_out, F4);
  not not_169 (not_169_out, F5);
  not not_170 (not_170_out, OP2);
  not not_171 (not_171_out, OP3);
  not not_172 (not_172_out, OP4);
  not not_173 (not_173_out, OP5);
  not not_174 (not_174_out, OP2);
  not not_175 (not_175_out, OP3);
  not not_176 (not_176_out, OP4);
  not not_177 (not_177_out, OP5);
  not not_178 (not_178_out, OP4);
  not not_179 (not_179_out, OP5);
  not not_180 (not_180_out, OP1);
  not not_181 (not_181_out, OP2);
  not not_182 (not_182_out, OP3);
  not not_183 (not_183_out, OP4);
  not not_184 (not_184_out, OP5);
  not not_185 (not_185_out, OP0);
  not not_186 (not_186_out, OP1);
  not not_187 (not_187_out, OP2);
  not not_188 (not_188_out, OP3);
  not not_189 (not_189_out, OP4);
  and and_1 (and_1_out, not_1_out, not_2_out, not_3_out, not_4_out, not_5_out, OP5);
  and and_2 (and_2_out, OP0, OP1, not_6_out, not_7_out, not_8_out, OP5);
  and and_3 (MemWrite, OP0, OP1, not_9_out, OP3, not_10_out, OP5);
  and and_4 (and_4_out, not_11_out, not_12_out, not_13_out, not_14_out, not_15_out, OP5);
  and and_5 (and_5_out, not_16_out, OP3, not_17_out, not_18_out);
  and and_6 (and_6_out, not_19_out, OP3, not_20_out, not_21_out);
  and and_7 (and_7_out, OP0, OP3, not_22_out, not_23_out);
  and and_8 (and_8_out, OP0, OP1, not_24_out, not_25_out, OP5);
  and and_9 (and_9_out, not_26_out, not_27_out, not_28_out, not_29_out, not_30_out, not_31_out, not_32_out, not_33_out, not_34_out);
  and and_10 (and_10_out, not_35_out, not_36_out, not_37_out, not_38_out, not_39_out, not_40_out, not_41_out, not_42_out, F5);
  and and_11 (and_11_out, not_43_out, not_44_out, not_45_out, not_46_out, not_47_out, F1, not_48_out, not_49_out, not_50_out, not_51_out);
  and and_12 (and_12_out, not_52_out, not_53_out, not_54_out, not_55_out, not_56_out, F1, not_57_out, F3, not_58_out, F5);
  and and_13 (and_13_out, not_59_out, not_60_out, not_61_out, not_62_out, not_63_out, F0, F2, not_64_out, not_65_out, F5);
  and and_14 (and_14_out, not_66_out, not_67_out, not_68_out, not_69_out, not_70_out, OP5);
  and and_15 (and_15_out, not_71_out, OP3, not_72_out, not_73_out);
  and and_16 (and_16_out, not_74_out, OP3, not_75_out, not_76_out);
  and and_17 (and_17_out, OP0, OP3, not_77_out, not_78_out);
  and and_18 (and_18_out, OP0, OP1, not_79_out, not_80_out, not_81_out);
  and and_19 (SysCALL, not_82_out, not_83_out, not_84_out, not_85_out, not_86_out, not_87_out, not_88_out, not_89_out, F2, F3, not_90_out, not_91_out);
  and and_20 (SignedExt, not_92_out, not_93_out, OP3, OP2, not_94_out, OP0);
  and and_21 (and_21_out, not_95_out, not_96_out, not_97_out, not_98_out, not_99_out, not_100_out, not_101_out, not_102_out, not_103_out, not_104_out);
  and and_22 (and_22_out, not_105_out, not_106_out, not_107_out, not_108_out, not_109_out, not_110_out, not_111_out, not_112_out, not_113_out, F5);
  and and_23 (and_23_out, not_114_out, not_115_out, not_116_out, not_117_out, not_118_out, not_119_out, F1, not_120_out, not_121_out, not_122_out, not_123_out);
  and and_24 (and_24_out, not_124_out, not_125_out, not_126_out, not_127_out, not_128_out, not_129_out, F1, not_130_out, F3, not_131_out, F5);
  and and_25 (and_25_out, not_132_out, not_133_out, not_134_out, not_135_out, not_136_out, not_137_out, F0, F2, not_138_out, not_139_out, F5);
  and and_26 (BEQ, not_140_out, not_141_out, OP2, not_142_out, not_143_out, not_144_out);
  and and_27 (BNE, OP0, not_145_out, OP2, not_146_out, not_147_out, not_148_out);
  and and_28 (JR, not_149_out, not_150_out, not_151_out, not_152_out, not_153_out, not_154_out, not_155_out, not_156_out, not_157_out, F3, not_158_out, not_159_out);
  and and_29 (and_29_out, not_160_out, not_161_out, not_162_out, not_163_out, not_164_out, not_165_out, not_166_out, not_167_out, F3, not_168_out, not_169_out);
  and and_30 (and_30_out, OP1, not_170_out, not_171_out, not_172_out, not_173_out);
  and and_31 (JAL, OP0, OP1, not_174_out, not_175_out, not_176_out, not_177_out);
  and and_32 (LUI, OP0, OP1, OP2, OP3, not_178_out, not_179_out);
  and and_33 (BLTZ, OP0, not_180_out, not_181_out, not_182_out, not_183_out, not_184_out);
  and and_34 (LB, not_185_out, not_186_out, not_187_out, not_188_out, not_189_out, OP5);
  or or_1 (MemToReg, and_1_out, and_2_out);
  or or_2 (ALU_SRC, and_4_out, and_5_out, and_6_out, and_7_out, and_8_out);
  or or_3 (RegWrite, and_9_out, and_10_out, and_11_out, and_12_out, and_13_out, and_14_out, and_15_out, and_16_out, and_17_out, and_18_out);
  or or_4 (RegDst, and_21_out, and_22_out, and_23_out, and_24_out, and_25_out);
  or or_5 (JUMP, and_29_out, and_30_out);
endmodule

// ALU
module MIPS_ALU (
  input  [4:0] shamt,
  input  [31:0] X,
  input  [31:0] Y,
  input  [3:0] AluOP,
  output Equal,
  output [31:0] Result,
  output [31:0] Result_2
);

  wire [0:0] comparator_1_lt, comparator_2_lt;
  wire [31:0] adder_1_out, AND_out, divider_1_out, divider_1_rem, multiplier_1_cout, multiplier_1_out,
       NOR_out, OR_out, shifter_1_out, shifter_2_out, shifter_3_out, subtractor_1_out, XOR_out;

  assign AND_out = X & Y;  // AND_Gate AND, 32 bits wide
  assign OR_out = X | Y;  // OR_Gate OR, 32 bits wide
  Shifter #(.width(32), .shift("ll")) shifter_1 (.in(Y), .\dist (shamt), .out(shifter_1_out));
  Shifter #(.width(32), .shift("ar")) shifter_2 (.in(Y), .\dist (shamt), .out(shifter_2_out));
  Shifter #(.width(32), .shift("lr")) shifter_3 (.in(Y), .\dist (shamt), .out(shifter_3_out));
  Multiplier #(.width(32)) multiplier_1 (.a(X), .b(Y), .out(multiplier_1_out), .cout(multiplier_1_cout));  // open: cin
  Divider #(.width(32)) divider_1 (.a(X), .b(Y), .out(divider_1_out), .rem(divider_1_rem));  // open: upper
  Adder #(.width(32)) adder_1 (.a(X), .b(Y), .out(adder_1_out));  // open: cin, cout
  Subtractor #(.width(32)) subtractor_1 (.a(X), .b(Y), .out(subtractor_1_out));  // open: bin, bout
  assign XOR_out = X ^ Y;  // XOR_Gate XOR, 32 bits wide
  assign NOR_out = ~(X | Y);  // NOR_Gate NOR, 32 bits wide
  Comparator #(.width(32), .mode("twosComplement")) comparator_1 (
    .a(X), .b(Y), .eq(Equal), .lt(comparator_1_lt[0]));  // open: gt
  Comparator #(.width(32), .mode("unsigned")) comparator_2 (.a(X), .b(Y), .lt(comparator_2_lt[0]));  // open: gt, eq
  Multiplexer #(.select(4), .width(32), .disabled("Z"), .enable("false")) multiplexer_1 (
    .in0(shifter_1_out), .in1(shifter_2_out), .in2(shifter_3_out), .in3(multiplier_1_out),
    .in4(divider_1_out), .in5(adder_1_out), .in6(subtractor_1_out), .in7(AND_out), .in8(OR_out),
    .in9(XOR_out), .in10(NOR_out), .in11({{31{1'b0}}, comparator_1_lt[0]}),
    .in12({{31{1'b0}}, comparator_2_lt[0]}), .in13({32{1'b0}}), .in14({32{1'b0}}), .in15({32{1'b0}}),
    .out(Result), .sel(AluOP));
  Multiplexer #(.select(4), .width(32), .disabled("Z"), .enable("false")) multiplexer_2 (
    .in0({32{1'b0}}), .in1({32{1'b0}}), .in2({32{1'b0}}), .in3(multiplier_1_cout), .in4(divider_1_rem),
    .in5({32{1'b0}}), .in6({32{1'b0}}), .in7({32{1'b0}}), .in8({32{1'b0}}), .in9({32{1'b0}}),
    .in10({32{1'b0}}), .in11({32{1'b0}}), .in12({32{1'b0}}), .in13({32{1'b0}}), .in14({32{1'b0}}),
    .in15({32{1'b0}}), .out(Result_2), .sel(AluOP));

  // Other names for the same wires on the sheet: Result2[31:0] = Result_2; S[3:0] = AluOP

  // Notes on the sheet:
  //   不要改变此引脚区域内容，也不要改变ALU封装形式
  //   输入引脚
  //   输出引脚
endmodule

module MIPS_Regifile (
  input  [31:0] Din,
  input  Clk,
  input  WE,
  input  [4:0] R1_num,
  input  [4:0] W_num,
  input  [4:0] R2_num,
  output [31:0] R1,
  output [31:0] R2
);

  // RegisterFile registerfile_1: pin names not known; wires that end beside it: Din, Clk, WE, W_num, R1_num, R2_num, R1, R2
endmodule

module \MIPS_Regifile下降沿  (
  input  [31:0] Din,
  input  Clk,
  input  WE,
  input  [4:0] R1_num,
  input  [4:0] W_num,
  input  [4:0] R2_num,
  output [31:0] R1,
  output [31:0] R2
);

  // RegisterFile registerfile_1: pin names not known; wires that end beside it: Din, Clk, WE, W_num, R1_num, R2_num, R1, R2
endmodule

module \理想流水线  (
  output RegWrite,
  output MemWrite,
  output [31:0] out_3,
  output [31:0] out_4,
  output [31:0] out_5,
  output [31:0] out_6,
  output [31:0] out_7,
  output [31:0] RDin,
  output [31:0] MDin,
  output [31:0] out_10
);

  wire and_1_out, and_2_out, and_3_out, BEQ, BLTZ, BNE, CLK, Go, IR1, IR2, IR3, JAL, JMP, JR, LB, LUI,
       not_1_out, not_2_out, or_1_out, RST, SignedExt, syscall, tunnel, W1, W2, W3, \单周期硬布线控制器_1_alu_src ,
       \单周期硬布线控制器_1_beq , \单周期硬布线控制器_1_bne , \单周期硬布线控制器_1_memtoreg , \单周期硬布线控制器_1_memwrite ,
       \单周期硬布线控制器_1_regdst , \单周期硬布线控制器_1_regwrite , \单周期硬布线控制器_1_syscall , \理想流水ex_mem_1_mentoreg_2 ,
       \理想流水ex_mem_1_regwrite_2 , \理想流水ex_mem_1_syscall_2 , \理想流水id_ex_1_alusrcb_2 ,
       \理想流水id_ex_1_mentoreg_2 , \理想流水id_ex_1_menwrite , \理想流水id_ex_1_regwrite_2 , \理想流水id_ex_1_syscall_2 ,
       \理想流水mem_wb_1_mentoreg_2 ;
  wire [3:0] \单周期硬布线控制器_1_alu_op , \理想流水id_ex_1_aluop_2 ;
  wire [4:0] multiplexer_2_out, multiplexer_5_out, \理想流水ex_mem_1_w_2 , \理想流水id_ex_1_w_2 , \理想流水mem_wb_1_w_2 ;
  wire [11:0] MEM_PC;
  wire [15:0] \LoadUse次数 , \总周期数 , \插入气泡数 , \无条件分支数 , \条件分支成功数 ;
  wire [31:0] adder_2_out, bit_extender_1_out, bit_extender_2_out, IR, mips_alu_1_result,
       \mips_regifile下降沿_1_r1 , \mips_regifile下降沿_1_r2 , multiplexer_1_out, multiplexer_3_out,
       multiplexer_4_out, PC_4, ram_1_data, rom_1_data, shifter_1_out, \理想流水ex_mem_1_r_2 ,
       \理想流水id_ex_1_imm_2 , \理想流水id_ex_1_pc_4_2 , \理想流水id_ex_1_r1_2 , \理想流水id_ex_1_r2_2 , \理想流水if_id_1_ir_2 ,
       \理想流水mem_wb_1_alu_data_2 , \理想流水mem_wb_1_mem_readdata_2 ;

  Button \u_总复位  (.out(RST));
  Button _1 (.out(IR1));
  Button _2 (.out(IR2));
  Button _3 (.out(IR3));
  // Probe on multiplexer_1_out
  Button \u_继续运行  (.out(Go));
  LED #(.active("true")) led_1 (.in(W1));
  LED #(.active("true")) led_2 (.in(W2));
  LED #(.active("true")) led_3 (.in(W3));
  not not_1 (not_1_out, syscall);
  Counter #(.width(16), .max('hffff), .ongoal("wrap"), .trigger("rising"), .behavior("old")) counter_1 (
    .count(not_1_out), .Q(\总周期数 ), .clk(CLK), .clr(1'b0));  // open: load, D, carry, preset
  Register #(.width(32), .trigger("rising"), .Select("low")) PC (
    .D(multiplexer_1_out), .en(not_1_out), .Q(out_3), .clk(CLK), .clr(1'b0));
  Hex_Digit_Display hex_digit_display_1 (.value(out_10[31:28]));  // open: dp
  // Probe on \总周期数 
  Adder #(.width(32)) adder_1 (.a(out_3), .b(32'h4), .out(PC_4));  // open: cin, cout
  Multiplexer #(.select(1), .width(32), .disabled("Z"), .enable("false")) multiplexer_1 (
    .in0(PC_4), .in1(adder_2_out), .out(multiplexer_1_out), .sel(or_1_out));
  or or_1 (or_1_out, and_1_out, and_2_out);
  and and_1 (and_1_out, BEQ, tunnel);
  and and_2 (and_2_out, ~tunnel, BNE);  // AND_Gate
  Hex_Digit_Display hex_digit_display_2 (.value(out_10[23:20]));  // open: dp
  Hex_Digit_Display hex_digit_display_3 (.value(out_10[27:24]));  // open: dp
  Hex_Digit_Display hex_digit_display_4 (.value(out_10[15:12]));  // open: dp
  Hex_Digit_Display hex_digit_display_5 (.value(out_10[19:16]));  // open: dp
  ROM #(.addrWidth(10), .dataWidth(32), .Select("high")) rom_1 (.addr(out_3[11:2]), .data(rom_1_data));
  Hex_Digit_Display hex_digit_display_6 (.value(out_10[7:4]));  // open: dp
  Hex_Digit_Display hex_digit_display_7 (.value(out_10[11:8]));  // open: dp
  Clock #(.highDuration(1), .lowDuration(1)) clock_1 (.out(CLK));
  \理想流水IF_ID  \u_理想流水if_id_1  (
    .PC_4(rom_1_data), .IR(PC_4), .PC_4_2(IR), .IR_2(\理想流水if_id_1_ir_2 ), .CLK(CLK), .EN(not_1_out),
    .Reset(RST), .Jaddr(out_3), .Jaddr_2(out_4));
  Hex_Digit_Display hex_digit_display_8 (.value(out_10[3:0]));  // open: dp
  assign bit_extender_1_out = {{16{IR[15]}}, IR[15:0]};  // Bit_Extender bit_extender_1
  assign bit_extender_2_out = {{16{1'b0}}, IR[15:0]};  // Bit_Extender bit_extender_2
  \单周期硬布线控制器  \u_单周期硬布线控制器_1  (
    .ALU_OP(\单周期硬布线控制器_1_alu_op ), .MemToReg(\单周期硬布线控制器_1_memtoreg ), .MemWrite(\单周期硬布线控制器_1_memwrite ),
    .ALU_SRC(\单周期硬布线控制器_1_alu_src ), .RegWrite(\单周期硬布线控制器_1_regwrite ), .SysCALL(\单周期硬布线控制器_1_syscall ),
    .SignedExt(SignedExt), .RegDst(\单周期硬布线控制器_1_regdst ), .JR(JR), .JMP(JMP), .Beq(\单周期硬布线控制器_1_beq ),
    .JAL(JAL), .Bne(\单周期硬布线控制器_1_bne ), .LUI(LUI), .BLTZ(BLTZ), .LB(LB), .IR(IR));  // open: ERET, 关中断, 开中断
  Multiplexer #(.select(1), .width(5), .disabled("Z"), .enable("false")) multiplexer_2 (
    .in0(IR[20:16]), .in1(IR[15:11]), .out(multiplexer_2_out), .sel(\单周期硬布线控制器_1_regdst ));
  // Probe on \总周期数 
  // Probe on \无条件分支数 
  // Probe on \条件分支成功数 
  // Probe on \插入气泡数 
  // Probe on \LoadUse次数 
  Multiplexer #(.select(1), .width(32), .disabled("Z"), .enable("false")) multiplexer_3 (
    .in0(bit_extender_1_out), .in1(bit_extender_2_out), .out(multiplexer_3_out), .sel(SignedExt));
  // Probe on out_3[11:0]
  // Probe on out_4[11:0]
  // Probe on out_5[11:0]
  \MIPS_Regifile下降沿  \mips_regifile下降沿_1  (
    .Din(RDin), .Clk(CLK), .R1(\mips_regifile下降沿_1_r1 ), .R2(\mips_regifile下降沿_1_r2 ), .WE(RegWrite),
    .W_num(\理想流水mem_wb_1_w_2 ), .R1_num(IR[25:21]), .R2_num(IR[20:16]));
  // Probe on MEM_PC
  \理想流水ID_EX  \u_理想流水id_ex_1  (
    .MenToReg_2(\理想流水id_ex_1_mentoreg_2 ), .MenWrite(\理想流水id_ex_1_menwrite ),
    .AluOP_2(\理想流水id_ex_1_aluop_2 ), .AluSrcB_2(\理想流水id_ex_1_alusrcb_2 ),
    .RegWrite_2(\理想流水id_ex_1_regwrite_2 ), .Syscall_2(\理想流水id_ex_1_syscall_2 ), .R1_2(\理想流水id_ex_1_r1_2 ),
    .R2_2(\理想流水id_ex_1_r2_2 ), .W_2(\理想流水id_ex_1_w_2 ), .PC_4_2(\理想流水id_ex_1_pc_4_2 ), .CLK(CLK),
    .BEQ_2(BEQ), .BNE_2(BNE), .EN(not_1_out), .Imm_2(\理想流水id_ex_1_imm_2 ), .BEQ(\单周期硬布线控制器_1_beq ),
    .BNE(\单周期硬布线控制器_1_bne ), .MenToReg(\单周期硬布线控制器_1_memtoreg ), .MemWrite(\单周期硬布线控制器_1_memwrite ),
    .AluOP(\单周期硬布线控制器_1_alu_op ), .AluSrcB(\单周期硬布线控制器_1_alu_src ), .RegWrite(\单周期硬布线控制器_1_regwrite ),
    .Syscall(\单周期硬布线控制器_1_syscall ), .R1(\mips_regifile下降沿_1_r1 ), .R2(\mips_regifile下降沿_1_r2 ),
    .W(multiplexer_2_out), .PC_4(multiplexer_3_out), .Imm(\理想流水if_id_1_ir_2 ), .RST(RST), .Jaddr(out_4),
    .Jaddr_2(out_5));
  // Probe on out_7[11:0]
  Shifter #(.width(32), .shift("ll")) shifter_1 (.in(\理想流水id_ex_1_pc_4_2 ), .\dist (5'b00010), .out(shifter_1_out));
  Multiplexer #(.select(1), .width(32), .disabled("Z"), .enable("false")) multiplexer_4 (
    .in0(\理想流水id_ex_1_r2_2 ), .in1(\理想流水id_ex_1_pc_4_2 ), .out(multiplexer_4_out),
    .sel(\理想流水id_ex_1_alusrcb_2 ));
  Adder #(.width(32)) adder_2 (.a(shifter_1_out), .b(\理想流水id_ex_1_imm_2 ), .out(adder_2_out));  // open: cin, cout
  MIPS_ALU mips_alu_1 (
    .X(\理想流水id_ex_1_r1_2 ), .Y(multiplexer_4_out), .AluOP(\理想流水id_ex_1_aluop_2 ), .Equal(tunnel),
    .Result(mips_alu_1_result), .shamt(multiplexer_5_out));  // open: Result_2
  Multiplexer #(.select(1), .width(5), .disabled("Z"), .enable("false")) multiplexer_5 (
    .in0(IR[10:6]), .in1(5'b10000), .out(multiplexer_5_out), .sel(LUI));
  \理想流水EX_MEM  \u_理想流水ex_mem_1  (
    .MenToReg(\理想流水id_ex_1_mentoreg_2 ), .MemWrite(\理想流水id_ex_1_menwrite ),
    .RegWrite(\理想流水id_ex_1_regwrite_2 ), .Syscall(\理想流水id_ex_1_syscall_2 ), .R(mips_alu_1_result),
    .R2(\理想流水id_ex_1_r2_2 ), .W(\理想流水id_ex_1_w_2 ), .MenToReg_2(\理想流水ex_mem_1_mentoreg_2 ),
    .MenWrite(MemWrite), .RegWrite_2(\理想流水ex_mem_1_regwrite_2 ), .Syscall_2(\理想流水ex_mem_1_syscall_2 ),
    .R_2(\理想流水ex_mem_1_r_2 ), .R2_2(MDin), .W_2(\理想流水ex_mem_1_w_2 ), .CLK(CLK), .EN(not_1_out), .RST(RST),
    .PC(out_5), .PC_2(out_6));
  // Probe on \理想流水ex_mem_1_r_2 
  and and_3 (and_3_out, MemWrite, not_2_out);
  not not_2 (not_2_out, syscall);
  \理想流水MEM_WB  \u_理想流水mem_wb_1  (
    .CLK(CLK), .MenToReg(\理想流水ex_mem_1_mentoreg_2 ), .MenToReg_2(\理想流水mem_wb_1_mentoreg_2 ),
    .RegWrite(\理想流水ex_mem_1_regwrite_2 ), .RegWrite_2(RegWrite), .Syscall(\理想流水ex_mem_1_syscall_2 ),
    .Syscall_2(syscall), .ALU_Data(\理想流水ex_mem_1_r_2 ), .ALU_Data_2(\理想流水mem_wb_1_alu_data_2 ),
    .MEM_ReadData(ram_1_data), .MEM_ReadData_2(\理想流水mem_wb_1_mem_readdata_2 ), .W(\理想流水ex_mem_1_w_2 ),
    .W_2(\理想流水mem_wb_1_w_2 ), .EN(not_1_out), .RST(RST), .PC(out_6), .PC_2(out_7));
  RAM #(.addrWidth(10), .dataWidth(32), .bus("separate"), .Select("high")) ram_1 (
    .addr({2'b00, \理想流水ex_mem_1_r_2 [9:2]}), .din(MDin), .data(ram_1_data), .str(and_3_out), .clk(CLK),
    .ld(not_2_out), .clr(1'b0));  // open: sel
  Multiplexer #(.select(1), .width(32), .disabled("Z"), .enable("false")) multiplexer_6 (
    .in0(\理想流水mem_wb_1_alu_data_2 ), .in1(\理想流水mem_wb_1_mem_readdata_2 ), .out(RDin),
    .sel(\理想流水mem_wb_1_mentoreg_2 ));

  // Other names for the same wires on the sheet: EX_PC[31:0] = out_5; ID_PC[31:0] = out_4; shamt[4:0] = IR[10:6];
  //   LedData[31:0] = out_10; M_PC[31:0] = out_6; IF_PC[31:0] = out_3; PC[31:0] = out_3; WB_PC[31:0] = out_7

  // Notes on the sheet:
  //   中断源
  //   中断等待指示
  //   IF
  //   指令存储器
  //   数码管输出
  //   IR
  //   contents of rom_1 (hex, n*v repeats v):
  //   20100000 20110000 20120000 20130000 36100000 36310001 36520002 36730003 ae100000 ae110004 ae120008
  //   ae13000c 2002000a 20110000 20120000 20130000 c
  //   rs
  //   rt
  //   rd
  //   imm
  //   JMP
  //   JR
  //   Beq
  //   Bne
  //   LB
  //   MemToReg
  //   MemWrite
  //   AluOP
  //   AluSrcB
  //   RegWrite
  //   JAL
  //   RegDst
  //   Syscall
  //   ID
  //   流水调试日志用
  //   EX
  //   MEM
  //   WB
endmodule
module \气泡流水线  (
  output RegWrite,
  output MemWrite,
  output [31:0] RDin,
  output [31:0] out_4,
  output [31:0] out_5,
  output [31:0] out_6,
  output [31:0] out_7,
  output [31:0] out_8,
  output [31:0] MDin,
  output [31:0] out_10
);

  wire and_1_out, and_2_out, BEQ, BLTZ, BNE, CLK, comparator_1_eq, comparator_2_eq, EX_JAL, ex_mem_1_jal_2,
       ex_mem_1_lb_2, ex_mem_1_mentoreg_2, ex_mem_1_syscall_2, EX_RegWrite, Go, id_ex_1_alusrcb_2,
       id_ex_1_lb_2, id_ex_1_mentoreg_2, id_ex_1_menwrite_2, id_ex_1_syscall_2, \ID_EX气泡 , ID_SysCall, IR1,
       IR2, IR3, JMP, JR, LB, LUI, MEM_RegWrite, mem_wb_1_mentoreg_2, multiplexer_1_out, multiplexer_12_out,
       not_1_out, not_2_out, not_3_out, Pause, \PC_IF_ID使能 , R1_Used, R2_Used, SignedExt, syscall, tunnel,
       W1, W2, W3, WB_JAL, \修改的单周期硬布线控制器_1_alu_src , \修改的单周期硬布线控制器_1_beq , \修改的单周期硬布线控制器_1_bltz ,
       \修改的单周期硬布线控制器_1_bne , \修改的单周期硬布线控制器_1_jal , \修改的单周期硬布线控制器_1_jmp , \修改的单周期硬布线控制器_1_jr ,
       \修改的单周期硬布线控制器_1_lb , \修改的单周期硬布线控制器_1_lui , \修改的单周期硬布线控制器_1_memtoreg , \修改的单周期硬布线控制器_1_memwrite ,
       \修改的单周期硬布线控制器_1_regdst , \修改的单周期硬布线控制器_1_regwrite , \插入气泡 ;
  wire [1:0] \mem_wb_1_lb低两位_2 ;
  wire [3:0] id_ex_1_aluop_2, \修改的单周期硬布线控制器_1_alu_op ;
  wire [4:0] EX_W_num, id_ex_1_shamt_2, MEM_W_num, mem_wb_1_w_2, multiplexer_2_out, multiplexer_3_out,
       multiplexer_7_out, multiplexer_9_out, R1_num, R2_num;
  wire [15:0] counter_2_q, counter_3_q, \LoadUse次数 , \总周期数 , \插入气泡数 , \无条件分支数 , \条件分支成功数 ;
  wire [31:0] a0, adder_2_out, bit_extender_1_out, bit_extender_2_out, BLTZ_result, ex_mem_1_pc_4_2,
       ex_mem_1_r1_2, ex_mem_1_r2_3, ex_mem_1_r_2, EX_R1, id_ex_1_imm_2, id_ex_1_pc_4_2, id_ex_1_r2_2,
       if_id_1_jaddr_2, if_id_1_pc_4_2, IR, Jaddr, \j型指令转跳地址判断器_1_out_12 , mem_wb_1_alu_data_2,
       mem_wb_1_mem_readdata_2, \mips_regifile下降沿_1_r1 , \mips_regifile下降沿_1_r2 , multiplexer_5_out,
       multiplexer_8_out, multiplexer_13_out, multiplexer_14_out, PC_4, ram_1_data, rom_1_data,
       shifter_1_out, v0, WB_PC_4, WB_R1, WB_R2;

  Clock #(.highDuration(1), .lowDuration(1)) clock_1 (.out(CLK));
  Button _1 (.out(IR1));
  Button _2 (.out(IR2));
  Button _3 (.out(IR3));
  // Probe on \j型指令转跳地址判断器_1_out_12 
  Button \u_继续运行  (.out(Go));
  LED #(.active("true")) led_1 (.in(W1));
  LED #(.active("true")) led_2 (.in(W2));
  LED #(.active("true")) led_3 (.in(W3));
  Register #(.width(32), .trigger("rising"), .Select("low")) PC (
    .D(\j型指令转跳地址判断器_1_out_12 ), .en(\PC_IF_ID使能 ), .Q(out_4), .clk(CLK), .clr(1'b0));
  \J型指令转跳地址判断器  \j型指令转跳地址判断器_1  (
    .JR(JR), .JMP(JMP), .BNE(BNE), .in_2(tunnel), .BEQ(BEQ), .JAL(EX_JAL), .BLTZ(multiplexer_1_out),
    .out_12(\j型指令转跳地址判断器_1_out_12 ), .PC_4(PC_4), .BNE_BEQ_BLTZaddr(adder_2_out), .J_JALaddr(Jaddr),
    .JRaddr(EX_R1), .\转跳信号灯 (\插入气泡 ));
  Hex_Digit_Display hex_digit_display_1 (.value(out_10[31:28]));  // open: dp
  // Probe on \总周期数 
  // Probe on \无条件分支数 
  // Probe on \条件分支成功数 
  // Probe on \插入气泡数 
  // Probe on \LoadUse次数 
  // Probe on out_4[11:0]
  // Probe on out_5[11:0]
  // Probe on out_6[11:0]
  // Probe on out_7[11:0]
  // Probe on out_8[11:0]
  Adder #(.width(32)) adder_1 (.a(out_4), .b(32'h4), .out(PC_4));  // open: cin, cout
  Multiplexer #(.select(1), .width(1), .disabled("Z"), .enable("false")) multiplexer_1 (
    .in0(1'b0), .in1(BLTZ), .out(multiplexer_1_out), .sel(comparator_1_eq));
  Comparator #(.width(32), .mode("unsigned")) comparator_1 (
    .a(BLTZ_result), .b(32'h1), .eq(comparator_1_eq));  // open: gt, lt
  Hex_Digit_Display hex_digit_display_2 (.value(out_10[27:24]));  // open: dp
  Hex_Digit_Display hex_digit_display_3 (.value(out_10[23:20]));  // open: dp
  Hex_Digit_Display hex_digit_display_4 (.value(out_10[15:12]));  // open: dp
  Hex_Digit_Display hex_digit_display_5 (.value(out_10[19:16]));  // open: dp
  ROM #(.addrWidth(10), .dataWidth(32), .Select("high")) rom_1 (.addr(out_4[11:2]), .data(rom_1_data));
  Hex_Digit_Display hex_digit_display_6 (.value(out_10[7:4]));  // open: dp
  Hex_Digit_Display hex_digit_display_7 (.value(out_10[11:8]));  // open: dp
  // Probe on \总周期数 
  IF_ID if_id_1 (
    .IR(rom_1_data), .Jaddr({out_4[31:28], rom_1_data[25:0], 2'b00}), .PC_4(PC_4), .IR_2(IR),
    .Jaddr_2(if_id_1_jaddr_2), .PC_4_2(if_id_1_pc_4_2), .Reset(\插入气泡 ), .EN(\PC_IF_ID使能 ), .CLK(CLK),
    .PC(out_4), .PC_2(out_5));
  Hex_Digit_Display hex_digit_display_8 (.value(out_10[3:0]));  // open: dp
  \修改的单周期硬布线控制器  \u_修改的单周期硬布线控制器_1  (
    .OP(IR[31:26]), .Func(IR[5:0]), .ALU_OP(\修改的单周期硬布线控制器_1_alu_op ), .MemToReg(\修改的单周期硬布线控制器_1_memtoreg ),
    .MemWrite(\修改的单周期硬布线控制器_1_memwrite ), .ALU_SRC(\修改的单周期硬布线控制器_1_alu_src ),
    .RegWrite(\修改的单周期硬布线控制器_1_regwrite ), .SysCALL(ID_SysCall), .SignedExt(SignedExt),
    .RegDst(\修改的单周期硬布线控制器_1_regdst ), .Beq(\修改的单周期硬布线控制器_1_beq ), .Bne(\修改的单周期硬布线控制器_1_bne ),
    .JR(\修改的单周期硬布线控制器_1_jr ), .JMP(\修改的单周期硬布线控制器_1_jmp ), .JAL(\修改的单周期硬布线控制器_1_jal ),
    .LUI(\修改的单周期硬布线控制器_1_lui ), .BLTZ(\修改的单周期硬布线控制器_1_bltz ), .LB(\修改的单周期硬布线控制器_1_lb ));  // open: ERET
  \源寄存器使用情况封装电路  \u_源寄存器使用情况封装电路_1  (.OP(IR[31:26]), .Func(IR[5:0]), .R1_Used(R1_Used), .R2_Used(R2_Used));
  // Probe on IR[25:21]
  // Probe on IR[20:16]
  Multiplexer #(.select(1), .width(5), .disabled("Z"), .enable("false")) multiplexer_2 (
    .in0(IR[20:16]), .in1(IR[15:11]), .out(multiplexer_2_out), .sel(\修改的单周期硬布线控制器_1_regdst ));
  assign bit_extender_1_out = {{16{IR[15]}}, IR[15:0]};  // Bit_Extender bit_extender_1
  assign bit_extender_2_out = {{16{1'b0}}, IR[15:0]};  // Bit_Extender bit_extender_2
  Multiplexer #(.select(1), .width(5), .disabled("Z"), .enable("false")) multiplexer_3 (
    .in0(IR[25:21]), .in1({5{1'b1}}), .out(multiplexer_3_out), .sel(\修改的单周期硬布线控制器_1_jr ));
  Multiplexer #(.select(1), .width(5), .disabled("Z"), .enable("false")) multiplexer_4 (
    .in0(IR[20:16]), .in1(5'b00100), .out(R2_num), .sel(ID_SysCall));
  Multiplexer #(.select(1), .width(32), .disabled("Z"), .enable("false")) multiplexer_5 (
    .in0(bit_extender_1_out), .in1(bit_extender_2_out), .out(multiplexer_5_out), .sel(SignedExt));
  Multiplexer #(.select(1), .width(5), .disabled("Z"), .enable("false")) multiplexer_6 (
    .in0(multiplexer_3_out), .in1(5'b00010), .out(R1_num), .sel(ID_SysCall));
  Multiplexer #(.select(1), .width(5), .disabled("Z"), .enable("false")) multiplexer_7 (
    .in0(mem_wb_1_w_2), .in1({5{1'b1}}), .out(multiplexer_7_out), .sel(WB_JAL));
  not not_1 (not_1_out, Pause);
  \MIPS_Regifile下降沿  \mips_regifile下降沿_1  (
    .Din(RDin), .Clk(CLK), .R1(\mips_regifile下降沿_1_r1 ), .R2(\mips_regifile下降沿_1_r2 ), .WE(RegWrite),
    .W_num(multiplexer_7_out), .R1_num(R1_num), .R2_num(R2_num));
  ID_EX id_ex_1 (
    .AluOP(\修改的单周期硬布线控制器_1_alu_op ), .AluSrcB(\修改的单周期硬布线控制器_1_alu_src ), .R1(\mips_regifile下降沿_1_r1 ),
    .R2(\mips_regifile下降沿_1_r2 ), .W(multiplexer_2_out), .Jaddr(if_id_1_jaddr_2), .AluOP_2(id_ex_1_aluop_2),
    .AluSrcB_2(id_ex_1_alusrcb_2), .R1_2(EX_R1), .R2_2(id_ex_1_r2_2), .W_2(EX_W_num), .Imm_2(id_ex_1_imm_2),
    .Jaddr_2(Jaddr), .PC_4_2(id_ex_1_pc_4_2), .Imm(multiplexer_5_out), .PC_4(if_id_1_pc_4_2),
    .RST(\ID_EX气泡 ), .EN(not_1_out), .CLK(CLK), .JR_2(JR), .JR(\修改的单周期硬布线控制器_1_jr ),
    .JMP(\修改的单周期硬布线控制器_1_jmp ), .JMP_2(JMP), .Bne(\修改的单周期硬布线控制器_1_bne ), .Bne_2(BNE),
    .Beq(\修改的单周期硬布线控制器_1_beq ), .Beq_2(BEQ), .BLTZ(\修改的单周期硬布线控制器_1_bltz ), .BLTZ_2(BLTZ),
    .LUI(\修改的单周期硬布线控制器_1_lui ), .LUI_2(LUI), .MenWrite(\修改的单周期硬布线控制器_1_memwrite ),
    .MenWrite_2(id_ex_1_menwrite_2), .MenToReg(\修改的单周期硬布线控制器_1_memtoreg ), .MenToReg_2(id_ex_1_mentoreg_2),
    .JAL(\修改的单周期硬布线控制器_1_jal ), .JAL_2(EX_JAL), .SysCall(ID_SysCall), .SysCall_2(id_ex_1_syscall_2),
    .LB(\修改的单周期硬布线控制器_1_lb ), .LB_2(id_ex_1_lb_2), .RegWrite(\修改的单周期硬布线控制器_1_regwrite ),
    .RegWrite_2(EX_RegWrite), .shamt_2(id_ex_1_shamt_2), .shamt(IR[10:6]), .PC(out_5), .PC_2(out_6));  // open: ERET, ERET_2
  Counter #(.width(16), .max('hffff), .ongoal("wrap"), .trigger("rising"), .behavior("old")) counter_1 (
    .count(not_1_out), .Q(\总周期数 ), .clk(CLK), .clr(1'b0));  // open: load, D, carry, preset
  Multiplexer #(.select(1), .width(32), .disabled("Z"), .enable("false")) multiplexer_8 (
    .in0(id_ex_1_r2_2), .in1(id_ex_1_imm_2), .out(multiplexer_8_out), .sel(id_ex_1_alusrcb_2));
  Shifter #(.width(32), .shift("ll")) shifter_1 (.in(id_ex_1_imm_2), .\dist (5'b00010), .out(shifter_1_out));
  // Probe on \总周期数 
  Multiplexer #(.select(1), .width(5), .disabled("Z"), .enable("false")) multiplexer_9 (
    .in0(id_ex_1_shamt_2), .in1(5'b10000), .out(multiplexer_9_out), .sel(LUI));
  Adder #(.width(32)) adder_2 (.a(shifter_1_out), .b(id_ex_1_pc_4_2), .out(adder_2_out));  // open: cin, cout
  MIPS_ALU mips_alu_1 (
    .X(EX_R1), .Y(multiplexer_8_out), .AluOP(id_ex_1_aluop_2), .Equal(tunnel), .Result(BLTZ_result),
    .shamt(multiplexer_9_out));  // open: Result_2
  // Probe on BLTZ_result
  Multiplexer #(.select(1), .width(32), .disabled("Z"), .enable("false")) multiplexer_10 (
    .in0({32{1'b0}}), .in1(WB_R1), .out(v0), .sel(syscall));
  EX_MEM ex_mem_1 (
    .LB(id_ex_1_lb_2), .SysCall(id_ex_1_syscall_2), .RegWrite(EX_RegWrite), .MenToReg(id_ex_1_mentoreg_2),
    .R(BLTZ_result), .R2(id_ex_1_r2_2), .W(EX_W_num), .LB_2(ex_mem_1_lb_2), .SysCall_2(ex_mem_1_syscall_2),
    .RegWrite_2(MEM_RegWrite), .MenToReg_2(ex_mem_1_mentoreg_2), .R_2(ex_mem_1_r_2), .R2_2(MDin),
    .W_2(MEM_W_num), .RST(1'b0), .EN(not_1_out), .CLK(CLK), .MenWrite(id_ex_1_menwrite_2),
    .MenWrite_2(MemWrite), .JAL_2(ex_mem_1_jal_2), .JAL(EX_JAL), .PC_4(id_ex_1_pc_4_2),
    .PC_4_2(ex_mem_1_pc_4_2), .R2_3(ex_mem_1_r2_3), .R1(EX_R1), .R1_2(ex_mem_1_r1_2), .PC(out_6), .PC_2(out_7));  // open: ERET, ERET_2
  // Probe on ex_mem_1_r_2
  Multiplexer #(.select(1), .width(32), .disabled("Z"), .enable("false")) multiplexer_11 (
    .in0({32{1'b0}}), .in1(WB_R2), .out(a0), .sel(syscall));
  and and_1 (and_1_out, MemWrite, not_2_out);
  not not_2 (not_2_out, syscall);
  Comparator #(.width(32), .mode("unsigned")) comparator_2 (.a(v0), .b(32'ha), .eq(comparator_2_eq));  // open: gt, lt
  not not_3 (not_3_out, comparator_2_eq);
  MEM_WB mem_wb_1 (
    .LB(ex_mem_1_lb_2), .SysCall(ex_mem_1_syscall_2), .RegWrite(MEM_RegWrite),
    .MenToReg(ex_mem_1_mentoreg_2), .ALU_Data(ex_mem_1_r_2), .MEM_ReadData(ram_1_data), .W(MEM_W_num),
    .LB_2(LB), .SysCall_2(syscall), .RegWrite_2(RegWrite), .MenToReg_2(mem_wb_1_mentoreg_2),
    .ALU_Data_2(mem_wb_1_alu_data_2), .MEM_ReadData_2(mem_wb_1_mem_readdata_2), .W_2(mem_wb_1_w_2),
    .RST(1'b0), .EN(not_1_out), .CLK(CLK), .JAL(ex_mem_1_jal_2), .JAL_2(WB_JAL), .PC_4(ex_mem_1_pc_4_2),
    .PC_4_2(WB_PC_4), .\LB低两位 (ex_mem_1_r_2[1:0]), .\LB低两位_2 (\mem_wb_1_lb低两位_2 ), .R1(ex_mem_1_r1_2),
    .R1_2(WB_R1), .R2(ex_mem_1_r2_3), .R2_2(WB_R2), .PC(out_7), .PC_2(out_8));  // open: ERET, ERET_2
  RAM #(.addrWidth(10), .dataWidth(32), .bus("separate"), .Select("high")) ram_1 (
    .addr({2'b00, ex_mem_1_r_2[9:2]}), .din(MDin), .data(ram_1_data), .str(and_1_out), .clk(CLK),
    .ld(not_2_out), .clr(1'b0));  // open: sel
  Multiplexer #(.select(1), .width(1), .disabled("Z"), .enable("false")) multiplexer_12 (
    .in0(1'b0), .in1(Go), .out(multiplexer_12_out), .sel(comparator_2_eq));
  xor xor_1 (Pause, comparator_2_eq, multiplexer_12_out);
  Counter #(.width(16), .max('hffff), .ongoal("wrap"), .trigger("rising"), .behavior("old")) counter_2 (
    .count(\ID_EX气泡 ), .Q(counter_2_q), .clk(CLK), .clr(1'b0));  // open: load, D, carry, preset
  Multiplexer #(.select(1), .width(32), .disabled("Z"), .enable("false")) multiplexer_13 (
    .in0(mem_wb_1_alu_data_2), .in1(mem_wb_1_mem_readdata_2), .out(multiplexer_13_out),
    .sel(mem_wb_1_mentoreg_2));
  and and_2 (and_2_out, syscall, not_3_out);
  Multiplexer #(.select(1), .width(32), .disabled("Z"), .enable("false")) multiplexer_14 (
    .in0(out_10), .in1(a0), .out(multiplexer_14_out), .sel(and_2_out));
  Counter #(.width(16), .max('hffff), .ongoal("wrap"), .trigger("rising"), .behavior("old")) counter_3 (
    .count(\插入气泡 ), .Q(counter_3_q), .clk(CLK), .clr(1'b0));  // open: load, D, carry, preset
  Register #(.width(32), .trigger("rising"), .Select("low")) register_1 (
    .D(multiplexer_14_out), .Q(out_10), .clk(CLK));  // open: en, clr
  Subtractor #(.width(16)) subtractor_1 (.a(counter_2_q), .b(counter_3_q), .out(\插入气泡数 ));  // open: bin, bout
  \数据相关检测  \u_数据相关检测器  (
    .Pause(Pause), .\转跳插入气泡 (\插入气泡 ), .\ID_EX气泡 (\ID_EX气泡 ), .PC_IF_ID_EN(\PC_IF_ID使能 ),
    .MEM_RegWrite(MEM_RegWrite), .EX_RegWrite(EX_RegWrite), .EX_W_num(EX_W_num), .MEM_W_num(MEM_W_num),
    .R2_Used(R2_Used), .R2_num(R2_num), .R1_Used(R1_Used), .R1_num(R1_num));
  \写入寄存器数据判断处理器  \u_写入寄存器数据判断处理器_1  (
    .in_3(multiplexer_13_out), .WB_PC_4(WB_PC_4), .out_6(RDin), .LB(LB), .WB_JAL(WB_JAL),
    .\LB低两位 (\mem_wb_1_lb低两位_2 ));

  // Other names for the same wires on the sheet: IF_PC[31:0] = out_4; PC[31:0] = out_4; EX_PC[31:0] = out_6;
  //   ID_PC[31:0] = out_5; JRaddr[31:0] = EX_R1; LedData[31:0] = out_10; MEM_PC[31:0] = out_7; WB_PC[31:0] = out_8

  // Notes on the sheet:
  //   中断源
  //   中断等待指示
  //   IF
  //   指令存储器
  //   数码管输出
  //   contents of rom_1 (hex, n*v repeats v):
  //   20110001 8000c05 20110001 20120002 20130003 8000c09 20110001 20120002 20130003 8000c0d 20110001
  //   20120002 20130003 8000c11 20110001 20120002 20130003 c000cb8 20100001 20110001 118fc0 112020
  //   20020022 c 118882 12200001 8000c15 112020 20020022 c 20110001 118880 112020 20020022 c 12200001
  //   8000c1f 20110001 118fc0 112020 20020022 c 1188c3 112020 20020022 c 118903 112020 20020022 c 118903
  //   112020 20020022 c 118903 112020 20020022 c 118903 112020 20020022 c 118903 112020 20020022 c 118903
  //   112020 20020022 c 118903 112020 20020022 c 20100001 109fc0 139fc3 8021 2012000c 24160003 26100001
  //   3210000f 20080008 20090001 139900 2709825 132020 20020022 c 1094022 1500fff9 22100001 2018000f
  //   2188024 108700 20080008 20090001 139902 2709825 132021 20020022 c 1094022 1500fff9 108702 2c9b022
  //   12c00001 8000c50 4020 1084027 84400 3508ffff 82021 20020022 c 2010ffff 20110000 ae300000 22100001
  //   22310004 ae300000 22100001 22310004 ae300000 22100001 22310004 ae300000 22100001 22310004 ae300000
  //   22100001 22310004 ae300000 22100001 22310004 ae300000 22100001 22310004 ae300000 22100001 22310004
  //   ae300000 22100001 22310004 ae300000 22100001 22310004 ae300000 22100001 22310004 ae300000 22100001
  //   22310004 ae300000 22100001 22310004 ae300000 22100001 22310004 ae300000 22100001 22310004 ae300000
  //   22100001 22310004 22100001 8020 2011003c 8e130000 8e340000 274402a 11000002 ae330000 ae140000
  //   2231fffc 1611fff8 102020 20020022 c 22100004 2011003c 1611fff2 2002000a c 20100000 22100001 102020
  //   20020022 c 22100002 102020 20020022 c 22100003 102020 20020022 c 22100004 102020 20020022 c 22100005
  //   102020 20020022 c 22100006 102020 20020022 c 22100007 102020 20020022 c 22100008 102020 20020022
  //   20020022 c 3e00008
  //   IR
  //   OP
  //   Func
  //   rs
  //   rt
  //   rd
  //   shamt
  //   imm
  //   RegDst
  //   SignedExt
  //   $a0
  //   ID
  //   RegDst
  //   $v0
  //   为方便自动评测，需要输出PC，IR，寄存器文件写入端口RDin，内存写入端口MDin等信号
  //   LUI
  //   Bne
  //   BLTZ
  //   Beq
  //   EX
  //   JMP
  //   JAL
  //   JR
  //   AluSrcB
  //   AluOP
  //   数码管输出应该用寄存器锁存，否则显示数据只能一闪而过
  //   总复位信号应将除ROM以外所有存储组件全部清零
  //   MEM
  //   MemWrite
  //   LB
  //   Syscall
  //   WB
  //   RegWrite
  //   MemToReg
endmodule

module \气泡流水线_单级中断  (
  input  IR1,
  input  IR2,
  input  IR3,
  output RegWrite,
  output MemWrite,
  output [31:0] RDin,
  output [31:0] MDin,
  output [31:0] out_8,
  output [31:0] out_9,
  output [31:0] out_10,
  output [31:0] out_11,
  output [31:0] out_12,
  output [31:0] out_13
);

  wire \_1号中断清零信号 , \_2号中断清零信号 , \_3号中断清零信号 , and_6_out, and_7_out, BEQ, BLTZ, BNE, CLK, comparator_1_eq,
       comparator_2_eq, comparator_3_eq, comparator_4_eq, comparator_5_eq, comparator_6_eq,
       demultiplexer_1_out1, demultiplexer_1_out2, demultiplexer_1_out3, ERET, EX_JAL, ex_mem_1_eret_2,
       ex_mem_1_jal_2, ex_mem_1_lb_2, ex_mem_1_mentoreg_2, ex_mem_1_syscall_2, EX_RegWrite, Go,
       id_ex_1_alusrcb_2, id_ex_1_eret_2, id_ex_1_lb_2, id_ex_1_mentoreg_2, id_ex_1_menwrite_2,
       id_ex_1_syscall_2, \ID_EX气泡 , ID_SysCall, IE, IR1_t, IR2_t, IR3_t, IRA, IRB, IRC, JMP, JR, LB, LUI,
       MEM_RegWrite, mem_wb_1_mentoreg_2, multiplexer_5_out, multiplexer_17_out, not_1_out, not_2_out,
       not_3_out, or_1_out, or_3_out, or_4_out, Pause, \PC_IF_ID使能 , priority_encoder_1_gs, R1_Used, R2_Used,
       SignedExt, syscall, tunnel, W1, W2, W3, WB_JAL, \中断信号 , \中断信息记录信号 , \中断按键参考电路_1__1号与中断屏蔽位与 ,
       \中断按键参考电路_1__2号与中断屏蔽位与 , \中断按键参考电路_1__3号与中断屏蔽位与 , \中断清零信号 , \修改的单周期硬布线控制器_1_alu_src ,
       \修改的单周期硬布线控制器_1_beq , \修改的单周期硬布线控制器_1_bltz , \修改的单周期硬布线控制器_1_bne , \修改的单周期硬布线控制器_1_eret ,
       \修改的单周期硬布线控制器_1_jal , \修改的单周期硬布线控制器_1_jmp , \修改的单周期硬布线控制器_1_jr , \修改的单周期硬布线控制器_1_lb ,
       \修改的单周期硬布线控制器_1_lui , \修改的单周期硬布线控制器_1_memtoreg , \修改的单周期硬布线控制器_1_memwrite , \修改的单周期硬布线控制器_1_regdst ,
       \修改的单周期硬布线控制器_1_regwrite , \插入气泡 , \气泡_中断 ;
  wire [1:0] \mem_wb_1_lb低两位_2 , multiplexer_2_out, priority_encoder_1_out, \中断编号 ;
  wire [3:0] id_ex_1_aluop_2, \修改的单周期硬布线控制器_1_alu_op ;
  wire [4:0] EX_W_num, id_ex_1_shamt_2, MEM_W_num, mem_wb_1_w_2, multiplexer_8_out, multiplexer_9_out,
       multiplexer_12_out, multiplexer_16_out, R1_num, R2_num;
  wire [15:0] counter_2_q, counter_3_q, \LoadUse次数 , \总周期数 , \插入气泡数 , \无条件分支数 , \条件分支成功数 ;
  wire [31:0] a0, adder_2_out, bit_extender_1_out, bit_extender_2_out, BLTZ_result, EPC, ex_mem_1_pc_4_2,
       ex_mem_1_r1_2, ex_mem_1_r2_3, ex_mem_1_r_2, EX_PC_4, EX_R1, id_ex_1_imm_2, id_ex_1_r2_2,
       if_id_1_jaddr_2, if_id_1_pc_4_2, IR, Jaddr, mem_wb_1_alu_data_2, mem_wb_1_mem_readdata_2,
       \mips_regifile下降沿_1_r1 , \mips_regifile下降沿_1_r2 , multiplexer_1_out, multiplexer_3_out,
       multiplexer_4_out, multiplexer_6_out, multiplexer_10_out, multiplexer_15_out, multiplexer_18_out,
       multiplexer_19_out, PC_4, ram_1_data, rom_1_data, shifter_1_out, v0, WB_PC_4, WB_R1, WB_R2, \正常程序地址 ;

  Clock #(.highDuration(1), .lowDuration(1)) clock_1 (.out(CLK));
  Button _1 ();  // open: out
  Button _2 ();  // open: out
  Button _3 ();  // open: out
  Button \u_继续运行  (.out(Go));
  LED #(.active("true")) led_1 (.in(W1));
  LED #(.active("true")) led_2 (.in(W2));
  LED #(.active("true")) led_3 (.in(W3));
  \中断按键参考电路  \u_中断按键参考电路_1  (
    .\_1号同步清零信号 (\_1号中断清零信号 ), .\_1号中断 (IR1_t), .CLK(CLK), .\_1号中断等待指示灯 (W1), .\_2号中断 (IR2_t),
    .\_2号中断等待指示灯 (W2), .\_3号中断 (IR3_t), .\_3号中断等待指示灯 (W3), .\_2号同步清零信号 (\_2号中断清零信号 ),
    .\_3号同步清零信号 (\_3号中断清零信号 ), .\_1号与中断屏蔽位与 (\中断按键参考电路_1__1号与中断屏蔽位与 ),
    .\_2号与中断屏蔽位与 (\中断按键参考电路_1__2号与中断屏蔽位与 ), .\_3号与中断屏蔽位与 (\中断按键参考电路_1__3号与中断屏蔽位与 ));
  Hex_Digit_Display hex_digit_display_1 (.value(out_13[31:28]));  // open: dp
  // Probe on \总周期数 
  // Probe on \无条件分支数 
  // Probe on \条件分支成功数 
  // Probe on \插入气泡数 
  // Probe on \LoadUse次数 
  // Probe on out_8[11:0]
  // Probe on out_9[11:0]
  // Probe on out_10[11:0]
  // Probe on out_11[11:0]
  // Probe on out_12[11:0]
  Priority_Encoder #(.select(2), .disabled("Z")) priority_encoder_1 (
    .in0(1'b0), .in1(\中断按键参考电路_1__1号与中断屏蔽位与 ), .in2(\中断按键参考电路_1__2号与中断屏蔽位与 ), .in3(\中断按键参考电路_1__3号与中断屏蔽位与 ),
    .out(priority_encoder_1_out), .gs(priority_encoder_1_gs));  // open: en_out, en_in
  Comparator #(.width(16), .mode("twosComplement")) comparator_1 (
    .a(16'h23b), .b(\总周期数 ), .eq(comparator_1_eq));  // open: gt, lt
  Comparator #(.width(16), .mode("twosComplement")) comparator_2 (
    .a(\总周期数 ), .b(16'h1), .eq(comparator_2_eq));  // open: gt, lt
  Comparator #(.width(16), .mode("twosComplement")) comparator_3 (
    .a(\总周期数 ), .b(16'h4), .eq(comparator_3_eq));  // open: gt, lt
  Comparator #(.width(16), .mode("twosComplement")) comparator_4 (
    .a(\总周期数 ), .b(16'h7), .eq(comparator_4_eq));  // open: gt, lt
  Hex_Digit_Display hex_digit_display_2 (.value(out_13[27:24]));  // open: dp
  Hex_Digit_Display hex_digit_display_3 (.value(out_13[23:20]));  // open: dp
  Register #(.width(32), .trigger("rising"), .Select("low")) u_EPC (
    .D(\正常程序地址 ), .en(\中断信息记录信号 ), .Q(EPC), .clk(CLK));  // open: clr
  Multiplexer #(.select(1), .width(32), .disabled("Z"), .enable("false")) multiplexer_1 (
    .in0(\正常程序地址 ), .in1(EPC), .out(multiplexer_1_out), .sel(ERET));
  Multiplexer #(.select(1), .width(2), .disabled("Z"), .enable("false")) multiplexer_2 (
    .in0(2'b00), .in1(priority_encoder_1_out), .out(multiplexer_2_out), .sel(\中断信息记录信号 ));
  or or_1 (or_1_out, comparator_1_eq, comparator_2_eq);
  Pull_Resistor #(.pull(0)) pull_resistor_1 (.node(IRA));
  assign IRA = or_1_out ? ~CLK : 1'bz;  // Controlled_Inverter controlled_inverter_1
  Pull_Resistor #(.pull(0)) pull_resistor_2 (.node(IRB));
  assign IRB = comparator_3_eq ? ~CLK : 1'bz;  // Controlled_Inverter controlled_inverter_2
  Pull_Resistor #(.pull(0)) pull_resistor_3 (.node(IRC));
  assign IRC = comparator_4_eq ? ~CLK : 1'bz;  // Controlled_Inverter controlled_inverter_3
  Hex_Digit_Display hex_digit_display_4 (.value(out_13[19:16]));  // open: dp
  Hex_Digit_Display hex_digit_display_5 (.value(out_13[15:12]));  // open: dp
  and and_1 (\_1号中断清零信号 , demultiplexer_1_out1, ERET);
  and and_2 (\_2号中断清零信号 , demultiplexer_1_out2, ERET);
  and and_3 (\_3号中断清零信号 , demultiplexer_1_out3, ERET);
  Multiplexer #(.select(2), .width(32), .disabled("Z"), .enable("false")) multiplexer_3 (
    .in0(multiplexer_1_out), .in1(32'h30ac), .in2(32'h3150), .in3(32'h31f4), .out(multiplexer_3_out),
    .sel(multiplexer_2_out));
  // Probe on multiplexer_3_out
  and and_4 (\中断信号 , priority_encoder_1_gs, ~IE);  // AND_Gate
  Hex_Digit_Display hex_digit_display_6 (.value(out_13[11:8]));  // open: dp
  Hex_Digit_Display hex_digit_display_7 (.value(out_13[7:4]));  // open: dp
  // Probe on \总周期数 
  or or_2 (\中断清零信号 , \_1号中断清零信号 , \_2号中断清零信号 , \_3号中断清零信号 );
  and and_5 (\中断信息记录信号 , \中断信号 , ~\中断清零信号 );  // AND_Gate
  Register #(.width(2), .trigger("rising"), .Select("low")) \u_中断编号  (
    .D(multiplexer_2_out), .en(\中断信息记录信号 ), .Q(\中断编号 ), .clk(CLK));  // open: clr
  Hex_Digit_Display hex_digit_display_8 (.value(out_13[3:0]));  // open: dp
  Demultiplexer #(.select(2), .width(1), .tristate("false"), .disabled("Z"), .enable("false")) demultiplexer_1 (
    .out1(demultiplexer_1_out1), .out2(demultiplexer_1_out2), .out3(demultiplexer_1_out3), .in(1'b1),
    .sel(\中断编号 ));  // open: out0
  or or_3 (or_3_out, \中断信息记录信号 , \PC_IF_ID使能 );
  // Probe on \正常程序地址 
  Register #(.width(32), .trigger("rising"), .Select("low")) PC (
    .D(multiplexer_3_out), .en(or_3_out), .Q(out_8), .clk(CLK), .clr(1'b0));
  \J型指令转跳地址判断器  \j型指令转跳地址判断器_1  (
    .JR(JR), .JMP(JMP), .BNE(BNE), .in_2(tunnel), .BEQ(BEQ), .JAL(EX_JAL), .BLTZ(multiplexer_5_out),
    .out_12(\正常程序地址 ), .PC_4(multiplexer_4_out), .BNE_BEQ_BLTZaddr(adder_2_out), .J_JALaddr(Jaddr),
    .JRaddr(EX_R1), .\转跳信号灯 (\插入气泡 ));
  Register #(.width(1), .trigger("rising"), .Select("low")) u_IE (
    .D(\中断信号 ), .en(\中断信息记录信号 ), .Q(IE), .clk(CLK), .clr(ERET));
  Adder #(.width(32)) adder_1 (.a(out_8), .b(32'h4), .out(PC_4));  // open: cin, cout
  Multiplexer #(.select(1), .width(32), .disabled("Z"), .enable("false")) multiplexer_4 (
    .in0(PC_4), .in1(multiplexer_6_out), .out(multiplexer_4_out), .sel(\中断信息记录信号 ));
  Multiplexer #(.select(1), .width(1), .disabled("Z"), .enable("false")) multiplexer_5 (
    .in0(1'b0), .in1(BLTZ), .out(multiplexer_5_out), .sel(comparator_5_eq));
  Comparator #(.width(32), .mode("unsigned")) comparator_5 (
    .a(BLTZ_result), .b(32'h1), .eq(comparator_5_eq));  // open: gt, lt
  or or_4 (or_4_out, \PC_IF_ID使能 , \中断信息记录信号 );
  or or_5 (\气泡_中断 , \中断信息记录信号 , \插入气泡 , ERET);
  ROM #(.addrWidth(10), .dataWidth(32), .Select("high")) rom_1 (.addr(out_8[11:2]), .data(rom_1_data));
  Multiplexer #(.select(1), .width(32), .disabled("Z"), .enable("false")) multiplexer_6 (
    .in0(EX_PC_4), .in1(out_9), .out(multiplexer_6_out), .sel(\ID_EX气泡 ));
  IF_ID if_id_1 (
    .IR(rom_1_data), .Jaddr({out_8[31:28], rom_1_data[25:0], 2'b00}), .PC_4(PC_4), .IR_2(IR),
    .Jaddr_2(if_id_1_jaddr_2), .PC_4_2(if_id_1_pc_4_2), .Reset(\气泡_中断 ), .EN(or_4_out), .CLK(CLK),
    .PC(out_8), .PC_2(out_9));
  \源寄存器使用情况封装电路  \u_源寄存器使用情况封装电路_1  (.OP(IR[31:26]), .Func(IR[5:0]), .R1_Used(R1_Used), .R2_Used(R2_Used));
  // Probe on IR[25:21]
  // Probe on IR[20:16]
  \修改的单周期硬布线控制器  \u_修改的单周期硬布线控制器_1  (
    .OP(IR[31:26]), .Func(IR[5:0]), .ALU_OP(\修改的单周期硬布线控制器_1_alu_op ), .MemToReg(\修改的单周期硬布线控制器_1_memtoreg ),
    .MemWrite(\修改的单周期硬布线控制器_1_memwrite ), .ALU_SRC(\修改的单周期硬布线控制器_1_alu_src ),
    .RegWrite(\修改的单周期硬布线控制器_1_regwrite ), .SysCALL(ID_SysCall), .SignedExt(SignedExt),
    .RegDst(\修改的单周期硬布线控制器_1_regdst ), .Beq(\修改的单周期硬布线控制器_1_beq ), .Bne(\修改的单周期硬布线控制器_1_bne ),
    .JR(\修改的单周期硬布线控制器_1_jr ), .JMP(\修改的单周期硬布线控制器_1_jmp ), .JAL(\修改的单周期硬布线控制器_1_jal ),
    .LUI(\修改的单周期硬布线控制器_1_lui ), .BLTZ(\修改的单周期硬布线控制器_1_bltz ), .LB(\修改的单周期硬布线控制器_1_lb ),
    .ERET(\修改的单周期硬布线控制器_1_eret ));
  Multiplexer #(.select(1), .width(5), .disabled("Z"), .enable("false")) multiplexer_7 (
    .in0(IR[20:16]), .in1(5'b00100), .out(R2_num), .sel(ID_SysCall));
  Multiplexer #(.select(1), .width(5), .disabled("Z"), .enable("false")) multiplexer_8 (
    .in0(IR[20:16]), .in1(IR[15:11]), .out(multiplexer_8_out), .sel(\修改的单周期硬布线控制器_1_regdst ));
  assign bit_extender_1_out = {{16{IR[15]}}, IR[15:0]};  // Bit_Extender bit_extender_1
  assign bit_extender_2_out = {{16{1'b0}}, IR[15:0]};  // Bit_Extender bit_extender_2
  Multiplexer #(.select(1), .width(5), .disabled("Z"), .enable("false")) multiplexer_9 (
    .in0(IR[25:21]), .in1({5{1'b1}}), .out(multiplexer_9_out), .sel(\修改的单周期硬布线控制器_1_jr ));
  Multiplexer #(.select(1), .width(32), .disabled("Z"), .enable("false")) multiplexer_10 (
    .in0(bit_extender_1_out), .in1(bit_extender_2_out), .out(multiplexer_10_out), .sel(SignedExt));
  Multiplexer #(.select(1), .width(5), .disabled("Z"), .enable("false")) multiplexer_11 (
    .in0(multiplexer_9_out), .in1(5'b00010), .out(R1_num), .sel(ID_SysCall));
  Multiplexer #(.select(1), .width(5), .disabled("Z"), .enable("false")) multiplexer_12 (
    .in0(mem_wb_1_w_2), .in1({5{1'b1}}), .out(multiplexer_12_out), .sel(WB_JAL));
  Multiplexer #(.select(1), .width(32), .disabled("Z"), .enable("false")) multiplexer_13 (
    .in0({32{1'b0}}), .in1(WB_R1), .out(v0), .sel(syscall));
  not not_1 (not_1_out, Pause);
  \MIPS_Regifile下降沿  \mips_regifile下降沿_1  (
    .Din(RDin), .Clk(CLK), .R1(\mips_regifile下降沿_1_r1 ), .R2(\mips_regifile下降沿_1_r2 ), .WE(RegWrite),
    .W_num(multiplexer_12_out), .R1_num(R1_num), .R2_num(R2_num));
  ID_EX id_ex_1 (
    .AluOP(\修改的单周期硬布线控制器_1_alu_op ), .AluSrcB(\修改的单周期硬布线控制器_1_alu_src ), .R1(\mips_regifile下降沿_1_r1 ),
    .R2(\mips_regifile下降沿_1_r2 ), .W(multiplexer_8_out), .Jaddr(if_id_1_jaddr_2), .AluOP_2(id_ex_1_aluop_2),
    .AluSrcB_2(id_ex_1_alusrcb_2), .R1_2(EX_R1), .R2_2(id_ex_1_r2_2), .W_2(EX_W_num), .Imm_2(id_ex_1_imm_2),
    .Jaddr_2(Jaddr), .PC_4_2(EX_PC_4), .Imm(multiplexer_10_out), .PC_4(if_id_1_pc_4_2), .RST(\ID_EX气泡 ),
    .EN(not_1_out), .CLK(CLK), .JR_2(JR), .JR(\修改的单周期硬布线控制器_1_jr ), .JMP(\修改的单周期硬布线控制器_1_jmp ), .JMP_2(JMP),
    .Bne(\修改的单周期硬布线控制器_1_bne ), .Bne_2(BNE), .Beq(\修改的单周期硬布线控制器_1_beq ), .Beq_2(BEQ),
    .BLTZ(\修改的单周期硬布线控制器_1_bltz ), .BLTZ_2(BLTZ), .LUI(\修改的单周期硬布线控制器_1_lui ), .LUI_2(LUI),
    .MenWrite(\修改的单周期硬布线控制器_1_memwrite ), .MenWrite_2(id_ex_1_menwrite_2),
    .MenToReg(\修改的单周期硬布线控制器_1_memtoreg ), .MenToReg_2(id_ex_1_mentoreg_2), .JAL(\修改的单周期硬布线控制器_1_jal ),
    .JAL_2(EX_JAL), .SysCall(ID_SysCall), .SysCall_2(id_ex_1_syscall_2), .LB(\修改的单周期硬布线控制器_1_lb ),
    .LB_2(id_ex_1_lb_2), .RegWrite(\修改的单周期硬布线控制器_1_regwrite ), .RegWrite_2(EX_RegWrite),
    .shamt_2(id_ex_1_shamt_2), .shamt(IR[10:6]), .PC(out_9), .PC_2(out_10), .ERET(\修改的单周期硬布线控制器_1_eret ),
    .ERET_2(id_ex_1_eret_2));
  Multiplexer #(.select(1), .width(32), .disabled("Z"), .enable("false")) multiplexer_14 (
    .in0({32{1'b0}}), .in1(WB_R2), .out(a0), .sel(syscall));
  Counter #(.width(16), .max('hffff), .ongoal("wrap"), .trigger("rising"), .behavior("old")) counter_1 (
    .count(not_1_out), .Q(\总周期数 ), .clk(CLK), .clr(1'b0));  // open: load, D, carry, preset
  // Probe on \总周期数 
  Multiplexer #(.select(1), .width(32), .disabled("Z"), .enable("false")) multiplexer_15 (
    .in0(id_ex_1_r2_2), .in1(id_ex_1_imm_2), .out(multiplexer_15_out), .sel(id_ex_1_alusrcb_2));
  Shifter #(.width(32), .shift("ll")) shifter_1 (.in(id_ex_1_imm_2), .\dist (5'b00010), .out(shifter_1_out));
  Comparator #(.width(32), .mode("unsigned")) comparator_6 (.a(v0), .b(32'ha), .eq(comparator_6_eq));  // open: gt, lt
  not not_2 (not_2_out, comparator_6_eq);
  Multiplexer #(.select(1), .width(5), .disabled("Z"), .enable("false")) multiplexer_16 (
    .in0(id_ex_1_shamt_2), .in1(5'b10000), .out(multiplexer_16_out), .sel(LUI));
  Adder #(.width(32)) adder_2 (.a(shifter_1_out), .b(EX_PC_4), .out(adder_2_out));  // open: cin, cout
  Multiplexer #(.select(1), .width(1), .disabled("Z"), .enable("false")) multiplexer_17 (
    .in0(1'b0), .in1(Go), .out(multiplexer_17_out), .sel(comparator_6_eq));
  MIPS_ALU mips_alu_1 (
    .X(EX_R1), .Y(multiplexer_15_out), .AluOP(id_ex_1_aluop_2), .Equal(tunnel), .Result(BLTZ_result),
    .shamt(multiplexer_16_out));  // open: Result_2
  // Probe on BLTZ_result
  xor xor_1 (Pause, comparator_6_eq, multiplexer_17_out);
  EX_MEM ex_mem_1 (
    .LB(id_ex_1_lb_2), .SysCall(id_ex_1_syscall_2), .RegWrite(EX_RegWrite), .MenToReg(id_ex_1_mentoreg_2),
    .R(BLTZ_result), .R2(id_ex_1_r2_2), .W(EX_W_num), .LB_2(ex_mem_1_lb_2), .SysCall_2(ex_mem_1_syscall_2),
    .RegWrite_2(MEM_RegWrite), .MenToReg_2(ex_mem_1_mentoreg_2), .R_2(ex_mem_1_r_2), .R2_2(MDin),
    .W_2(MEM_W_num), .RST(ERET), .EN(not_1_out), .CLK(CLK), .MenWrite(id_ex_1_menwrite_2),
    .MenWrite_2(MemWrite), .JAL_2(ex_mem_1_jal_2), .JAL(EX_JAL), .PC_4(EX_PC_4), .PC_4_2(ex_mem_1_pc_4_2),
    .R2_3(ex_mem_1_r2_3), .R1(EX_R1), .R1_2(ex_mem_1_r1_2), .PC(out_10), .PC_2(out_11),
    .ERET(id_ex_1_eret_2), .ERET_2(ex_mem_1_eret_2));
  and and_6 (and_6_out, syscall, not_2_out);
  Multiplexer #(.select(1), .width(32), .disabled("Z"), .enable("false")) multiplexer_18 (
    .in0(out_13), .in1(a0), .out(multiplexer_18_out), .sel(and_6_out));
  // Probe on ex_mem_1_r_2
  Register #(.width(32), .trigger("rising"), .Select("low")) register_1 (
    .D(multiplexer_18_out), .Q(out_13), .clk(CLK));  // open: en, clr
  and and_7 (and_7_out, MemWrite, not_3_out);
  RAM #(.addrWidth(10), .dataWidth(32), .bus("separate"), .Select("high")) ram_1 (
    .addr({2'b00, ex_mem_1_r_2[9:2]}), .din(MDin), .data(ram_1_data), .str(and_7_out), .clk(CLK),
    .ld(not_3_out), .clr(1'b0));  // open: sel
  not not_3 (not_3_out, syscall);
  or or_6 (IR1_t, IR1, IRA);
  MEM_WB mem_wb_1 (
    .LB(ex_mem_1_lb_2), .SysCall(ex_mem_1_syscall_2), .RegWrite(MEM_RegWrite),
    .MenToReg(ex_mem_1_mentoreg_2), .ALU_Data(ex_mem_1_r_2), .MEM_ReadData(ram_1_data), .W(MEM_W_num),
    .LB_2(LB), .SysCall_2(syscall), .RegWrite_2(RegWrite), .MenToReg_2(mem_wb_1_mentoreg_2),
    .ALU_Data_2(mem_wb_1_alu_data_2), .MEM_ReadData_2(mem_wb_1_mem_readdata_2), .W_2(mem_wb_1_w_2),
    .RST(1'b0), .EN(not_1_out), .CLK(CLK), .JAL(ex_mem_1_jal_2), .JAL_2(WB_JAL), .PC_4(ex_mem_1_pc_4_2),
    .PC_4_2(WB_PC_4), .\LB低两位 (ex_mem_1_r_2[1:0]), .\LB低两位_2 (\mem_wb_1_lb低两位_2 ), .R1(ex_mem_1_r1_2),
    .R1_2(WB_R1), .R2(ex_mem_1_r2_3), .R2_2(WB_R2), .PC(out_11), .PC_2(out_12), .ERET(ex_mem_1_eret_2),
    .ERET_2(ERET));
  or or_7 (IR2_t, IR2, IRB);
  Multiplexer #(.select(1), .width(32), .disabled("Z"), .enable("false")) multiplexer_19 (
    .in0(mem_wb_1_alu_data_2), .in1(mem_wb_1_mem_readdata_2), .out(multiplexer_19_out),
    .sel(mem_wb_1_mentoreg_2));
  Counter #(.width(16), .max('hffff), .ongoal("wrap"), .trigger("rising"), .behavior("old")) counter_2 (
    .count(\ID_EX气泡 ), .Q(counter_2_q), .clk(CLK), .clr(1'b0));  // open: load, D, carry, preset
  Counter #(.width(16), .max('hffff), .ongoal("wrap"), .trigger("rising"), .behavior("old")) counter_3 (
    .count(\插入气泡 ), .Q(counter_3_q), .clk(CLK), .clr(1'b0));  // open: load, D, carry, preset
  \写入寄存器数据判断处理器  \u_写入寄存器数据判断处理器_1  (
    .in_3(multiplexer_19_out), .WB_PC_4(WB_PC_4), .out_6(RDin), .LB(LB), .WB_JAL(WB_JAL),
    .\LB低两位 (\mem_wb_1_lb低两位_2 ));
  or or_8 (IR3_t, IR3, IRC);
  \数据相关检测  \u_数据相关检测_1  (
    .Pause(Pause), .\转跳插入气泡 (\气泡_中断 ), .\ID_EX气泡 (\ID_EX气泡 ), .PC_IF_ID_EN(\PC_IF_ID使能 ),
    .MEM_RegWrite(MEM_RegWrite), .EX_RegWrite(EX_RegWrite), .EX_W_num(EX_W_num), .MEM_W_num(MEM_W_num),
    .R2_Used(R2_Used), .R2_num(R2_num), .R1_Used(R1_Used), .R1_num(R1_num));
  Subtractor #(.width(16)) subtractor_1 (.a(counter_2_q), .b(counter_3_q), .out(\插入气泡数 ));  // open: bin, bout

  // Other names for the same wires on the sheet: IF_PC[31:0] = out_8; PC[31:0] = out_8; EX_PC[31:0] = out_10;
  //   ID_PC[31:0] = out_9; JRaddr[31:0] = EX_R1; LedData[31:0] = out_13; MEM_PC[31:0] = out_11; WB_PC[31:0] = out_12

  // Notes on the sheet:
  //   中断源
  //   中断等待指示
  //   单级中断测试信号
  //   数码管输出
  //   IF
  //   指令存储器
  //   contents of rom_1 (hex, n*v repeats v):
  //   201d07d0 20100001 109fc0 139fc3 8021 2012000c 24160008 26100001 3210000f 20080008 20090001 139900
  //   2709825 132020 20020022 c 1094022 1500fff9 22100001 2018000f 2188024 108700 20080008 20090001 139902
  //   2709825 132021 20020022 c 1094022 1500fff9 108702 2c9b022 12c00001 8000c07 4020 1084027 84400
  //   3508ffff 82021 20020022 c 8000c01 afa20000 23bd0004 afa40000 23bd0004 afb00000 23bd0004 afb30000
  //   23bd0004 afb40000 23bd0004 afb50000 23bd0004 afb60000 23bd0004 20160001 20140003 20150001 168020
  //   108100 2149825 132020 20020022 c 1600fffa 295a022 1680fff7 23bdfffc 8fb60000 23bdfffc 8fb50000
  //   23bdfffc 8fb40000 23bdfffc 8fb30000 23bdfffc 8fb00000 23bdfffc 8fa40000 23bdfffc 8fa20000 42000018
  //   afa20000 23bd0004 afa40000 23bd0004 afb00000 23bd0004 afb30000 23bd0004 afb40000 23bd0004 afb50000
  //   23bd0004 afb60000 23bd0004 20160002 20140003 20150001 168020 108100 2149825 132020 20020022 c
  //   1600fffa 295a022 1680fff7 23bdfffc 8fb60000 23bdfffc 8fb50000 23bdfffc 8fb40000 23bdfffc 8fb30000
  //   23bdfffc 8fb00000 23bdfffc 8fa40000 23bdfffc 8fa20000 42000018 afa20000 23bd0004 afa40000 23bd0004
  //   afb00000 23bd0004 afb30000 23bd0004 afb40000 23bd0004 afb50000 23bd0004 afb60000 23bd0004 20160003
  //   20140003 20150001 168020 108100 2149825 132020 20020022 c 1600fffa 295a022 1680fff7 23bdfffc
  //   8fb60000 23bdfffc 8fb50000 23bdfffc 8fb40000 23bdfffc 8fb30000 23bdfffc 8fb00000 23bdfffc 8fa40000
  //   23bdfffc 8fa20000 42000018
  //   为方便自动评测，需要输出PC，IR，寄存器文件写入端口RDin，内存写入端口MDin等信号
  //   IR
  //   OP
  //   Func
  //   RegDst
  //   rs
  //   rt
  //   rd
  //   shamt
  //   imm
  //   ID
  //   SignedExt
  //   RegDst
  //   $v0
  //   $a0
  //   数码管输出应该用寄存器锁存，否则显示数据只能一闪而过
  //   总复位信号应将除ROM以外所有存储组件全部清零
  //   LUI
  //   BLTZ
  //   Bne
  //   EX
  //   Beq
  //   JAL
  //   AluOP
  //   JMP
  //   JR
  //   AluSrcB
  //   MEM
  //   MemWrite
  //   LB
  //   WB
  //   RegWrite
  //   Syscall
  //   MemToReg
endmodule

module \重定向流水线  (
  output RegWrite,
  output MemWrite,
  output [31:0] RDin,
  output [31:0] out_4,
  output [31:0] out_5,
  output [31:0] out_6,
  output [31:0] out_7,
  output [31:0] out_8,
  output [31:0] MDin,
  output [31:0] out_10
);

  wire and_1_out, and_2_out, BEQ, BLTZ, BNE, CLK, comparator_1_eq, comparator_2_eq, EX_JAL, ex_mem_1_jal_2,
       ex_mem_1_lb_2, ex_mem_1_syscall_2, EX_MenToReg, EX_RegWrite, Go, id_ex_1_alusrcb_2, id_ex_1_lb_2,
       id_ex_1_menwrite_2, id_ex_1_syscall_2, \ID_EX气泡 , ID_SysCall, IR1, IR2, IR3, JMP, JR, LB, LUI,
       MEM_MenToReg, MEM_RegWrite, mem_wb_1_mentoreg_2, multiplexer_1_out, multiplexer_14_out, not_1_out,
       not_2_out, not_3_out, Pause, \PC_IF_ID使能 , R1_Used, R2_Used, SignedExt, syscall, tunnel, W1, W2, W3,
       WB_JAL, \修改的单周期硬布线控制器_1_alu_src , \修改的单周期硬布线控制器_1_beq , \修改的单周期硬布线控制器_1_bltz , \修改的单周期硬布线控制器_1_bne ,
       \修改的单周期硬布线控制器_1_jal , \修改的单周期硬布线控制器_1_jmp , \修改的单周期硬布线控制器_1_jr , \修改的单周期硬布线控制器_1_lb ,
       \修改的单周期硬布线控制器_1_lui , \修改的单周期硬布线控制器_1_memtoreg , \修改的单周期硬布线控制器_1_memwrite , \修改的单周期硬布线控制器_1_regdst ,
       \修改的单周期硬布线控制器_1_regwrite , \插入气泡 ;
  wire [1:0] Forward1, Forward2, \mem_wb_1_lb低两位_2 , \重定向数据相关检测_1_forward1 , \重定向数据相关检测_1_forward2 ;
  wire [3:0] id_ex_1_aluop_2, \修改的单周期硬布线控制器_1_alu_op ;
  wire [4:0] EX_W_num, id_ex_1_shamt_2, MEM_W_num, mem_wb_1_w_2, multiplexer_2_out, multiplexer_3_out,
       multiplexer_7_out, multiplexer_11_out, R1_num, R2_num;
  wire [15:0] counter_2_q, counter_3_q, \LoadUse次数 , \总周期数 , \插入气泡数 , \无条件分支数 , \条件分支成功数 ;
  wire [31:0] a0, adder_2_out, bit_extender_1_out, bit_extender_2_out, BLTZ_result, ex_mem_1_pc_4_2,
       ex_mem_1_r1_2, ex_mem_1_r2_3, EX_R1, id_ex_1_imm_2, id_ex_1_pc_4_2, id_ex_1_r1_2, id_ex_1_r2_2,
       if_id_1_jaddr_2, if_id_1_pc_4_2, IR, Jaddr, \j型指令转跳地址判断器_1_out_12 , MEM_ALUResult,
       mem_wb_1_alu_data_2, mem_wb_1_mem_readdata_2, mem_wb_1_pc_4_2, \mips_regifile下降沿_1_r1 ,
       \mips_regifile下降沿_1_r2 , multiplexer_5_out, multiplexer_8_out, multiplexer_10_out, multiplexer_15_out,
       PC_4, ram_1_data, rom_1_data, shifter_1_out, v0, WB_ALUResult, WB_R1, WB_R2, WB_ReadData;

  Clock #(.highDuration(1), .lowDuration(1)) clock_1 (.out(CLK));
  Button _1 (.out(IR1));
  Button _2 (.out(IR2));
  Button _3 (.out(IR3));
  // Probe on \j型指令转跳地址判断器_1_out_12 
  Button \u_继续运行  (.out(Go));
  LED #(.active("true")) led_1 (.in(W1));
  LED #(.active("true")) led_2 (.in(W2));
  LED #(.active("true")) led_3 (.in(W3));
  Register #(.width(32), .trigger("rising"), .Select("low")) PC (
    .D(\j型指令转跳地址判断器_1_out_12 ), .en(\PC_IF_ID使能 ), .Q(out_4), .clk(CLK), .clr(1'b0));
  \J型指令转跳地址判断器  \j型指令转跳地址判断器_1  (
    .JR(JR), .JMP(JMP), .BNE(BNE), .in_2(tunnel), .BEQ(BEQ), .JAL(EX_JAL), .BLTZ(multiplexer_1_out),
    .out_12(\j型指令转跳地址判断器_1_out_12 ), .PC_4(PC_4), .BNE_BEQ_BLTZaddr(adder_2_out), .J_JALaddr(Jaddr),
    .JRaddr(EX_R1), .\转跳信号灯 (\插入气泡 ));
  Hex_Digit_Display hex_digit_display_1 (.value(out_10[31:28]));  // open: dp
  // Probe on \总周期数 
  // Probe on \无条件分支数 
  // Probe on \条件分支成功数 
  // Probe on \插入气泡数 
  // Probe on \LoadUse次数 
  // Probe on out_4[11:0]
  // Probe on out_5[11:0]
  // Probe on out_6[11:0]
  // Probe on out_7[11:0]
  // Probe on out_8[11:0]
  Adder #(.width(32)) adder_1 (.a(out_4), .b(32'h4), .out(PC_4));  // open: cin, cout
  Multiplexer #(.select(1), .width(1), .disabled("Z"), .enable("false")) multiplexer_1 (
    .in0(1'b0), .in1(BLTZ), .out(multiplexer_1_out), .sel(comparator_1_eq));
  Comparator #(.width(32), .mode("unsigned")) comparator_1 (
    .a(BLTZ_result), .b(32'h1), .eq(comparator_1_eq));  // open: gt, lt
  Hex_Digit_Display hex_digit_display_2 (.value(out_10[27:24]));  // open: dp
  Hex_Digit_Display hex_digit_display_3 (.value(out_10[23:20]));  // open: dp
  Hex_Digit_Display hex_digit_display_4 (.value(out_10[19:16]));  // open: dp
  Hex_Digit_Display hex_digit_display_5 (.value(out_10[15:12]));  // open: dp
  ROM #(.addrWidth(10), .dataWidth(32), .Select("high")) rom_1 (.addr(out_4[11:2]), .data(rom_1_data));
  Hex_Digit_Display hex_digit_display_6 (.value(out_10[11:8]));  // open: dp
  Hex_Digit_Display hex_digit_display_7 (.value(out_10[7:4]));  // open: dp
  // Probe on \总周期数 
  IF_ID if_id_1 (
    .IR(rom_1_data), .Jaddr({out_4[31:28], rom_1_data[25:0], 2'b00}), .PC_4(PC_4), .IR_2(IR),
    .Jaddr_2(if_id_1_jaddr_2), .PC_4_2(if_id_1_pc_4_2), .Reset(\插入气泡 ), .EN(\PC_IF_ID使能 ), .CLK(CLK),
    .PC(out_4), .PC_2(out_5));
  Hex_Digit_Display hex_digit_display_8 (.value(out_10[3:0]));  // open: dp
  \修改的单周期硬布线控制器  \u_修改的单周期硬布线控制器_1  (
    .OP(IR[31:26]), .Func(IR[5:0]), .ALU_OP(\修改的单周期硬布线控制器_1_alu_op ), .MemToReg(\修改的单周期硬布线控制器_1_memtoreg ),
    .MemWrite(\修改的单周期硬布线控制器_1_memwrite ), .ALU_SRC(\修改的单周期硬布线控制器_1_alu_src ),
    .RegWrite(\修改的单周期硬布线控制器_1_regwrite ), .SysCALL(ID_SysCall), .SignedExt(SignedExt),
    .RegDst(\修改的单周期硬布线控制器_1_regdst ), .Beq(\修改的单周期硬布线控制器_1_beq ), .Bne(\修改的单周期硬布线控制器_1_bne ),
    .JR(\修改的单周期硬布线控制器_1_jr ), .JMP(\修改的单周期硬布线控制器_1_jmp ), .JAL(\修改的单周期硬布线控制器_1_jal ),
    .LUI(\修改的单周期硬布线控制器_1_lui ), .BLTZ(\修改的单周期硬布线控制器_1_bltz ), .LB(\修改的单周期硬布线控制器_1_lb ));  // open: ERET
  \源寄存器使用情况封装电路  \u_源寄存器使用情况封装电路_1  (.OP(IR[31:26]), .Func(IR[5:0]), .R1_Used(R1_Used), .R2_Used(R2_Used));
  // Probe on IR[25:21]
  // Probe on IR[20:16]
  Multiplexer #(.select(1), .width(5), .disabled("Z"), .enable("false")) multiplexer_2 (
    .in0(IR[20:16]), .in1(IR[15:11]), .out(multiplexer_2_out), .sel(\修改的单周期硬布线控制器_1_regdst ));
  assign bit_extender_1_out = {{16{IR[15]}}, IR[15:0]};  // Bit_Extender bit_extender_1
  assign bit_extender_2_out = {{16{1'b0}}, IR[15:0]};  // Bit_Extender bit_extender_2
  Multiplexer #(.select(1), .width(5), .disabled("Z"), .enable("false")) multiplexer_3 (
    .in0(IR[25:21]), .in1({5{1'b1}}), .out(multiplexer_3_out), .sel(\修改的单周期硬布线控制器_1_jr ));
  Multiplexer #(.select(1), .width(5), .disabled("Z"), .enable("false")) multiplexer_4 (
    .in0(IR[20:16]), .in1(5'b00100), .out(R2_num), .sel(ID_SysCall));
  Multiplexer #(.select(1), .width(32), .disabled("Z"), .enable("false")) multiplexer_5 (
    .in0(bit_extender_1_out), .in1(bit_extender_2_out), .out(multiplexer_5_out), .sel(SignedExt));
  Multiplexer #(.select(1), .width(5), .disabled("Z"), .enable("false")) multiplexer_6 (
    .in0(multiplexer_3_out), .in1(5'b00010), .out(R1_num), .sel(ID_SysCall));
  Multiplexer #(.select(1), .width(5), .disabled("Z"), .enable("false")) multiplexer_7 (
    .in0(mem_wb_1_w_2), .in1({5{1'b1}}), .out(multiplexer_7_out), .sel(WB_JAL));
  not not_1 (not_1_out, Pause);
  \MIPS_Regifile下降沿  \mips_regifile下降沿_1  (
    .Din(RDin), .Clk(CLK), .R1(\mips_regifile下降沿_1_r1 ), .R2(\mips_regifile下降沿_1_r2 ), .WE(RegWrite),
    .W_num(multiplexer_7_out), .R1_num(R1_num), .R2_num(R2_num));
  ID_EX id_ex_1 (
    .AluOP(\修改的单周期硬布线控制器_1_alu_op ), .AluSrcB(\修改的单周期硬布线控制器_1_alu_src ), .R1(\mips_regifile下降沿_1_r1 ),
    .R2(\mips_regifile下降沿_1_r2 ), .W(multiplexer_2_out), .Jaddr(if_id_1_jaddr_2), .AluOP_2(id_ex_1_aluop_2),
    .AluSrcB_2(id_ex_1_alusrcb_2), .R1_2(id_ex_1_r1_2), .R2_2(id_ex_1_r2_2), .W_2(EX_W_num),
    .Imm_2(id_ex_1_imm_2), .Jaddr_2(Jaddr), .PC_4_2(id_ex_1_pc_4_2), .Imm(multiplexer_5_out),
    .PC_4(if_id_1_pc_4_2), .RST(\ID_EX气泡 ), .EN(not_1_out), .CLK(CLK), .JR_2(JR), .JR(\修改的单周期硬布线控制器_1_jr ),
    .JMP(\修改的单周期硬布线控制器_1_jmp ), .JMP_2(JMP), .Bne(\修改的单周期硬布线控制器_1_bne ), .Bne_2(BNE),
    .Beq(\修改的单周期硬布线控制器_1_beq ), .Beq_2(BEQ), .BLTZ(\修改的单周期硬布线控制器_1_bltz ), .BLTZ_2(BLTZ),
    .LUI(\修改的单周期硬布线控制器_1_lui ), .LUI_2(LUI), .MenWrite(\修改的单周期硬布线控制器_1_memwrite ),
    .MenWrite_2(id_ex_1_menwrite_2), .MenToReg(\修改的单周期硬布线控制器_1_memtoreg ), .MenToReg_2(EX_MenToReg),
    .JAL(\修改的单周期硬布线控制器_1_jal ), .JAL_2(EX_JAL), .SysCall(ID_SysCall), .SysCall_2(id_ex_1_syscall_2),
    .LB(\修改的单周期硬布线控制器_1_lb ), .LB_2(id_ex_1_lb_2), .RegWrite(\修改的单周期硬布线控制器_1_regwrite ),
    .RegWrite_2(EX_RegWrite), .shamt_2(id_ex_1_shamt_2), .shamt(IR[10:6]), .PC(out_5), .PC_2(out_6));  // open: ERET, ERET_2
  // Probe on RDin
  Counter #(.width(16), .max('hffff), .ongoal("wrap"), .trigger("rising"), .behavior("old")) counter_1 (
    .count(not_1_out), .Q(\总周期数 ), .clk(CLK), .clr(1'b0));  // open: load, D, carry, preset
  // Probe on \总周期数 
  Multiplexer #(.select(2), .width(32), .disabled("Z"), .enable("false")) multiplexer_8 (
    .in0(id_ex_1_r2_2), .in1(WB_ReadData), .in2(WB_ALUResult), .in3(MEM_ALUResult), .out(multiplexer_8_out),
    .sel(Forward2));
  Shifter #(.width(32), .shift("ll")) shifter_1 (.in(id_ex_1_imm_2), .\dist (5'b00010), .out(shifter_1_out));
  Multiplexer #(.select(2), .width(32), .disabled("Z"), .enable("false")) multiplexer_9 (
    .in0(id_ex_1_r1_2), .in1(WB_ReadData), .in2(WB_ALUResult), .in3(MEM_ALUResult), .out(EX_R1),
    .sel(Forward1));
  Multiplexer #(.select(1), .width(32), .disabled("Z"), .enable("false")) multiplexer_10 (
    .in0(multiplexer_8_out), .in1(id_ex_1_imm_2), .out(multiplexer_10_out), .sel(id_ex_1_alusrcb_2));
  Multiplexer #(.select(1), .width(5), .disabled("Z"), .enable("false")) multiplexer_11 (
    .in0(id_ex_1_shamt_2), .in1(5'b10000), .out(multiplexer_11_out), .sel(LUI));
  Adder #(.width(32)) adder_2 (.a(shifter_1_out), .b(id_ex_1_pc_4_2), .out(adder_2_out));  // open: cin, cout
  MIPS_ALU mips_alu_1 (
    .X(EX_R1), .Y(multiplexer_10_out), .AluOP(id_ex_1_aluop_2), .Equal(tunnel), .Result(BLTZ_result),
    .shamt(multiplexer_11_out));  // open: Result_2
  // Probe on BLTZ_result
  Multiplexer #(.select(1), .width(32), .disabled("Z"), .enable("false")) multiplexer_12 (
    .in0({32{1'b0}}), .in1(WB_R1), .out(v0), .sel(syscall));
  EX_MEM ex_mem_1 (
    .LB(id_ex_1_lb_2), .SysCall(id_ex_1_syscall_2), .RegWrite(EX_RegWrite), .MenToReg(EX_MenToReg),
    .R(BLTZ_result), .R2(multiplexer_8_out), .W(EX_W_num), .LB_2(ex_mem_1_lb_2),
    .SysCall_2(ex_mem_1_syscall_2), .RegWrite_2(MEM_RegWrite), .MenToReg_2(MEM_MenToReg),
    .R_2(MEM_ALUResult), .R2_2(MDin), .W_2(MEM_W_num), .RST(1'b0), .EN(not_1_out), .CLK(CLK),
    .MenWrite(id_ex_1_menwrite_2), .MenWrite_2(MemWrite), .JAL_2(ex_mem_1_jal_2), .JAL(EX_JAL),
    .PC_4(id_ex_1_pc_4_2), .PC_4_2(ex_mem_1_pc_4_2), .R2_3(ex_mem_1_r2_3), .R1(EX_R1), .R1_2(ex_mem_1_r1_2),
    .PC(out_6), .PC_2(out_7));  // open: ERET, ERET_2
  // Probe on MEM_ALUResult
  Multiplexer #(.select(1), .width(32), .disabled("Z"), .enable("false")) multiplexer_13 (
    .in0({32{1'b0}}), .in1(WB_R2), .out(a0), .sel(syscall));
  and and_1 (and_1_out, MemWrite, not_2_out);
  not not_2 (not_2_out, syscall);
  Comparator #(.width(32), .mode("unsigned")) comparator_2 (.a(v0), .b(32'ha), .eq(comparator_2_eq));  // open: gt, lt
  not not_3 (not_3_out, comparator_2_eq);
  MEM_WB mem_wb_1 (
    .LB(ex_mem_1_lb_2), .SysCall(ex_mem_1_syscall_2), .RegWrite(MEM_RegWrite), .MenToReg(MEM_MenToReg),
    .ALU_Data(MEM_ALUResult), .MEM_ReadData(ram_1_data), .W(MEM_W_num), .LB_2(LB), .SysCall_2(syscall),
    .RegWrite_2(RegWrite), .MenToReg_2(mem_wb_1_mentoreg_2), .ALU_Data_2(mem_wb_1_alu_data_2),
    .MEM_ReadData_2(mem_wb_1_mem_readdata_2), .W_2(mem_wb_1_w_2), .RST(1'b0), .EN(not_1_out), .CLK(CLK),
    .JAL(ex_mem_1_jal_2), .JAL_2(WB_JAL), .PC_4(ex_mem_1_pc_4_2), .PC_4_2(mem_wb_1_pc_4_2),
    .\LB低两位 (MEM_ALUResult[1:0]), .\LB低两位_2 (\mem_wb_1_lb低两位_2 ), .R1(ex_mem_1_r1_2), .R1_2(WB_R1),
    .R2(ex_mem_1_r2_3), .R2_2(WB_R2), .PC(out_7), .PC_2(out_8));  // open: ERET, ERET_2
  RAM #(.addrWidth(10), .dataWidth(32), .bus("separate"), .Select("high")) ram_1 (
    .addr({2'b00, MEM_ALUResult[9:2]}), .din(MDin), .data(ram_1_data), .str(and_1_out), .clk(CLK),
    .ld(not_2_out), .clr(1'b0));  // open: sel
  Multiplexer #(.select(1), .width(1), .disabled("Z"), .enable("false")) multiplexer_14 (
    .in0(1'b0), .in1(Go), .out(multiplexer_14_out), .sel(comparator_2_eq));
  xor xor_1 (Pause, comparator_2_eq, multiplexer_14_out);
  \写入寄存器数据判断处理器  \u_写入寄存器数据判断处理器_1  (
    .in_3(mem_wb_1_alu_data_2), .WB_PC_4(mem_wb_1_pc_4_2), .out_6(WB_ALUResult), .LB(LB), .WB_JAL(WB_JAL),
    .\LB低两位 (\mem_wb_1_lb低两位_2 ));
  \写入寄存器数据判断处理器  \u_写入寄存器数据判断处理器_2  (
    .in_3(mem_wb_1_mem_readdata_2), .WB_PC_4(mem_wb_1_pc_4_2), .out_6(WB_ReadData), .LB(LB), .WB_JAL(WB_JAL),
    .\LB低两位 (\mem_wb_1_lb低两位_2 ));
  and and_2 (and_2_out, syscall, not_3_out);
  Multiplexer #(.select(1), .width(32), .disabled("Z"), .enable("false")) multiplexer_15 (
    .in0(out_10), .in1(a0), .out(multiplexer_15_out), .sel(and_2_out));
  // Probe on counter_2_q
  Counter #(.width(16), .max('hffff), .ongoal("wrap"), .trigger("rising"), .behavior("old")) counter_2 (
    .count(\ID_EX气泡 ), .Q(counter_2_q), .clk(CLK), .clr(1'b0));  // open: load, D, carry, preset
  Counter #(.width(16), .max('hffff), .ongoal("wrap"), .trigger("rising"), .behavior("old")) counter_3 (
    .count(\插入气泡 ), .Q(counter_3_q), .clk(CLK), .clr(1'b0));  // open: load, D, carry, preset
  Register #(.width(32), .trigger("rising"), .Select("low")) register_1 (
    .D(multiplexer_15_out), .Q(out_10), .clk(CLK));  // open: en, clr
  Subtractor #(.width(16)) subtractor_1 (.a(counter_2_q), .b(counter_3_q), .out(\插入气泡数 ));  // open: bin, bout
  Multiplexer #(.select(1), .width(32), .disabled("Z"), .enable("false")) multiplexer_16 (
    .in0(WB_ALUResult), .in1(WB_ReadData), .out(RDin), .sel(mem_wb_1_mentoreg_2));
  \重定向数据相关检测  \u_重定向数据相关检测_1  (
    .EX_MemToReg(EX_MenToReg), .EX_RegWrite(EX_RegWrite), .MEM_MemToReg(MEM_MenToReg),
    .MEM_RegWrite(MEM_RegWrite), .MEM_W_num(MEM_W_num), .Pause(Pause), .EX_W_num(EX_W_num),
    .\转跳插入气泡 (\插入气泡 ), .ID_R1_num(R1_num), .ID_R2_num(R2_num), .R1_Used(R1_Used), .R2_Used(R2_Used),
    .Forward1(\重定向数据相关检测_1_forward1 ), .Forward2(\重定向数据相关检测_1_forward2 ), .\ID_EX气泡 (\ID_EX气泡 ),
    .PC_IF_ID_EN(\PC_IF_ID使能 ));
  Register #(.width(2), .trigger("rising"), .Select("low")) register_2 (
    .D(\重定向数据相关检测_1_forward1 ), .Q(Forward1), .clk(CLK));  // open: en, clr
  Register #(.width(2), .trigger("rising"), .Select("low")) register_3 (
    .D(\重定向数据相关检测_1_forward2 ), .Q(Forward2), .clk(CLK));  // open: en, clr
  // Probe on Forward1
  // Probe on Forward2

  // Other names for the same wires on the sheet: IF_PC[31:0] = out_4; PC[31:0] = out_4; EX_PC[31:0] = out_6;
  //   ID_PC[31:0] = out_5; JRaddr[31:0] = EX_R1; LedData[31:0] = out_10; MEM_PC[31:0] = out_7; WB_PC[31:0] = out_8

  // Notes on the sheet:
  //   中断源
  //   中断等待指示
  //   IF
  //   指令存储器
  //   数码管输出
  //   contents of rom_1 (hex, n*v repeats v):
  //   20110001 8000c05 20110001 20120002 20130003 8000c09 20110001 20120002 20130003 8000c0d 20110001
  //   20120002 20130003 8000c11 20110001 20120002 20130003 c000cf0 20100001 20110001 118fc0 112020
  //   20020022 c 118882 12200001 8000c15 112020 20020022 c 20110001 118880 112020 20020022 c 12200001
  //   8000c1f 20110001 118fc0 112020 20020022 c 1188c3 112020 20020022 c 118903 112020 20020022 c 118903
  //   112020 20020022 c 118903 112020 20020022 c 118903 112020 20020022 c 118903 112020 20020022 c 118903
  //   112020 20020022 c 118903 112020 20020022 c 20100001 109fc0 139fc3 8021 2012000c 24160003 26100001
  //   3210000f 20080008 20090001 139900 2709825 132020 20020022 c 1094022 1500fff9 22100001 2018000f
  //   2188024 108700 20080008 20090001 139902 2709825 132021 20020022 c 1094022 1500fff9 108702 2c9b022
  //   12c00001 8000c50 4020 1084027 84400 3508ffff 82021 20020022 c 2010ffff 20110000 ae300000 22100001
  //   22310004 ae300000 22100001 22310004 ae300000 22100001 22310004 ae300000 22100001 22310004 ae300000
  //   22100001 22310004 ae300000 22100001 22310004 ae300000 22100001 22310004 ae300000 22100001 22310004
  //   ae300000 22100001 22310004 ae300000 22100001 22310004 ae300000 22100001 22310004 ae300000 22100001
  //   22310004 ae300000 22100001 22310004 ae300000 22100001 22310004 ae300000 22100001 22310004 ae300000
  //   22100001 22310004 22100001 8020 2011003c 8e130000 8e340000 274402a 11000002 ae330000 ae140000
  //   2231fffc 1611fff8 102020 20020022 c 22100004 2011003c 1611fff2 20020032 c 200b0008 3c11fedc 3631ffff
  //   112020 20020022 c 3c11ba98 112020 c 3c117654 112020 c 3c113210 112020 c 216bffff 1560fff0 2008ffff
  //   20090000 20111997 112020 20020022 c 2288820 2e291949 1120fffa 20090000 200b0010 34118483 20120404
  //   118c00 129400 36318281 22520404 ad310000 2328820 21290004 216bffff 1560fffb 200b0020 20090000
  //   81310000 112020 20020022 c 21290001 216bffff 1560fff9 2011fff1 112020 20020022 c 22310001 620fffb
  //   2002000a c 20100000 22100001 102020 20020022 c 22100002 102020 20020022 c 22100003 102020 20020022 c
  //   22100004 102020 20020022 c 22100005 102020 20020022 c 22100006 102020 20020022 c 22100007 102020
  //   20020022 c 22100008 102020 20020022 20020022 c 3e00008
  //   IR
  //   OP
  //   Func
  //   rs
  //   rt
  //   rd
  //   shamt
  //   imm
  //   RegDst
  //   SignedExt
  //   $a0
  //   ID
  //   RegDst
  //   $v0
  //   为方便自动评测，需要输出PC，IR，寄存器文件写入端口RDin，内存写入端口MDin等信号
  //   LUI
  //   Bne
  //   Beq
  //   BLTZ
  //   EX
  //   JMP
  //   JAL
  //   JR
  //   AluSrcB
  //   AluOP
  //   数码管输出应该用寄存器锁存，否则显示数据只能一闪而过
  //   总复位信号应将除ROM以外所有存储组件全部清零
  //   MEM
  //   MemWrite
  //   LB
  //   Syscall
  //   WB
  //   RegWrite
  //   MemToReg
endmodule

module \动态分支预测  (
  output RegWrite,
  output MemWrite,
  output [31:0] out_3,
  output [31:0] out_4,
  output [31:0] out_5,
  output [31:0] out_6,
  output [31:0] out_7,
  output [31:0] RDin,
  output [31:0] MDin,
  output [31:0] out_10
);

  wire and_1_out, and_2_out, BEQ, BLTZ, BNE, CLK, comparator_1_eq, comparator_2_eq, EX_JAL, ex_mem_1_jal_2,
       ex_mem_1_lb_2, ex_mem_1_syscall_2, EX_MenToReg, EX_RegWrite, Go, id_ex_1_alusrcb_2, id_ex_1_lb_2,
       id_ex_1_menwrite_2, id_ex_1_syscall_2, \ID_EX气泡 , ID_SysCall, IR1, IR2, IR3, JMP, JR, LB, LUI,
       MEM_MenToReg, MEM_RegWrite, mem_wb_1_mentoreg_2, multiplexer_1_out, multiplexer_14_out, not_1_out,
       not_2_out, not_3_out, Pause, \PC_IF_ID使能 , R1_Used, R2_Used, SignedExt, syscall, tunnel, W1, W2, W3,
       WB_JAL, \修改的单周期硬布线控制器_1_alu_src , \修改的单周期硬布线控制器_1_beq , \修改的单周期硬布线控制器_1_bltz , \修改的单周期硬布线控制器_1_bne ,
       \修改的单周期硬布线控制器_1_jal , \修改的单周期硬布线控制器_1_jmp , \修改的单周期硬布线控制器_1_jr , \修改的单周期硬布线控制器_1_lb ,
       \修改的单周期硬布线控制器_1_lui , \修改的单周期硬布线控制器_1_memtoreg , \修改的单周期硬布线控制器_1_memwrite , \修改的单周期硬布线控制器_1_regdst ,
       \修改的单周期硬布线控制器_1_regwrite , \插入气泡 ;
  wire [1:0] Forward1, Forward2, \mem_wb_1_lb低两位_2 , \重定向数据相关检测_1_forward1 , \重定向数据相关检测_1_forward2 ;
  wire [3:0] id_ex_1_aluop_2, \修改的单周期硬布线控制器_1_alu_op ;
  wire [4:0] EX_W_num, id_ex_1_shamt_2, MEM_W_num, mem_wb_1_w_2, multiplexer_3_out, multiplexer_5_out,
       multiplexer_7_out, multiplexer_12_out, R1_num, R2_num;
  wire [15:0] counter_2_q, counter_3_q, \LoadUse次数 , \总周期数 , \插入气泡数 , \无条件分支数 , \条件分支成功数 ;
  wire [31:0] a0, adder_2_out, bht_1_npc, bit_extender_1_out, bit_extender_2_out, BLTZ_result,
       ex_mem_1_pc_4_2, ex_mem_1_r1_2, ex_mem_1_r2_3, EX_R1, id_ex_1_imm_2, id_ex_1_pc_4_2, id_ex_1_r1_2,
       id_ex_1_r2_2, if_id_1_jaddr_2, if_id_1_pc_4_2, IR, Jaddr, MEM_ALUResult, mem_wb_1_alu_data_2,
       mem_wb_1_mem_readdata_2, mem_wb_1_pc_4_2, \mips_regifile下降沿_1_r1 , \mips_regifile下降沿_1_r2 ,
       multiplexer_4_out, multiplexer_8_out, multiplexer_11_out, multiplexer_15_out, PC_4, ram_1_data,
       rom_1_data, shifter_1_out, v0, WB_ALUResult, WB_R1, WB_R2, WB_ReadData;

  Clock #(.highDuration(1), .lowDuration(1)) clock_1 (.out(CLK));
  Button _1 (.out(IR1));
  Button _2 (.out(IR2));
  Button _3 (.out(IR3));
  Button \u_继续运行  (.out(Go));
  LED #(.active("true")) led_1 (.in(W1));
  LED #(.active("true")) led_2 (.in(W2));
  LED #(.active("true")) led_3 (.in(W3));
  // Probe on bht_1_npc
  Hex_Digit_Display hex_digit_display_1 (.value(out_10[31:28]));  // open: dp
  // Probe on \总周期数 
  // Probe on \无条件分支数 
  // Probe on \条件分支成功数 
  // Probe on \插入气泡数 
  // Probe on \LoadUse次数 
  // Probe on out_3[11:0]
  // Probe on out_4[11:0]
  // Probe on out_5[11:0]
  // Probe on out_6[11:0]
  // Probe on out_7[11:0]
  BHT bht_1 (
    .JR(JR), .BNE(BNE), .BLTZ(multiplexer_1_out), .JMP(JMP), .in_8(tunnel), .CLK(CLK), .IF_PC(out_3),
    .ID_PC(out_4), .EX_PC(out_5), .JAL(EX_JAL), .BEQ(BEQ), .J_JALaddr(Jaddr), .BNE_BEQ_BLTZaddr(adder_2_out),
    .JRaddr(EX_R1), .NPC(bht_1_npc), .\插入气泡 (\插入气泡 ));
  Hex_Digit_Display hex_digit_display_2 (.value(out_10[27:24]));  // open: dp
  Hex_Digit_Display hex_digit_display_3 (.value(out_10[23:20]));  // open: dp
  Multiplexer #(.select(1), .width(1), .disabled("Z"), .enable("false")) multiplexer_1 (
    .in0(1'b0), .in1(BLTZ), .out(multiplexer_1_out), .sel(comparator_1_eq));
  Comparator #(.width(32), .mode("unsigned")) comparator_1 (
    .a(BLTZ_result), .b(32'h1), .eq(comparator_1_eq));  // open: gt, lt
  Hex_Digit_Display hex_digit_display_4 (.value(out_10[15:12]));  // open: dp
  Hex_Digit_Display hex_digit_display_5 (.value(out_10[19:16]));  // open: dp
  Register #(.width(32), .trigger("rising"), .Select("low")) PC (
    .D(bht_1_npc), .en(\PC_IF_ID使能 ), .Q(out_3), .clk(CLK), .clr(1'b0));
  Hex_Digit_Display hex_digit_display_6 (.value(out_10[11:8]));  // open: dp
  Hex_Digit_Display hex_digit_display_7 (.value(out_10[7:4]));  // open: dp
  // Probe on \总周期数 
  Adder #(.width(32)) adder_1 (.a(out_3), .b(32'h4), .out(PC_4));  // open: cin, cout
  Hex_Digit_Display hex_digit_display_8 (.value(out_10[3:0]));  // open: dp
  ROM #(.addrWidth(10), .dataWidth(32), .Select("high")) rom_1 (.addr(out_3[11:2]), .data(rom_1_data));
  IF_ID if_id_1 (
    .IR(rom_1_data), .Jaddr({out_3[31:28], rom_1_data[25:0], 2'b00}), .PC_4(PC_4), .IR_2(IR),
    .Jaddr_2(if_id_1_jaddr_2), .PC_4_2(if_id_1_pc_4_2), .Reset(\插入气泡 ), .EN(\PC_IF_ID使能 ), .CLK(CLK),
    .PC(out_3), .PC_2(out_4));
  \修改的单周期硬布线控制器  \u_修改的单周期硬布线控制器_1  (
    .OP(IR[31:26]), .Func(IR[5:0]), .ALU_OP(\修改的单周期硬布线控制器_1_alu_op ), .MemToReg(\修改的单周期硬布线控制器_1_memtoreg ),
    .MemWrite(\修改的单周期硬布线控制器_1_memwrite ), .ALU_SRC(\修改的单周期硬布线控制器_1_alu_src ),
    .RegWrite(\修改的单周期硬布线控制器_1_regwrite ), .SysCALL(ID_SysCall), .SignedExt(SignedExt),
    .RegDst(\修改的单周期硬布线控制器_1_regdst ), .Beq(\修改的单周期硬布线控制器_1_beq ), .Bne(\修改的单周期硬布线控制器_1_bne ),
    .JR(\修改的单周期硬布线控制器_1_jr ), .JMP(\修改的单周期硬布线控制器_1_jmp ), .JAL(\修改的单周期硬布线控制器_1_jal ),
    .LUI(\修改的单周期硬布线控制器_1_lui ), .BLTZ(\修改的单周期硬布线控制器_1_bltz ), .LB(\修改的单周期硬布线控制器_1_lb ));  // open: ERET
  \源寄存器使用情况封装电路  \u_源寄存器使用情况封装电路_1  (.OP(IR[31:26]), .Func(IR[5:0]), .R1_Used(R1_Used), .R2_Used(R2_Used));
  // Probe on IR[25:21]
  // Probe on IR[20:16]
  assign bit_extender_1_out = {{16{IR[15]}}, IR[15:0]};  // Bit_Extender bit_extender_1
  assign bit_extender_2_out = {{16{1'b0}}, IR[15:0]};  // Bit_Extender bit_extender_2
  Multiplexer #(.select(1), .width(5), .disabled("Z"), .enable("false")) multiplexer_2 (
    .in0(IR[20:16]), .in1(5'b00100), .out(R2_num), .sel(ID_SysCall));
  Multiplexer #(.select(1), .width(5), .disabled("Z"), .enable("false")) multiplexer_3 (
    .in0(IR[20:16]), .in1(IR[15:11]), .out(multiplexer_3_out), .sel(\修改的单周期硬布线控制器_1_regdst ));
  Multiplexer #(.select(1), .width(32), .disabled("Z"), .enable("false")) multiplexer_4 (
    .in0(bit_extender_1_out), .in1(bit_extender_2_out), .out(multiplexer_4_out), .sel(SignedExt));
  Multiplexer #(.select(1), .width(5), .disabled("Z"), .enable("false")) multiplexer_5 (
    .in0(IR[25:21]), .in1({5{1'b1}}), .out(multiplexer_5_out), .sel(\修改的单周期硬布线控制器_1_jr ));
  Multiplexer #(.select(1), .width(5), .disabled("Z"), .enable("false")) multiplexer_6 (
    .in0(multiplexer_5_out), .in1(5'b00010), .out(R1_num), .sel(ID_SysCall));
  Multiplexer #(.select(1), .width(5), .disabled("Z"), .enable("false")) multiplexer_7 (
    .in0(mem_wb_1_w_2), .in1({5{1'b1}}), .out(multiplexer_7_out), .sel(WB_JAL));
  \MIPS_Regifile下降沿  \mips_regifile下降沿_1  (
    .Din(RDin), .Clk(CLK), .R1(\mips_regifile下降沿_1_r1 ), .R2(\mips_regifile下降沿_1_r2 ), .WE(RegWrite),
    .W_num(multiplexer_7_out), .R1_num(R1_num), .R2_num(R2_num));
  not not_1 (not_1_out, Pause);
  ID_EX id_ex_1 (
    .AluOP(\修改的单周期硬布线控制器_1_alu_op ), .AluSrcB(\修改的单周期硬布线控制器_1_alu_src ), .R1(\mips_regifile下降沿_1_r1 ),
    .R2(\mips_regifile下降沿_1_r2 ), .W(multiplexer_3_out), .Jaddr(if_id_1_jaddr_2), .AluOP_2(id_ex_1_aluop_2),
    .AluSrcB_2(id_ex_1_alusrcb_2), .R1_2(id_ex_1_r1_2), .R2_2(id_ex_1_r2_2), .W_2(EX_W_num),
    .Imm_2(id_ex_1_imm_2), .Jaddr_2(Jaddr), .PC_4_2(id_ex_1_pc_4_2), .Imm(multiplexer_4_out),
    .PC_4(if_id_1_pc_4_2), .RST(\ID_EX气泡 ), .EN(not_1_out), .CLK(CLK), .JR_2(JR), .JR(\修改的单周期硬布线控制器_1_jr ),
    .JMP(\修改的单周期硬布线控制器_1_jmp ), .JMP_2(JMP), .Bne(\修改的单周期硬布线控制器_1_bne ), .Bne_2(BNE),
    .Beq(\修改的单周期硬布线控制器_1_beq ), .Beq_2(BEQ), .BLTZ(\修改的单周期硬布线控制器_1_bltz ), .BLTZ_2(BLTZ),
    .LUI(\修改的单周期硬布线控制器_1_lui ), .LUI_2(LUI), .MenWrite(\修改的单周期硬布线控制器_1_memwrite ),
    .MenWrite_2(id_ex_1_menwrite_2), .MenToReg(\修改的单周期硬布线控制器_1_memtoreg ), .MenToReg_2(EX_MenToReg),
    .JAL(\修改的单周期硬布线控制器_1_jal ), .JAL_2(EX_JAL), .SysCall(ID_SysCall), .SysCall_2(id_ex_1_syscall_2),
    .LB(\修改的单周期硬布线控制器_1_lb ), .LB_2(id_ex_1_lb_2), .RegWrite(\修改的单周期硬布线控制器_1_regwrite ),
    .RegWrite_2(EX_RegWrite), .shamt_2(id_ex_1_shamt_2), .shamt(IR[10:6]), .PC(out_4), .PC_2(out_5));  // open: ERET, ERET_2
  // Probe on RDin
  Counter #(.width(16), .max('hffff), .ongoal("wrap"), .trigger("rising"), .behavior("old")) counter_1 (
    .count(not_1_out), .Q(\总周期数 ), .clk(CLK), .clr(1'b0));  // open: load, D, carry, preset
  Multiplexer #(.select(2), .width(32), .disabled("Z"), .enable("false")) multiplexer_8 (
    .in0(id_ex_1_r2_2), .in1(WB_ReadData), .in2(WB_ALUResult), .in3(MEM_ALUResult), .out(multiplexer_8_out),
    .sel(Forward2));
  Multiplexer #(.select(1), .width(32), .disabled("Z"), .enable("false")) multiplexer_9 (
    .in0({32{1'b0}}), .in1(WB_R1), .out(v0), .sel(syscall));
  // Probe on \总周期数 
  Multiplexer #(.select(2), .width(32), .disabled("Z"), .enable("false")) multiplexer_10 (
    .in0(id_ex_1_r1_2), .in1(WB_ReadData), .in2(WB_ALUResult), .in3(MEM_ALUResult), .out(EX_R1),
    .sel(Forward1));
  Multiplexer #(.select(1), .width(32), .disabled("Z"), .enable("false")) multiplexer_11 (
    .in0(multiplexer_8_out), .in1(id_ex_1_imm_2), .out(multiplexer_11_out), .sel(id_ex_1_alusrcb_2));
  Shifter #(.width(32), .shift("ll")) shifter_1 (.in(id_ex_1_imm_2), .\dist (5'b00010), .out(shifter_1_out));
  Adder #(.width(32)) adder_2 (.a(shifter_1_out), .b(id_ex_1_pc_4_2), .out(adder_2_out));  // open: cin, cout
  MIPS_ALU mips_alu_1 (
    .X(EX_R1), .Y(multiplexer_11_out), .AluOP(id_ex_1_aluop_2), .Equal(tunnel), .Result(BLTZ_result),
    .shamt(multiplexer_12_out));  // open: Result_2
  // Probe on BLTZ_result
  Multiplexer #(.select(1), .width(5), .disabled("Z"), .enable("false")) multiplexer_12 (
    .in0(id_ex_1_shamt_2), .in1(5'b10000), .out(multiplexer_12_out), .sel(LUI));
  Multiplexer #(.select(1), .width(32), .disabled("Z"), .enable("false")) multiplexer_13 (
    .in0({32{1'b0}}), .in1(WB_R2), .out(a0), .sel(syscall));
  EX_MEM ex_mem_1 (
    .LB(id_ex_1_lb_2), .SysCall(id_ex_1_syscall_2), .RegWrite(EX_RegWrite), .MenToReg(EX_MenToReg),
    .R(BLTZ_result), .R2(multiplexer_8_out), .W(EX_W_num), .LB_2(ex_mem_1_lb_2),
    .SysCall_2(ex_mem_1_syscall_2), .RegWrite_2(MEM_RegWrite), .MenToReg_2(MEM_MenToReg),
    .R_2(MEM_ALUResult), .R2_2(MDin), .W_2(MEM_W_num), .RST(1'b0), .EN(not_1_out), .CLK(CLK),
    .MenWrite(id_ex_1_menwrite_2), .MenWrite_2(MemWrite), .JAL_2(ex_mem_1_jal_2), .JAL(EX_JAL),
    .PC_4(id_ex_1_pc_4_2), .PC_4_2(ex_mem_1_pc_4_2), .R2_3(ex_mem_1_r2_3), .R1(EX_R1), .R1_2(ex_mem_1_r1_2),
    .PC(out_5), .PC_2(out_6));  // open: ERET, ERET_2
  // Probe on MEM_ALUResult
  Comparator #(.width(32), .mode("unsigned")) comparator_2 (.a(v0), .b(32'ha), .eq(comparator_2_eq));  // open: gt, lt
  not not_2 (not_2_out, comparator_2_eq);
  Multiplexer #(.select(1), .width(1), .disabled("Z"), .enable("false")) multiplexer_14 (
    .in0(1'b0), .in1(Go), .out(multiplexer_14_out), .sel(comparator_2_eq));
  and and_1 (and_1_out, MemWrite, not_3_out);
  not not_3 (not_3_out, syscall);
  xor xor_1 (Pause, comparator_2_eq, multiplexer_14_out);
  RAM #(.addrWidth(10), .dataWidth(32), .bus("separate"), .Select("high")) ram_1 (
    .addr({2'b00, MEM_ALUResult[9:2]}), .din(MDin), .data(ram_1_data), .str(and_1_out), .clk(CLK),
    .ld(not_3_out), .clr(1'b0));  // open: sel
  and and_2 (and_2_out, syscall, not_2_out);
  Multiplexer #(.select(1), .width(32), .disabled("Z"), .enable("false")) multiplexer_15 (
    .in0(out_10), .in1(a0), .out(multiplexer_15_out), .sel(and_2_out));
  MEM_WB mem_wb_1 (
    .LB(ex_mem_1_lb_2), .SysCall(ex_mem_1_syscall_2), .RegWrite(MEM_RegWrite), .MenToReg(MEM_MenToReg),
    .ALU_Data(MEM_ALUResult), .MEM_ReadData(ram_1_data), .W(MEM_W_num), .LB_2(LB), .SysCall_2(syscall),
    .RegWrite_2(RegWrite), .MenToReg_2(mem_wb_1_mentoreg_2), .ALU_Data_2(mem_wb_1_alu_data_2),
    .MEM_ReadData_2(mem_wb_1_mem_readdata_2), .W_2(mem_wb_1_w_2), .RST(1'b0), .EN(not_1_out), .CLK(CLK),
    .JAL(ex_mem_1_jal_2), .JAL_2(WB_JAL), .PC_4(ex_mem_1_pc_4_2), .PC_4_2(mem_wb_1_pc_4_2),
    .\LB低两位 (MEM_ALUResult[1:0]), .\LB低两位_2 (\mem_wb_1_lb低两位_2 ), .R1(ex_mem_1_r1_2), .R1_2(WB_R1),
    .R2(ex_mem_1_r2_3), .R2_2(WB_R2), .PC(out_6), .PC_2(out_7));  // open: ERET, ERET_2
  Register #(.width(32), .trigger("rising"), .Select("low")) register_1 (
    .D(multiplexer_15_out), .Q(out_10), .clk(CLK));  // open: en, clr
  \写入寄存器数据判断处理器  \u_写入寄存器数据判断处理器_1  (
    .in_3(mem_wb_1_alu_data_2), .WB_PC_4(mem_wb_1_pc_4_2), .out_6(WB_ALUResult), .LB(LB), .WB_JAL(WB_JAL),
    .\LB低两位 (\mem_wb_1_lb低两位_2 ));
  \写入寄存器数据判断处理器  \u_写入寄存器数据判断处理器_2  (
    .in_3(mem_wb_1_mem_readdata_2), .WB_PC_4(mem_wb_1_pc_4_2), .out_6(WB_ReadData), .LB(LB), .WB_JAL(WB_JAL),
    .\LB低两位 (\mem_wb_1_lb低两位_2 ));
  Multiplexer #(.select(1), .width(32), .disabled("Z"), .enable("false")) multiplexer_16 (
    .in0(WB_ALUResult), .in1(WB_ReadData), .out(RDin), .sel(mem_wb_1_mentoreg_2));
  \重定向数据相关检测  \u_重定向数据相关检测_1  (
    .EX_MemToReg(EX_MenToReg), .EX_RegWrite(EX_RegWrite), .MEM_MemToReg(MEM_MenToReg),
    .MEM_RegWrite(MEM_RegWrite), .MEM_W_num(MEM_W_num), .Pause(Pause), .EX_W_num(EX_W_num),
    .\转跳插入气泡 (\插入气泡 ), .ID_R1_num(R1_num), .ID_R2_num(R2_num), .R1_Used(R1_Used), .R2_Used(R2_Used),
    .Forward1(\重定向数据相关检测_1_forward1 ), .Forward2(\重定向数据相关检测_1_forward2 ), .\ID_EX气泡 (\ID_EX气泡 ),
    .PC_IF_ID_EN(\PC_IF_ID使能 ));
  // Probe on Forward1
  Register #(.width(2), .trigger("rising"), .Select("low")) register_2 (
    .D(\重定向数据相关检测_1_forward1 ), .Q(Forward1), .clk(CLK));  // open: en, clr
  // Probe on Forward2
  Register #(.width(2), .trigger("rising"), .Select("low")) register_3 (
    .D(\重定向数据相关检测_1_forward2 ), .Q(Forward2), .clk(CLK));  // open: en, clr
  // Probe on counter_2_q
  Counter #(.width(16), .max('hffff), .ongoal("wrap"), .trigger("rising"), .behavior("old")) counter_2 (
    .count(\ID_EX气泡 ), .Q(counter_2_q), .clk(CLK), .clr(1'b0));  // open: load, D, carry, preset
  Counter #(.width(16), .max('hffff), .ongoal("wrap"), .trigger("rising"), .behavior("old")) counter_3 (
    .count(\插入气泡 ), .Q(counter_3_q), .clk(CLK), .clr(1'b0));  // open: load, D, carry, preset
  Subtractor #(.width(16)) subtractor_1 (.a(counter_2_q), .b(counter_3_q), .out(\插入气泡数 ));  // open: bin, bout

  // Other names for the same wires on the sheet: IF_PC[31:0] = out_3; PC[31:0] = out_3; EX_PC[31:0] = out_5;
  //   ID_PC[31:0] = out_4; JRaddr[31:0] = EX_R1; LedData[31:0] = out_10; MEM_PC[31:0] = out_6; WB_PC[31:0] = out_7

  // Notes on the sheet:
  //   中断源
  //   中断等待指示
  //   IF
  //   数码管输出
  //   指令存储器
  //   拓展指令依次为：LUI、SLTIU、LB、BLTZ
  //   contents of rom_1 (hex, n*v repeats v):
  //   20110001 8000c05 20110001 20120002 20130003 8000c09 20110001 20120002 20130003 8000c0d 20110001
  //   20120002 20130003 8000c11 20110001 20120002 20130003 c000cf4 20100001 20110001 118fc0 112020
  //   20020022 c 118882 12200001 8000c15 112020 20020022 c 20110001 118880 112020 20020022 c 12200001
  //   8000c1f 20110001 118fc0 112020 20020022 c 1188c3 112020 20020022 c 118903 112020 20020022 c 118903
  //   112020 20020022 c 118903 112020 20020022 c 118903 112020 20020022 c 118903 112020 20020022 c 118903
  //   112020 20020022 c 118903 112020 20020022 c 20100001 109fc0 139fc3 8021 2012000c 24160003 26100001
  //   3210000f 20080008 20090001 139900 2709825 132020 20020022 c 1094022 1500fff9 22100001 2018000f
  //   2188024 108700 20080008 20090001 139902 2709825 132021 20020022 c 1094022 1500fff9 108702 2c9b022
  //   12c00001 8000c50 4020 1084027 84400 3508ffff 82021 20020022 c 2010ffff 20110000 ae300000 22100001
  //   22310004 ae300000 22100001 22310004 ae300000 22100001 22310004 ae300000 22100001 22310004 ae300000
  //   22100001 22310004 ae300000 22100001 22310004 ae300000 22100001 22310004 ae300000 22100001 22310004
  //   ae300000 22100001 22310004 ae300000 22100001 22310004 ae300000 22100001 22310004 ae300000 22100001
  //   22310004 ae300000 22100001 22310004 ae300000 22100001 22310004 ae300000 22100001 22310004 ae300000
  //   22100001 22310004 22100001 8020 2011003c 8e130000 8e340000 274402a 11000002 ae330000 ae140000
  //   2231fffc 1611fff8 102020 20020022 c 22100004 2011003c 1611fff2 2002000a c 200b0008 3c11fedc 3631ffff
  //   112020 20020022 c 3c11ba98 112020 c 3c117654 112020 c 3c113210 112020 c 216bffff 1560fff0 2002000a c
  //   2008ffff 20090000 20111997 112020 20020022 c 2288820 2e291949 1120fffa 20090000 200b0010 34118483
  //   20120404 118c00 129400 36318281 22520404 ad310000 2328820 21290004 216bffff 1560fffb 200b0020
  //   20090000 81310000 112020 20020022 c 21290001 216bffff 1560fff9 2002000a c 2011fff1 112020 20020022 c
  //   22310001 620fffb 2002000a c 20100000 22100001 102020 20020022 c 22100002 102020 20020022 c 22100003
  //   102020 20020022 c 22100004 102020 20020022 c 22100005 102020 20020022 c 22100006 102020 20020022 c
  //   22100007 102020 20020022 c 22100008 102020 20020022 20020022 c 3e00008
  //   IR
  //   SignedExt
  //   OP
  //   Func
  //   rs
  //   rt
  //   rd
  //   shamt
  //   imm
  //   ID
  //   RegDst
  //   RegDst
  //   为方便自动评测，需要输出PC，IR，寄存器文件写入端口RDin，内存写入端口MDin等信号
  //   $a0
  //   $v0
  //   Bne
  //   LUI
  //   BLTZ
  //   Beq
  //   EX
  //   JAL
  //   JMP
  //   JR
  //   AluSrcB
  //   AluOP
  //   数码管输出应该用寄存器锁存，否则显示数据只能一闪而过
  //   总复位信号应将除ROM以外所有存储组件全部清零
  //   MEM
  //   MemWrite
  //   LB
  //   Syscall
  //   WB
  //   RegWrite
  //   MemToReg
endmodule

module BHT (
  input  JR,
  input  BNE,
  input  BLTZ,
  input  [31:0] IF_PC,
  input  [31:0] ID_PC,
  input  [31:0] EX_PC,
  input  JMP,
  input  in_8,
  input  CLK,
  input  JAL,
  input  BEQ,
  input  [31:0] J_JALaddr,
  input  [31:0] BNE_BEQ_BLTZaddr,
  input  [31:0] JRaddr,
  output \插入气泡 ,
  output [31:0] NPC
);

  wire and_1_out, and_6_out, and_7_out, \BHT执行跳转 , \BHT未执行跳转 , BLTZ_out, comparator_2_eq, comparator_12_lt,
       comparator_13_lt, comparator_14_lt, comparator_15_lt, comparator_16_eq, comparator_17_eq,
       comparator_18_eq, comparator_19_eq, comparator_20_eq, comparator_21_eq, comparator_22_eq,
       comparator_23_eq, comparator_24_lt, comparator_25_lt, comparator_26_lt, comparator_27_eq,
       comparator_28_eq, comparator_29_eq, comparator_30_eq, comparator_31_eq, comparator_32_eq,
       comparator_33_eq, comparator_34_eq, EN1, EN2, EN3, EN4, EN5, EN6, EN7, EN8, EQJMP_out, EX_MISS,
       EX_PC_0, HIT1, HIT2, HIT3, HIT4, HIT5, HIT6, HIT7, HIT8, IF_MISS, J_out, JAL_out, JR_out,
       multiplexer_2_out, NEEQ_out, NEJMP_out, or_1_out, or_4_out, or_5_out, or_6_out, or_7_out, or_8_out,
       or_9_out, or_10_out, or_11_out, or_12_out, or_13_out, or_14_out, or_15_out, or_16_out, or_17_out,
       or_18_out, or_19_out, or_20_out, RST1, RST2, RST3, RST4, RST5, RST6, RST7, RST8, V1, V2, V3, V4, V5,
       V6, V7, V8, \不分支1 , \不分支2 , \不分支3 , \不分支4 , \不分支5 , \不分支6 , \不分支7 , \不分支8 , \不要跳且没跳 , \不要跳却跳 ,
       \不需要跳转 , \分支成功 , \有条件转跳语句 , \要跳不跳 , \要跳且跳 ;
  wire [1:0] H1, H2, H3, H4, H5, H6, H7, H8, \预测历史fsm_1_更新状态 , \预测历史fsm_2_更新状态 , \预测历史fsm_3_更新状态 ,
       \预测历史fsm_4_更新状态 , \预测历史fsm_5_更新状态 , \预测历史fsm_6_更新状态 , \预测历史fsm_7_更新状态 , \预测历史fsm_8_更新状态 ;
  wire [2:0] CMP1_1, CMP1_2, CMP1_3, CMP1_4, CMP2_1, CMP2_2, \写入寄存器编号 ;
  wire [31:0] CHOICE1, CHOICE2, CHOICE3, CHOICE4, CHOICE5, CHOICE6, CHOICE7, counter_1_q, EX_PC_4, IF_PC_4,
       IRPC1, IRPC2, IRPC3, IRPC4, IRPC5, IRPC6, IRPC7, IRPC8, LRU1, LRU2, LRU3, LRU4, LRU5, LRU6, LRU7,
       LRU8, multiplexer_3_out, multiplexer_4_out, multiplexer_5_out, multiplexer_6_out, multiplexer_7_out,
       multiplexer_8_out, multiplexer_9_out, multiplexer_10_out, multiplexer_26_out, multiplexer_27_out,
       multiplexer_28_out, multiplexer_29_out, multiplexer_30_out, multiplexer_31_out, multiplexer_32_out,
       multiplexer_33_out, multiplexer_34_out, TarPC1, TarPC2, TarPC3, TarPC4, TarPC5, TarPC6, TarPC7,
       TarPC8, \根据IF判断的NPC , \正常指令地址 , \目标转跳地址 ;

  Adder #(.width(32)) adder_1 (.a(IF_PC), .b(32'h4), .out(IF_PC_4));  // open: cin, cout
  and NEJMP (NEJMP_out, BNE, ~in_8);  // AND_Gate
  and EQJMP (EQJMP_out, in_8, BEQ);
  or or_1 (or_1_out, NEJMP_out, EQJMP_out);
  Counter #(.width(32), .max('hffffffff), .ongoal("wrap"), .trigger("rising"), .behavior("new")) counter_1 (
    .Q(counter_1_q), .clk(CLK));  // open: load, D, count, carry, clr, preset, down
  // Probe on counter_1_q
  and u_JR (JR_out, JR, JMP, ~JAL, ~NEJMP_out, ~EQJMP_out, ~BLTZ);  // AND_Gate
  and J (J_out, ~JR, JMP, ~JAL, ~NEJMP_out, ~EQJMP_out, ~BLTZ);  // AND_Gate
  and u_JAL (JAL_out, ~JR, JMP, JAL, ~NEJMP_out, ~EQJMP_out, ~BLTZ);  // AND_Gate
  and u_BLTZ (BLTZ_out, ~JR, ~JMP, ~JAL, ~NEJMP_out, ~EQJMP_out, BLTZ);  // AND_Gate
  and NEEQ (NEEQ_out, ~JR, ~JMP, ~JAL, or_1_out, ~BLTZ);  // AND_Gate
  and and_1 (and_1_out, ~NEEQ_out, ~BLTZ_out, ~JAL_out, ~J_out, ~JR_out);  // AND_Gate
  assign \正常指令地址  = and_1_out ? IF_PC_4 : 32'bz;  // Controlled_Buffer controlled_buffer_1
  assign \正常指令地址  = BLTZ_out ? BNE_BEQ_BLTZaddr : 32'bz;  // Controlled_Buffer controlled_buffer_2
  assign \正常指令地址  = NEEQ_out ? BNE_BEQ_BLTZaddr : 32'bz;  // Controlled_Buffer controlled_buffer_3
  assign \正常指令地址  = J_out ? J_JALaddr : 32'bz;  // Controlled_Buffer controlled_buffer_4
  assign \正常指令地址  = JAL_out ? J_JALaddr : 32'bz;  // Controlled_Buffer controlled_buffer_5
  or or_2 (\插入气泡 , \要跳不跳 , \不要跳却跳 );
  // Probe on NPC
  // Probe on \正常指令地址 
  assign \正常指令地址  = JR_out ? JRaddr : 32'bz;  // Controlled_Buffer controlled_buffer_6
  Comparator #(.width(32), .mode("unsigned")) comparator_1 (.a(\正常指令地址 ), .b(IF_PC_4), .eq(\不需要跳转 ));  // open: gt, lt
  not not_1 (\分支成功 , \不需要跳转 );
  and and_2 (\要跳不跳 , \分支成功 , \BHT未执行跳转 );
  and and_3 (\要跳且跳 , \分支成功 , \BHT执行跳转 );
  Register #(.width(1), .trigger("rising"), .Select("low")) register_1 (
    .D(1'b1), .en(EN1), .Q(V1), .clk(CLK));  // open: clr
  Register #(.width(1), .trigger("rising"), .Select("low")) register_2 (
    .D(1'b1), .en(EN2), .Q(V2), .clk(CLK));  // open: clr
  Register #(.width(1), .trigger("rising"), .Select("low")) register_3 (
    .D(1'b1), .en(EN3), .Q(V3), .clk(CLK));  // open: clr
  Register #(.width(1), .trigger("rising"), .Select("low")) register_4 (
    .D(1'b1), .en(EN4), .Q(V4), .clk(CLK));  // open: clr
  Register #(.width(1), .trigger("rising"), .Select("low")) register_5 (
    .D(1'b1), .en(EN5), .Q(V5), .clk(CLK));  // open: clr
  Register #(.width(1), .trigger("rising"), .Select("low")) register_6 (
    .D(1'b1), .en(EN6), .Q(V6), .clk(CLK));  // open: clr
  Register #(.width(1), .trigger("rising"), .Select("low")) register_7 (
    .D(1'b1), .en(EN7), .Q(V7), .clk(CLK));  // open: clr
  Register #(.width(1), .trigger("rising"), .Select("low")) register_8 (
    .D(1'b1), .en(EN8), .Q(V8), .clk(CLK));  // open: clr
  and and_4 (\不要跳且没跳 , \不需要跳转 , \BHT未执行跳转 );
  Register #(.width(32), .trigger("rising"), .Select("low")) register_9 (
    .D(EX_PC), .en(EN1), .Q(IRPC1), .clk(CLK));  // open: clr
  Register #(.width(32), .trigger("rising"), .Select("low")) register_10 (
    .D(EX_PC), .en(EN2), .Q(IRPC2), .clk(CLK));  // open: clr
  Register #(.width(32), .trigger("rising"), .Select("low")) register_11 (
    .D(EX_PC), .en(EN3), .Q(IRPC3), .clk(CLK));  // open: clr
  Register #(.width(32), .trigger("rising"), .Select("low")) register_12 (
    .D(EX_PC), .en(EN4), .Q(IRPC4), .clk(CLK));  // open: clr
  Register #(.width(32), .trigger("rising"), .Select("low")) register_13 (
    .D(EX_PC), .en(EN5), .Q(IRPC5), .clk(CLK));  // open: clr
  Register #(.width(32), .trigger("rising"), .Select("low")) register_14 (
    .D(EX_PC), .en(EN6), .Q(IRPC6), .clk(CLK));  // open: clr
  Register #(.width(32), .trigger("rising"), .Select("low")) register_15 (
    .D(EX_PC), .en(EN7), .Q(IRPC7), .clk(CLK));  // open: clr
  Register #(.width(32), .trigger("rising"), .Select("low")) register_16 (
    .D(EX_PC), .en(EN8), .Q(IRPC8), .clk(CLK));  // open: clr
  Comparator #(.width(32), .mode("unsigned")) comparator_2 (
    .a(ID_PC), .b(EX_PC_4), .eq(comparator_2_eq));  // open: gt, lt
  Multiplexer #(.select(1), .width(1), .disabled("Z"), .enable("false")) multiplexer_1 (
    .in0(comparator_2_eq), .in1(1'b1), .out(\BHT未执行跳转 ), .sel(EX_PC_0));
  Register #(.width(32), .trigger("rising"), .Select("low")) register_17 (
    .D(\目标转跳地址 ), .en(EN1), .Q(TarPC1), .clk(CLK));  // open: clr
  Register #(.width(32), .trigger("rising"), .Select("low")) register_18 (
    .D(\目标转跳地址 ), .en(EN2), .Q(TarPC2), .clk(CLK));  // open: clr
  Register #(.width(32), .trigger("rising"), .Select("low")) register_19 (
    .D(\目标转跳地址 ), .en(EN3), .Q(TarPC3), .clk(CLK));  // open: clr
  Register #(.width(32), .trigger("rising"), .Select("low")) register_20 (
    .D(\目标转跳地址 ), .en(EN4), .Q(TarPC4), .clk(CLK));  // open: clr
  Register #(.width(32), .trigger("rising"), .Select("low")) register_21 (
    .D(\目标转跳地址 ), .en(EN5), .Q(TarPC5), .clk(CLK));  // open: clr
  Register #(.width(32), .trigger("rising"), .Select("low")) register_22 (
    .D(\目标转跳地址 ), .en(EN6), .Q(TarPC6), .clk(CLK));  // open: clr
  Register #(.width(32), .trigger("rising"), .Select("low")) register_23 (
    .D(\目标转跳地址 ), .en(EN7), .Q(TarPC7), .clk(CLK));  // open: clr
  Register #(.width(32), .trigger("rising"), .Select("low")) register_24 (
    .D(\目标转跳地址 ), .en(EN8), .Q(TarPC8), .clk(CLK));  // open: clr
  not not_2 (\BHT执行跳转 , \BHT未执行跳转 );
  and and_5 (\不要跳却跳 , \不需要跳转 , \BHT执行跳转 );
  \预测历史FSM  \u_预测历史fsm_1  (.\前序状态 (H1), .\分支成功 (\分支成功 ), .\更新状态 (\预测历史fsm_1_更新状态 ), .EN(EN1));
  \预测历史FSM  \u_预测历史fsm_2  (.\前序状态 (H2), .\分支成功 (\分支成功 ), .\更新状态 (\预测历史fsm_2_更新状态 ), .EN(EN2));
  \预测历史FSM  \u_预测历史fsm_3  (.\前序状态 (H3), .\分支成功 (\分支成功 ), .\更新状态 (\预测历史fsm_3_更新状态 ), .EN(EN3));
  \预测历史FSM  \u_预测历史fsm_4  (.\前序状态 (H4), .\分支成功 (\分支成功 ), .\更新状态 (\预测历史fsm_4_更新状态 ), .EN(EN4));
  \预测历史FSM  \u_预测历史fsm_5  (.\前序状态 (H5), .\分支成功 (\分支成功 ), .\更新状态 (\预测历史fsm_5_更新状态 ), .EN(EN5));
  \预测历史FSM  \u_预测历史fsm_6  (.\前序状态 (H6), .\分支成功 (\分支成功 ), .\更新状态 (\预测历史fsm_6_更新状态 ), .EN(EN6));
  \预测历史FSM  \u_预测历史fsm_7  (.\前序状态 (H7), .\分支成功 (\分支成功 ), .\更新状态 (\预测历史fsm_7_更新状态 ), .EN(EN7));
  \预测历史FSM  \u_预测历史fsm_8  (.\前序状态 (H8), .\分支成功 (\分支成功 ), .\更新状态 (\预测历史fsm_8_更新状态 ), .EN(EN8));
  or or_3 (\有条件转跳语句 , BEQ, BNE, BLTZ);
  Comparator #(.width(32), .mode("unsigned")) comparator_3 (.a(EX_PC), .b({32{1'b0}}), .eq(EX_PC_0));  // open: gt, lt
  Adder #(.width(32)) adder_2 (.a(EX_PC), .b(32'h4), .out(EX_PC_4));  // open: cin, cout
  Register #(.width(2), .trigger("rising"), .Select("low")) register_25 (
    .D(\预测历史fsm_1_更新状态 ), .en(or_4_out), .Q(H1), .clk(CLK));  // open: clr
  or or_4 (or_4_out, HIT1, EN1);
  Register #(.width(2), .trigger("rising"), .Select("low")) register_26 (
    .D(\预测历史fsm_2_更新状态 ), .en(or_5_out), .Q(H2), .clk(CLK));  // open: clr
  or or_5 (or_5_out, HIT2, EN2);
  Register #(.width(2), .trigger("rising"), .Select("low")) register_27 (
    .D(\预测历史fsm_3_更新状态 ), .en(or_6_out), .Q(H3), .clk(CLK));  // open: clr
  or or_6 (or_6_out, HIT3, EN3);
  Register #(.width(2), .trigger("rising"), .Select("low")) register_28 (
    .D(\预测历史fsm_4_更新状态 ), .en(or_7_out), .Q(H4), .clk(CLK));  // open: clr
  or or_7 (or_7_out, HIT4, EN4);
  Register #(.width(2), .trigger("rising"), .Select("low")) register_29 (
    .D(\预测历史fsm_5_更新状态 ), .en(or_8_out), .Q(H5), .clk(CLK));  // open: clr
  or or_8 (or_8_out, HIT5, EN5);
  Register #(.width(2), .trigger("rising"), .Select("low")) register_30 (
    .D(\预测历史fsm_6_更新状态 ), .en(or_9_out), .Q(H6), .clk(CLK));  // open: clr
  or or_9 (or_9_out, HIT6, EN6);
  Register #(.width(2), .trigger("rising"), .Select("low")) register_31 (
    .D(\预测历史fsm_7_更新状态 ), .en(or_10_out), .Q(H7), .clk(CLK));  // open: clr
  or or_10 (or_10_out, HIT7, EN7);
  Register #(.width(2), .trigger("rising"), .Select("low")) register_32 (
    .D(\预测历史fsm_8_更新状态 ), .en(or_11_out), .Q(H8), .clk(CLK));  // open: clr
  or or_11 (or_11_out, HIT8, EN8);
  Comparator #(.width(2), .mode("unsigned")) comparator_4 (.a(2'b10), .b(H1), .gt(\不分支1 ));  // open: eq, lt
  Comparator #(.width(2), .mode("unsigned")) comparator_5 (.a(2'b10), .b(H2), .gt(\不分支2 ));  // open: eq, lt
  Comparator #(.width(2), .mode("unsigned")) comparator_6 (.a(2'b10), .b(H3), .gt(\不分支3 ));  // open: eq, lt
  Comparator #(.width(2), .mode("unsigned")) comparator_7 (.a(2'b10), .b(H4), .gt(\不分支4 ));  // open: eq, lt
  Comparator #(.width(2), .mode("unsigned")) comparator_8 (.a(2'b10), .b(H5), .gt(\不分支5 ));  // open: eq, lt
  Comparator #(.width(2), .mode("unsigned")) comparator_9 (.a(2'b10), .b(H6), .gt(\不分支6 ));  // open: eq, lt
  Comparator #(.width(2), .mode("unsigned")) comparator_10 (.a(2'b10), .b(H7), .gt(\不分支7 ));  // open: eq, lt
  Comparator #(.width(2), .mode("unsigned")) comparator_11 (.a(2'b10), .b(H8), .gt(\不分支8 ));  // open: eq, lt
  and and_6 (and_6_out, \要跳不跳 , EX_MISS);
  and and_7 (and_7_out, EX_MISS, \有条件转跳语句 , \不要跳且没跳 );
  or or_12 (or_12_out, and_6_out, and_7_out);
  Demultiplexer #(.select(3), .width(1), .tristate("false"), .disabled("Z"), .enable("false")) demultiplexer_1 (
    .out0(EN1), .out1(EN2), .out2(EN3), .out3(EN4), .out4(EN5), .out5(EN6), .out6(EN7), .out7(EN8),
    .in(multiplexer_2_out), .sel(\写入寄存器编号 ));
  Multiplexer #(.select(1), .width(1), .disabled("Z"), .enable("false")) multiplexer_2 (
    .in0(1'b0), .in1(1'b1), .out(multiplexer_2_out), .sel(or_12_out));
  or or_13 (or_13_out, RST1, EN1);
  Multiplexer #(.select(1), .width(32), .disabled("Z"), .enable("false")) multiplexer_3 (
    .in1({32{1'b0}}), .out(multiplexer_3_out), .sel(or_13_out));  // open: in0
  or or_14 (or_14_out, RST2, EN2);
  Multiplexer #(.select(1), .width(32), .disabled("Z"), .enable("false")) multiplexer_4 (
    .in1({32{1'b0}}), .out(multiplexer_4_out), .sel(or_14_out));  // open: in0
  or or_15 (or_15_out, RST3, EN3);
  Multiplexer #(.select(1), .width(32), .disabled("Z"), .enable("false")) multiplexer_5 (
    .in1({32{1'b0}}), .out(multiplexer_5_out), .sel(or_15_out));  // open: in0
  or or_16 (or_16_out, RST4, EN4);
  Multiplexer #(.select(1), .width(32), .disabled("Z"), .enable("false")) multiplexer_6 (
    .in1({32{1'b0}}), .out(multiplexer_6_out), .sel(or_16_out));  // open: in0
  or or_17 (or_17_out, RST5, EN5);
  Multiplexer #(.select(1), .width(32), .disabled("Z"), .enable("false")) multiplexer_7 (
    .in1({32{1'b0}}), .out(multiplexer_7_out), .sel(or_17_out));  // open: in0
  or or_18 (or_18_out, RST6, EN6);
  Multiplexer #(.select(1), .width(32), .disabled("Z"), .enable("false")) multiplexer_8 (
    .in1({32{1'b0}}), .out(multiplexer_8_out), .sel(or_18_out));  // open: in0
  or or_19 (or_19_out, RST7, EN7);
  Multiplexer #(.select(1), .width(32), .disabled("Z"), .enable("false")) multiplexer_9 (
    .in1({32{1'b0}}), .out(multiplexer_9_out), .sel(or_19_out));  // open: in0
  or or_20 (or_20_out, RST8, EN8);
  Multiplexer #(.select(1), .width(32), .disabled("Z"), .enable("false")) multiplexer_10 (
    .in1({32{1'b0}}), .out(multiplexer_10_out), .sel(or_20_out));  // open: in0
  Counter #(.width(32), .max('hffffffff), .ongoal("wrap"), .trigger("rising"), .behavior("new")) counter_2 (
    .load(EN1), .D(multiplexer_3_out), .Q(LRU1), .clk(CLK));  // open: count, carry, clr, preset, down
  Counter #(.width(32), .max('hffffffff), .ongoal("wrap"), .trigger("rising"), .behavior("new")) counter_3 (
    .load(EN2), .D(multiplexer_4_out), .Q(LRU2), .clk(CLK));  // open: count, carry, clr, preset, down
  Counter #(.width(32), .max('hffffffff), .ongoal("wrap"), .trigger("rising"), .behavior("new")) counter_4 (
    .load(EN3), .D(multiplexer_5_out), .Q(LRU3), .clk(CLK));  // open: count, carry, clr, preset, down
  Counter #(.width(32), .max('hffffffff), .ongoal("wrap"), .trigger("rising"), .behavior("new")) counter_5 (
    .load(EN4), .D(multiplexer_6_out), .Q(LRU4), .clk(CLK));  // open: count, carry, clr, preset, down
  Counter #(.width(32), .max('hffffffff), .ongoal("wrap"), .trigger("rising"), .behavior("new")) counter_6 (
    .load(EN5), .D(multiplexer_7_out), .Q(LRU5), .clk(CLK));  // open: count, carry, clr, preset, down
  Counter #(.width(32), .max('hffffffff), .ongoal("wrap"), .trigger("rising"), .behavior("new")) counter_7 (
    .load(EN6), .D(multiplexer_8_out), .Q(LRU6), .clk(CLK));  // open: count, carry, clr, preset, down
  Counter #(.width(32), .max('hffffffff), .ongoal("wrap"), .trigger("rising"), .behavior("new")) counter_8 (
    .load(EN7), .D(multiplexer_9_out), .Q(LRU7), .clk(CLK));  // open: count, carry, clr, preset, down
  Counter #(.width(32), .max('hffffffff), .ongoal("wrap"), .trigger("rising"), .behavior("new")) counter_9 (
    .load(EN8), .D(multiplexer_10_out), .Q(LRU8), .clk(CLK));  // open: count, carry, clr, preset, down
  Multiplexer #(.select(1), .width(32), .disabled("Z"), .enable("false")) multiplexer_11 (
    .in0(\正常指令地址 ), .in1(BNE_BEQ_BLTZaddr), .out(\目标转跳地址 ), .sel(and_7_out));
  Comparator #(.width(32), .mode("unsigned")) comparator_12 (
    .a(LRU1), .b(LRU2), .lt(comparator_12_lt));  // open: gt, eq
  Comparator #(.width(32), .mode("unsigned")) comparator_13 (
    .a(LRU3), .b(LRU4), .lt(comparator_13_lt));  // open: gt, eq
  Comparator #(.width(32), .mode("unsigned")) comparator_14 (
    .a(LRU5), .b(LRU6), .lt(comparator_14_lt));  // open: gt, eq
  Comparator #(.width(32), .mode("unsigned")) comparator_15 (
    .a(LRU7), .b(LRU8), .lt(comparator_15_lt));  // open: gt, eq
  Multiplexer #(.select(1), .width(3), .disabled("Z"), .enable("false")) multiplexer_12 (
    .in0(3'b000), .in1(3'b001), .out(CMP1_1), .sel(comparator_12_lt));
  Multiplexer #(.select(1), .width(3), .disabled("Z"), .enable("false")) multiplexer_13 (
    .in0(3'b010), .in1(3'b011), .out(CMP1_2), .sel(comparator_13_lt));
  Multiplexer #(.select(1), .width(3), .disabled("Z"), .enable("false")) multiplexer_14 (
    .in0(3'b100), .in1(3'b101), .out(CMP1_3), .sel(comparator_14_lt));
  Multiplexer #(.select(1), .width(3), .disabled("Z"), .enable("false")) multiplexer_15 (
    .in0(3'b110), .in1(3'b111), .out(CMP1_4), .sel(comparator_15_lt));
  Comparator #(.width(32), .mode("unsigned")) comparator_16 (
    .a(IF_PC), .b(IRPC1), .eq(comparator_16_eq));  // open: gt, lt
  Comparator #(.width(32), .mode("unsigned")) comparator_17 (
    .a(IF_PC), .b(IRPC2), .eq(comparator_17_eq));  // open: gt, lt
  Comparator #(.width(32), .mode("unsigned")) comparator_18 (
    .a(IF_PC), .b(IRPC3), .eq(comparator_18_eq));  // open: gt, lt
  Comparator #(.width(32), .mode("unsigned")) comparator_19 (
    .a(IF_PC), .b(IRPC4), .eq(comparator_19_eq));  // open: gt, lt
  Comparator #(.width(32), .mode("unsigned")) comparator_20 (
    .a(IF_PC), .b(IRPC5), .eq(comparator_20_eq));  // open: gt, lt
  Comparator #(.width(32), .mode("unsigned")) comparator_21 (
    .a(IF_PC), .b(IRPC6), .eq(comparator_21_eq));  // open: gt, lt
  Comparator #(.width(32), .mode("unsigned")) comparator_22 (
    .a(IF_PC), .b(IRPC7), .eq(comparator_22_eq));  // open: gt, lt
  Comparator #(.width(32), .mode("unsigned")) comparator_23 (
    .a(IF_PC), .b(IRPC8), .eq(comparator_23_eq));  // open: gt, lt
  and and_8 (RST1, comparator_16_eq, V1);
  and and_9 (RST2, comparator_17_eq, V2);
  and and_10 (RST3, comparator_18_eq, V3);
  and and_11 (RST4, comparator_19_eq, V4);
  and and_12 (RST5, comparator_20_eq, V5);
  and and_13 (RST6, comparator_21_eq, V6);
  and and_14 (RST7, comparator_22_eq, V7);
  and and_15 (RST8, comparator_23_eq, V8);
  Multiplexer #(.select(1), .width(32), .disabled("Z"), .enable("false")) multiplexer_16 (
    .in0(LRU1), .in1(LRU2), .out(CHOICE1), .sel(comparator_12_lt));
  Multiplexer #(.select(1), .width(32), .disabled("Z"), .enable("false")) multiplexer_17 (
    .in0(LRU3), .in1(LRU4), .out(CHOICE2), .sel(comparator_13_lt));
  Multiplexer #(.select(1), .width(32), .disabled("Z"), .enable("false")) multiplexer_18 (
    .in0(LRU5), .in1(LRU6), .out(CHOICE3), .sel(comparator_14_lt));
  Multiplexer #(.select(1), .width(32), .disabled("Z"), .enable("false")) multiplexer_19 (
    .in0(LRU7), .in1(LRU8), .out(CHOICE4), .sel(comparator_15_lt));
  and and_16 (IF_MISS, ~RST1, ~RST2, ~RST3, ~RST4, ~RST5, ~RST6, ~RST7, ~RST8);  // AND_Gate
  Comparator #(.width(32), .mode("unsigned")) comparator_24 (
    .a(CHOICE1), .b(CHOICE2), .lt(comparator_24_lt));  // open: gt, eq
  Comparator #(.width(32), .mode("unsigned")) comparator_25 (
    .a(CHOICE3), .b(CHOICE4), .lt(comparator_25_lt));  // open: gt, eq
  Comparator #(.width(32), .mode("unsigned")) comparator_26 (
    .a(CHOICE5), .b(CHOICE6), .lt(comparator_26_lt));  // open: gt, eq
  Comparator #(.width(32), .mode("unsigned")) comparator_27 (
    .a(EX_PC), .b(IRPC1), .eq(comparator_27_eq));  // open: gt, lt
  Comparator #(.width(32), .mode("unsigned")) comparator_28 (
    .a(EX_PC), .b(IRPC2), .eq(comparator_28_eq));  // open: gt, lt
  Comparator #(.width(32), .mode("unsigned")) comparator_29 (
    .a(EX_PC), .b(IRPC3), .eq(comparator_29_eq));  // open: gt, lt
  Comparator #(.width(32), .mode("unsigned")) comparator_30 (
    .a(EX_PC), .b(IRPC4), .eq(comparator_30_eq));  // open: gt, lt
  Comparator #(.width(32), .mode("unsigned")) comparator_31 (
    .a(EX_PC), .b(IRPC5), .eq(comparator_31_eq));  // open: gt, lt
  Comparator #(.width(32), .mode("unsigned")) comparator_32 (
    .a(EX_PC), .b(IRPC6), .eq(comparator_32_eq));  // open: gt, lt
  Comparator #(.width(32), .mode("unsigned")) comparator_33 (
    .a(EX_PC), .b(IRPC7), .eq(comparator_33_eq));  // open: gt, lt
  Comparator #(.width(32), .mode("unsigned")) comparator_34 (
    .a(EX_PC), .b(IRPC8), .eq(comparator_34_eq));  // open: gt, lt
  Multiplexer #(.select(1), .width(3), .disabled("Z"), .enable("false")) multiplexer_20 (
    .in0(CMP1_1), .in1(CMP1_2), .out(CMP2_1), .sel(comparator_24_lt));
  Multiplexer #(.select(1), .width(3), .disabled("Z"), .enable("false")) multiplexer_21 (
    .in0(CMP1_3), .in1(CMP1_4), .out(CMP2_2), .sel(comparator_25_lt));
  Multiplexer #(.select(1), .width(3), .disabled("Z"), .enable("false")) multiplexer_22 (
    .in0(CMP2_1), .in1(CMP2_2), .out(\写入寄存器编号 ), .sel(comparator_26_lt));
  and and_17 (HIT1, comparator_27_eq, V1);
  and and_18 (HIT2, comparator_28_eq, V2);
  and and_19 (HIT3, comparator_29_eq, V3);
  and and_20 (HIT4, comparator_30_eq, V4);
  and and_21 (HIT5, comparator_31_eq, V5);
  and and_22 (HIT6, comparator_32_eq, V6);
  and and_23 (HIT7, comparator_33_eq, V7);
  and and_24 (HIT8, comparator_34_eq, V8);
  Multiplexer #(.select(1), .width(32), .disabled("Z"), .enable("false")) multiplexer_23 (
    .in0(CHOICE1), .in1(CHOICE2), .out(CHOICE5), .sel(comparator_24_lt));
  Multiplexer #(.select(1), .width(32), .disabled("Z"), .enable("false")) multiplexer_24 (
    .in0(CHOICE3), .in1(CHOICE4), .out(CHOICE6), .sel(comparator_25_lt));
  Multiplexer #(.select(1), .width(32), .disabled("Z"), .enable("false")) multiplexer_25 (
    .in0(CHOICE5), .in1(CHOICE6), .out(CHOICE7), .sel(comparator_26_lt));
  and and_25 (EX_MISS, ~HIT1, ~HIT2, ~HIT3, ~HIT4, ~HIT5, ~HIT6, ~HIT7, ~HIT8);  // AND_Gate
  Multiplexer #(.select(1), .width(32), .disabled("Z"), .enable("false")) multiplexer_26 (
    .in0(TarPC1), .in1(IF_PC_4), .out(multiplexer_26_out), .sel(\不分支1 ));
  Multiplexer #(.select(1), .width(32), .disabled("Z"), .enable("false")) multiplexer_27 (
    .in0(TarPC2), .in1(IF_PC_4), .out(multiplexer_27_out), .sel(\不分支2 ));
  Multiplexer #(.select(1), .width(32), .disabled("Z"), .enable("false")) multiplexer_28 (
    .in0(TarPC3), .in1(IF_PC_4), .out(multiplexer_28_out), .sel(\不分支3 ));
  Multiplexer #(.select(1), .width(32), .disabled("Z"), .enable("false")) multiplexer_29 (
    .in0(TarPC4), .in1(IF_PC_4), .out(multiplexer_29_out), .sel(\不分支4 ));
  Multiplexer #(.select(1), .width(32), .disabled("Z"), .enable("false")) multiplexer_30 (
    .in0(TarPC5), .in1(IF_PC_4), .out(multiplexer_30_out), .sel(\不分支5 ));
  Multiplexer #(.select(1), .width(32), .disabled("Z"), .enable("false")) multiplexer_31 (
    .in0(TarPC6), .in1(IF_PC_4), .out(multiplexer_31_out), .sel(\不分支6 ));
  Multiplexer #(.select(1), .width(32), .disabled("Z"), .enable("false")) multiplexer_32 (
    .in0(TarPC7), .in1(IF_PC_4), .out(multiplexer_32_out), .sel(\不分支7 ));
  Multiplexer #(.select(1), .width(32), .disabled("Z"), .enable("false")) multiplexer_33 (
    .in0(TarPC8), .in1(IF_PC_4), .out(multiplexer_33_out), .sel(\不分支8 ));
  assign \根据IF判断的NPC  = RST1 ? multiplexer_26_out : 32'bz;  // Controlled_Buffer controlled_buffer_7
  assign \根据IF判断的NPC  = RST2 ? multiplexer_27_out : 32'bz;  // Controlled_Buffer controlled_buffer_8
  assign \根据IF判断的NPC  = RST3 ? multiplexer_28_out : 32'bz;  // Controlled_Buffer controlled_buffer_9
  assign \根据IF判断的NPC  = RST4 ? multiplexer_29_out : 32'bz;  // Controlled_Buffer controlled_buffer_10
  assign \根据IF判断的NPC  = RST5 ? multiplexer_30_out : 32'bz;  // Controlled_Buffer controlled_buffer_11
  assign \根据IF判断的NPC  = RST6 ? multiplexer_31_out : 32'bz;  // Controlled_Buffer controlled_buffer_12
  assign \根据IF判断的NPC  = RST7 ? multiplexer_32_out : 32'bz;  // Controlled_Buffer controlled_buffer_13
  assign \根据IF判断的NPC  = RST8 ? multiplexer_33_out : 32'bz;  // Controlled_Buffer controlled_buffer_14
  assign \根据IF判断的NPC  = IF_MISS ? IF_PC_4 : 32'bz;  // Controlled_Buffer controlled_buffer_15
  Multiplexer #(.select(1), .width(32), .disabled("Z"), .enable("false")) multiplexer_34 (
    .in0(\根据IF判断的NPC ), .in1(\正常指令地址 ), .out(multiplexer_34_out), .sel(\要跳不跳 ));
  Multiplexer #(.select(1), .width(32), .disabled("Z"), .enable("false")) multiplexer_35 (
    .in0(multiplexer_34_out), .in1(EX_PC_4), .out(NPC), .sel(\不要跳却跳 ));

  // Other names for the same wires on the sheet: tunnel = in_8; 需要跳转 = \分支成功 

  // Notes on the sheet:
  //   Valid
  //   转跳指令PC
  //   目标地址PC
  //   预测历史
  //   LRU
  //   IF.EX命中则RST为1
endmodule

module \预测历史FSM  (
  input  [1:0] \前序状态 ,
  input  \分支成功 ,
  input  EN,
  output [1:0] \更新状态 
);

  wire comparator_1_eq, comparator_2_eq, comparator_3_eq, comparator_4_eq;
  wire [1:0] controlled_buffer_1_out, multiplexer_1_out, multiplexer_2_out, multiplexer_3_out,
       multiplexer_4_out;

  Multiplexer #(.select(1), .width(2), .disabled("Z"), .enable("false")) multiplexer_1 (
    .in0(2'b00), .in1(2'b01), .out(multiplexer_1_out), .sel(\分支成功 ));
  Multiplexer #(.select(1), .width(2), .disabled("Z"), .enable("false")) multiplexer_2 (
    .in0(2'b00), .in1(2'b10), .out(multiplexer_2_out), .sel(\分支成功 ));
  Multiplexer #(.select(1), .width(2), .disabled("Z"), .enable("false")) multiplexer_3 (
    .in0(2'b11), .in1(2'b10), .out(multiplexer_3_out), .sel(\分支成功 ));
  Multiplexer #(.select(1), .width(2), .disabled("Z"), .enable("false")) multiplexer_4 (
    .in0(2'b00), .in1(2'b10), .out(multiplexer_4_out), .sel(\分支成功 ));
  Comparator #(.width(2), .mode("unsigned")) comparator_1 (
    .a(\前序状态 ), .b(2'b00), .eq(comparator_1_eq));  // open: gt, lt
  assign controlled_buffer_1_out = comparator_1_eq ? multiplexer_1_out : 2'bz;  // Controlled_Buffer controlled_buffer_1
  Comparator #(.width(2), .mode("unsigned")) comparator_2 (
    .a(\前序状态 ), .b(2'b01), .eq(comparator_2_eq));  // open: gt, lt
  assign controlled_buffer_1_out = comparator_2_eq ? multiplexer_2_out : 2'bz;  // Controlled_Buffer controlled_buffer_2
  Comparator #(.width(2), .mode("unsigned")) comparator_3 (
    .a(\前序状态 ), .b(2'b10), .eq(comparator_3_eq));  // open: gt, lt
  assign controlled_buffer_1_out = comparator_3_eq ? multiplexer_3_out : 2'bz;  // Controlled_Buffer controlled_buffer_3
  Comparator #(.width(2), .mode("unsigned")) comparator_4 (
    .a(\前序状态 ), .b(2'b11), .eq(comparator_4_eq));  // open: gt, lt
  assign controlled_buffer_1_out = comparator_4_eq ? multiplexer_4_out : 2'bz;  // Controlled_Buffer controlled_buffer_4
  Multiplexer #(.select(1), .width(2), .disabled("Z"), .enable("false")) multiplexer_5 (
    .in0(controlled_buffer_1_out), .in1(2'b11), .out(\更新状态 ), .sel(EN));
endmodule

module \J型指令转跳地址判断器  (
  input  BNE,
  input  in_2,
  input  BEQ,
  input  JR,
  input  JMP,
  input  JAL,
  input  BLTZ,
  input  [31:0] PC_4,
  input  [31:0] BNE_BEQ_BLTZaddr,
  input  [31:0] J_JALaddr,
  input  [31:0] JRaddr,
  output [31:0] out_12,
  output \转跳信号灯 
);

  wire and_1_out, BLTZ_out, EQJMP_out, J_out, JAL_out, JR_out, NEEQ_out, NEJMP_out, or_1_out;

  and NEJMP (NEJMP_out, BNE, ~in_2);  // AND_Gate
  or or_1 (or_1_out, NEJMP_out, EQJMP_out);
  and EQJMP (EQJMP_out, in_2, BEQ);
  and u_JR (JR_out, JR, JMP, ~JAL, ~NEJMP_out, ~EQJMP_out, ~BLTZ);  // AND_Gate
  and J (J_out, ~JR, JMP, ~JAL, ~NEJMP_out, ~EQJMP_out, ~BLTZ);  // AND_Gate
  and u_JAL (JAL_out, ~JR, JMP, JAL, ~NEJMP_out, ~EQJMP_out, ~BLTZ);  // AND_Gate
  and u_BLTZ (BLTZ_out, ~JR, ~JMP, ~JAL, ~NEJMP_out, ~EQJMP_out, BLTZ);  // AND_Gate
  and NEEQ (NEEQ_out, ~JR, ~JMP, ~JAL, or_1_out, ~BLTZ);  // AND_Gate
  and and_1 (and_1_out, ~NEEQ_out, ~BLTZ_out, ~JAL_out, ~J_out, ~JR_out);  // AND_Gate
  not not_1 (\转跳信号灯 , and_1_out);
  assign out_12 = and_1_out ? PC_4 : 32'bz;  // Controlled_Buffer controlled_buffer_1
  assign out_12 = BLTZ_out ? BNE_BEQ_BLTZaddr : 32'bz;  // Controlled_Buffer controlled_buffer_2
  assign out_12 = NEEQ_out ? BNE_BEQ_BLTZaddr : 32'bz;  // Controlled_Buffer controlled_buffer_3
  assign out_12 = J_out ? J_JALaddr : 32'bz;  // Controlled_Buffer controlled_buffer_4
  assign out_12 = JAL_out ? J_JALaddr : 32'bz;  // Controlled_Buffer controlled_buffer_5
  assign out_12 = JR_out ? JRaddr : 32'bz;  // Controlled_Buffer controlled_buffer_6

  // Notes on the sheet:
  //   $31---> PC
  //   JR指令跳转逻辑：同时出现JR控制信号和JMP控制信号
  //   J指令跳转逻辑：出现JMP控制信号
  //   JAL指令跳转逻辑：同时出现JMP控制信号和JAL信号
  //   BLTZ指令跳转逻辑：rs < 0时
  //   BEQ和BNE指令跳转逻辑：NEEQ
  //   其余时刻：PC+4
  //   指令0~25逻辑左移两位，高位为当前PC高四位 --->下一个CLK的PC
  //   将PC+4 ---> $31， 指令0~25逻辑左移两位，高位为当前PC高四位 --->下一个CLK的PC
endmodule

module \理想流水IF_ID  (
  input  Reset,
  input  EN,
  input  CLK,
  input  [31:0] PC_4,
  input  [31:0] IR,
  input  [31:0] Jaddr,
  output [31:0] PC_4_2,
  output [31:0] IR_2,
  output [31:0] Jaddr_2
);

  wire [31:0] multiplexer_1_out, multiplexer_2_out, multiplexer_3_out;

  Multiplexer #(.select(1), .width(32), .disabled("Z"), .enable("false")) multiplexer_1 (
    .in0(PC_4), .in1({32{1'b0}}), .out(multiplexer_1_out), .sel(Reset));
  Multiplexer #(.select(1), .width(32), .disabled("Z"), .enable("false")) multiplexer_2 (
    .in0(IR), .in1({32{1'b0}}), .out(multiplexer_2_out), .sel(Reset));
  Multiplexer #(.select(1), .width(32), .disabled("Z"), .enable("false")) multiplexer_3 (
    .in0(Jaddr), .in1({32{1'b0}}), .out(multiplexer_3_out), .sel(Reset));
  Register #(.width(32), .trigger("rising"), .Select("low")) register_1 (
    .D(multiplexer_1_out), .en(EN), .Q(PC_4_2), .clk(CLK));  // open: clr
  Register #(.width(32), .trigger("rising"), .Select("low")) register_2 (
    .D(multiplexer_2_out), .en(EN), .Q(IR_2), .clk(CLK));  // open: clr
  Register #(.width(32), .trigger("rising"), .Select("low")) register_3 (
    .D(multiplexer_3_out), .en(EN), .Q(Jaddr_2), .clk(CLK));  // open: clr
endmodule
module \理想流水ID_EX  (
  input  RST,
  input  EN,
  input  CLK,
  input  BEQ,
  input  BNE,
  input  MenToReg,
  input  MemWrite,
  input  [3:0] AluOP,
  input  AluSrcB,
  input  RegWrite,
  input  Syscall,
  input  [31:0] R1,
  input  [31:0] R2,
  input  [4:0] W,
  input  [31:0] PC_4,
  input  [31:0] Imm,
  input  [31:0] Jaddr,
  output BEQ_2,
  output BNE_2,
  output MenToReg_2,
  output MenWrite,
  output [3:0] AluOP_2,
  output AluSrcB_2,
  output RegWrite_2,
  output Syscall_2,
  output [31:0] R1_2,
  output [31:0] R2_2,
  output [4:0] W_2,
  output [31:0] PC_4_2,
  output [31:0] Imm_2,
  output [31:0] Jaddr_2
);

  wire multiplexer_1_out, multiplexer_2_out, multiplexer_3_out, multiplexer_4_out, multiplexer_6_out,
       multiplexer_7_out, multiplexer_8_out;
  wire [3:0] multiplexer_5_out;
  wire [4:0] multiplexer_11_out;
  wire [31:0] multiplexer_9_out, multiplexer_10_out, multiplexer_12_out, multiplexer_13_out,
       multiplexer_14_out;

  Multiplexer #(.select(1), .width(1), .disabled("Z"), .enable("false")) multiplexer_1 (
    .in0(BEQ), .in1(1'b0), .out(multiplexer_1_out), .sel(RST));
  Multiplexer #(.select(1), .width(1), .disabled("Z"), .enable("false")) multiplexer_2 (
    .in0(BNE), .in1(1'b0), .out(multiplexer_2_out), .sel(RST));
  Multiplexer #(.select(1), .width(1), .disabled("Z"), .enable("false")) multiplexer_3 (
    .in0(MenToReg), .in1(1'b0), .out(multiplexer_3_out), .sel(RST));
  Multiplexer #(.select(1), .width(1), .disabled("Z"), .enable("false")) multiplexer_4 (
    .in0(MemWrite), .in1(1'b0), .out(multiplexer_4_out), .sel(RST));
  Multiplexer #(.select(1), .width(4), .disabled("Z"), .enable("false")) multiplexer_5 (
    .in0(AluOP), .in1(4'b0000), .out(multiplexer_5_out), .sel(RST));
  Multiplexer #(.select(1), .width(1), .disabled("Z"), .enable("false")) multiplexer_6 (
    .in0(AluSrcB), .in1(1'b0), .out(multiplexer_6_out), .sel(RST));
  Multiplexer #(.select(1), .width(1), .disabled("Z"), .enable("false")) multiplexer_7 (
    .in0(RegWrite), .in1(1'b0), .out(multiplexer_7_out), .sel(RST));
  Multiplexer #(.select(1), .width(1), .disabled("Z"), .enable("false")) multiplexer_8 (
    .in0(Syscall), .in1(1'b0), .out(multiplexer_8_out), .sel(RST));
  Multiplexer #(.select(1), .width(32), .disabled("Z"), .enable("false")) multiplexer_9 (
    .in0(R1), .in1({32{1'b0}}), .out(multiplexer_9_out), .sel(RST));
  Multiplexer #(.select(1), .width(32), .disabled("Z"), .enable("false")) multiplexer_10 (
    .in0(R2), .in1({32{1'b0}}), .out(multiplexer_10_out), .sel(RST));
  Multiplexer #(.select(1), .width(5), .disabled("Z"), .enable("false")) multiplexer_11 (
    .in0(W), .in1({5{1'b0}}), .out(multiplexer_11_out), .sel(RST));
  Multiplexer #(.select(1), .width(32), .disabled("Z"), .enable("false")) multiplexer_12 (
    .in0(PC_4), .in1({32{1'b0}}), .out(multiplexer_12_out), .sel(RST));
  Multiplexer #(.select(1), .width(32), .disabled("Z"), .enable("false")) multiplexer_13 (
    .in0(Imm), .in1({32{1'b0}}), .out(multiplexer_13_out), .sel(RST));
  Multiplexer #(.select(1), .width(32), .disabled("Z"), .enable("false")) multiplexer_14 (
    .in0(Jaddr), .in1({32{1'b0}}), .out(multiplexer_14_out), .sel(RST));
  Register #(.width(1), .trigger("rising"), .Select("low")) register_1 (
    .D(multiplexer_1_out), .en(EN), .Q(BEQ_2), .clk(CLK));  // open: clr
  Register #(.width(1), .trigger("rising"), .Select("low")) register_2 (
    .D(multiplexer_2_out), .en(EN), .Q(BNE_2), .clk(CLK));  // open: clr
  Register #(.width(1), .trigger("rising"), .Select("low")) register_3 (
    .D(multiplexer_3_out), .en(EN), .Q(MenToReg_2), .clk(CLK));  // open: clr
  Register #(.width(1), .trigger("rising"), .Select("low")) register_4 (
    .D(multiplexer_4_out), .en(EN), .Q(MenWrite), .clk(CLK));  // open: clr
  Register #(.width(4), .trigger("rising"), .Select("low")) register_5 (
    .D(multiplexer_5_out), .en(EN), .Q(AluOP_2), .clk(CLK));  // open: clr
  Register #(.width(1), .trigger("rising"), .Select("low")) register_6 (
    .D(multiplexer_6_out), .en(EN), .Q(AluSrcB_2), .clk(CLK));  // open: clr
  Register #(.width(1), .trigger("rising"), .Select("low")) register_7 (
    .D(multiplexer_7_out), .en(EN), .Q(RegWrite_2), .clk(CLK));  // open: clr
  Register #(.width(1), .trigger("rising"), .Select("low")) register_8 (
    .D(multiplexer_8_out), .en(EN), .Q(Syscall_2), .clk(CLK));  // open: clr
  Register #(.width(32), .trigger("rising"), .Select("low")) register_9 (
    .D(multiplexer_9_out), .en(EN), .Q(R1_2), .clk(CLK));  // open: clr
  Register #(.width(32), .trigger("rising"), .Select("low")) register_10 (
    .D(multiplexer_10_out), .en(EN), .Q(R2_2), .clk(CLK));  // open: clr
  Register #(.width(5), .trigger("rising"), .Select("low")) register_11 (
    .D(multiplexer_11_out), .en(EN), .Q(W_2), .clk(CLK));  // open: clr
  Register #(.width(32), .trigger("rising"), .Select("low")) register_12 (
    .D(multiplexer_12_out), .en(EN), .Q(PC_4_2), .clk(CLK));  // open: clr
  Register #(.width(32), .trigger("rising"), .Select("low")) register_13 (
    .D(multiplexer_13_out), .en(EN), .Q(Imm_2), .clk(CLK));  // open: clr
  Register #(.width(32), .trigger("rising"), .Select("low")) register_14 (
    .D(multiplexer_14_out), .en(EN), .Q(Jaddr_2), .clk(CLK));  // open: clr
endmodule

module \理想流水EX_MEM  (
  input  RST,
  input  EN,
  input  CLK,
  input  MenToReg,
  input  MemWrite,
  input  RegWrite,
  input  Syscall,
  input  [31:0] R,
  input  [31:0] R2,
  input  [4:0] W,
  input  [31:0] PC,
  output MenToReg_2,
  output MenWrite,
  output RegWrite_2,
  output Syscall_2,
  output [31:0] R_2,
  output [31:0] R2_2,
  output [4:0] W_2,
  output [31:0] PC_2
);

  wire multiplexer_1_out, multiplexer_2_out, multiplexer_3_out, multiplexer_4_out;
  wire [4:0] multiplexer_7_out;
  wire [31:0] multiplexer_5_out, multiplexer_6_out, multiplexer_8_out;

  Multiplexer #(.select(1), .width(1), .disabled("Z"), .enable("false")) multiplexer_1 (
    .in0(MenToReg), .in1(1'b0), .out(multiplexer_1_out), .sel(RST));
  Multiplexer #(.select(1), .width(1), .disabled("Z"), .enable("false")) multiplexer_2 (
    .in0(MemWrite), .in1(1'b0), .out(multiplexer_2_out), .sel(RST));
  Multiplexer #(.select(1), .width(1), .disabled("Z"), .enable("false")) multiplexer_3 (
    .in0(RegWrite), .in1(1'b0), .out(multiplexer_3_out), .sel(RST));
  Multiplexer #(.select(1), .width(1), .disabled("Z"), .enable("false")) multiplexer_4 (
    .in0(Syscall), .in1(1'b0), .out(multiplexer_4_out), .sel(RST));
  Multiplexer #(.select(1), .width(32), .disabled("Z"), .enable("false")) multiplexer_5 (
    .in0(R), .in1({32{1'b0}}), .out(multiplexer_5_out), .sel(RST));
  Multiplexer #(.select(1), .width(32), .disabled("Z"), .enable("false")) multiplexer_6 (
    .in0(R2), .in1({32{1'b0}}), .out(multiplexer_6_out), .sel(RST));
  Multiplexer #(.select(1), .width(5), .disabled("Z"), .enable("false")) multiplexer_7 (
    .in0(W), .in1({5{1'b0}}), .out(multiplexer_7_out), .sel(RST));
  Multiplexer #(.select(1), .width(32), .disabled("Z"), .enable("false")) multiplexer_8 (
    .in0(PC), .in1({32{1'b0}}), .out(multiplexer_8_out), .sel(RST));
  Register #(.width(1), .trigger("rising"), .Select("low")) register_1 (
    .D(multiplexer_1_out), .en(EN), .Q(MenToReg_2), .clk(CLK));  // open: clr
  Register #(.width(1), .trigger("rising"), .Select("low")) register_2 (
    .D(multiplexer_2_out), .en(EN), .Q(MenWrite), .clk(CLK));  // open: clr
  Register #(.width(1), .trigger("rising"), .Select("low")) register_3 (
    .D(multiplexer_3_out), .en(EN), .Q(RegWrite_2), .clk(CLK));  // open: clr
  Register #(.width(1), .trigger("rising"), .Select("low")) register_4 (
    .D(multiplexer_4_out), .en(EN), .Q(Syscall_2), .clk(CLK));  // open: clr
  Register #(.width(32), .trigger("rising"), .Select("low")) register_5 (
    .D(multiplexer_5_out), .en(EN), .Q(R_2), .clk(CLK));  // open: clr
  Register #(.width(32), .trigger("rising"), .Select("low")) register_6 (
    .D(multiplexer_6_out), .en(EN), .Q(R2_2), .clk(CLK));  // open: clr
  Register #(.width(5), .trigger("rising"), .Select("low")) register_7 (
    .D(multiplexer_7_out), .en(EN), .Q(W_2), .clk(CLK));  // open: clr
  Register #(.width(32), .trigger("rising"), .Select("low")) register_8 (
    .D(multiplexer_8_out), .en(EN), .Q(PC_2), .clk(CLK));  // open: clr
endmodule

module \理想流水MEM_WB  (
  input  RST,
  input  EN,
  input  CLK,
  input  MenToReg,
  input  RegWrite,
  input  Syscall,
  input  [31:0] ALU_Data,
  input  [31:0] MEM_ReadData,
  input  [4:0] W,
  input  [31:0] PC,
  output MenToReg_2,
  output RegWrite_2,
  output Syscall_2,
  output [31:0] ALU_Data_2,
  output [31:0] MEM_ReadData_2,
  output [4:0] W_2,
  output [31:0] PC_2
);

  wire multiplexer_1_out, multiplexer_2_out, multiplexer_3_out;
  wire [4:0] multiplexer_6_out;
  wire [31:0] multiplexer_4_out, multiplexer_5_out, multiplexer_7_out;

  Multiplexer #(.select(1), .width(1), .disabled("Z"), .enable("false")) multiplexer_1 (
    .in0(MenToReg), .in1(1'b0), .out(multiplexer_1_out), .sel(RST));
  Multiplexer #(.select(1), .width(1), .disabled("Z"), .enable("false")) multiplexer_2 (
    .in0(RegWrite), .in1(1'b0), .out(multiplexer_2_out), .sel(RST));
  Multiplexer #(.select(1), .width(1), .disabled("Z"), .enable("false")) multiplexer_3 (
    .in0(Syscall), .in1(1'b0), .out(multiplexer_3_out), .sel(RST));
  Multiplexer #(.select(1), .width(32), .disabled("Z"), .enable("false")) multiplexer_4 (
    .in0(ALU_Data), .in1({32{1'b0}}), .out(multiplexer_4_out), .sel(RST));
  Multiplexer #(.select(1), .width(32), .disabled("Z"), .enable("false")) multiplexer_5 (
    .in0(MEM_ReadData), .in1({32{1'b0}}), .out(multiplexer_5_out), .sel(RST));
  Multiplexer #(.select(1), .width(5), .disabled("Z"), .enable("false")) multiplexer_6 (
    .in0(W), .in1({5{1'b0}}), .out(multiplexer_6_out), .sel(RST));
  Multiplexer #(.select(1), .width(32), .disabled("Z"), .enable("false")) multiplexer_7 (
    .in0(PC), .in1({32{1'b0}}), .out(multiplexer_7_out), .sel(RST));
  Register #(.width(1), .trigger("rising"), .Select("low")) register_1 (
    .D(multiplexer_1_out), .en(EN), .Q(MenToReg_2), .clk(CLK));  // open: clr
  Register #(.width(1), .trigger("rising"), .Select("low")) register_2 (
    .D(multiplexer_2_out), .en(EN), .Q(RegWrite_2), .clk(CLK));  // open: clr
  Register #(.width(1), .trigger("rising"), .Select("low")) register_3 (
    .D(multiplexer_3_out), .en(EN), .Q(Syscall_2), .clk(CLK));  // open: clr
  Register #(.width(32), .trigger("rising"), .Select("low")) register_4 (
    .D(multiplexer_4_out), .en(EN), .Q(ALU_Data_2), .clk(CLK));  // open: clr
  Register #(.width(32), .trigger("rising"), .Select("low")) register_5 (
    .D(multiplexer_5_out), .en(EN), .Q(MEM_ReadData_2), .clk(CLK));  // open: clr
  Register #(.width(5), .trigger("rising"), .Select("low")) register_6 (
    .D(multiplexer_6_out), .en(EN), .Q(W_2), .clk(CLK));  // open: clr
  Register #(.width(32), .trigger("rising"), .Select("low")) register_7 (
    .D(multiplexer_7_out), .en(EN), .Q(PC_2), .clk(CLK));  // open: clr
endmodule

// IF/ID
module IF_ID (
  input  Reset,
  input  EN,
  input  CLK,
  input  [31:0] IR,
  input  [31:0] Jaddr,
  input  [31:0] PC_4,
  input  [31:0] PC,
  output [31:0] IR_2,
  output [31:0] Jaddr_2,
  output [31:0] PC_4_2,
  output [31:0] PC_2
);

  wire [31:0] multiplexer_1_out, multiplexer_2_out, multiplexer_3_out, multiplexer_4_out;

  Pull_Resistor #(.pull(0)) pull_resistor_1 (.node(Reset));
  Multiplexer #(.select(1), .width(32), .disabled("Z"), .enable("false")) multiplexer_1 (
    .in0(IR), .in1({32{1'b0}}), .out(multiplexer_1_out), .sel(Reset));
  Multiplexer #(.select(1), .width(32), .disabled("Z"), .enable("false")) multiplexer_2 (
    .in0(Jaddr), .in1({32{1'b0}}), .out(multiplexer_2_out), .sel(Reset));
  Multiplexer #(.select(1), .width(32), .disabled("Z"), .enable("false")) multiplexer_3 (
    .in0(PC_4), .in1({32{1'b0}}), .out(multiplexer_3_out), .sel(Reset));
  Multiplexer #(.select(1), .width(32), .disabled("Z"), .enable("false")) multiplexer_4 (
    .in0(PC), .in1({32{1'b0}}), .out(multiplexer_4_out), .sel(Reset));
  Pull_Resistor #(.pull(0)) pull_resistor_2 (.node(EN));
  Register #(.width(32), .trigger("rising"), .Select("low")) register_1 (
    .D(multiplexer_1_out), .en(EN), .Q(IR_2), .clk(CLK));  // open: clr
  Register #(.width(32), .trigger("rising"), .Select("low")) register_2 (
    .D(multiplexer_2_out), .en(EN), .Q(Jaddr_2), .clk(CLK));  // open: clr
  Register #(.width(32), .trigger("rising"), .Select("low")) register_3 (
    .D(multiplexer_3_out), .en(EN), .Q(PC_4_2), .clk(CLK));  // open: clr
  Register #(.width(32), .trigger("rising"), .Select("low")) register_4 (
    .D(multiplexer_4_out), .en(EN), .Q(PC_2), .clk(CLK));  // open: clr
endmodule

module ID_EX (
  input  RST,
  input  EN,
  input  CLK,
  input  ERET,
  input  LB,
  input  SysCall,
  input  RegWrite,
  input  JAL,
  input  MenToReg,
  input  MenWrite,
  input  LUI,
  input  BLTZ,
  input  Beq,
  input  Bne,
  input  JMP,
  input  JR,
  input  [3:0] AluOP,
  input  AluSrcB,
  input  [31:0] R1,
  input  [31:0] R2,
  input  [4:0] W,
  input  [4:0] shamt,
  input  [31:0] Imm,
  input  [31:0] Jaddr,
  input  [31:0] PC_4,
  input  [31:0] PC,
  output ERET_2,
  output LB_2,
  output SysCall_2,
  output RegWrite_2,
  output JAL_2,
  output MenToReg_2,
  output MenWrite_2,
  output LUI_2,
  output BLTZ_2,
  output Beq_2,
  output Bne_2,
  output JMP_2,
  output JR_2,
  output [3:0] AluOP_2,
  output AluSrcB_2,
  output [31:0] R1_2,
  output [31:0] R2_2,
  output [4:0] W_2,
  output [4:0] shamt_2,
  output [31:0] Imm_2,
  output [31:0] Jaddr_2,
  output [31:0] PC_4_2,
  output [31:0] PC_2
);

  wire multiplexer_1_out, multiplexer_2_out, multiplexer_3_out, multiplexer_4_out, multiplexer_5_out,
       multiplexer_6_out, multiplexer_7_out, multiplexer_8_out, multiplexer_9_out, multiplexer_10_out,
       multiplexer_11_out, multiplexer_12_out, multiplexer_13_out, multiplexer_15_out;
  wire [3:0] multiplexer_14_out;
  wire [4:0] multiplexer_18_out, multiplexer_19_out;
  wire [31:0] multiplexer_16_out, multiplexer_17_out, multiplexer_20_out, multiplexer_21_out,
       multiplexer_22_out, multiplexer_23_out;

  Pull_Resistor #(.pull(0)) pull_resistor_1 (.node(RST));
  Multiplexer #(.select(1), .width(1), .disabled("Z"), .enable("false")) multiplexer_1 (
    .in0(ERET), .in1(1'b0), .out(multiplexer_1_out), .sel(RST));
  Multiplexer #(.select(1), .width(1), .disabled("Z"), .enable("false")) multiplexer_2 (
    .in0(LB), .in1(1'b0), .out(multiplexer_2_out), .sel(RST));
  Multiplexer #(.select(1), .width(1), .disabled("Z"), .enable("false")) multiplexer_3 (
    .in0(SysCall), .in1(1'b0), .out(multiplexer_3_out), .sel(RST));
  Multiplexer #(.select(1), .width(1), .disabled("Z"), .enable("false")) multiplexer_4 (
    .in0(RegWrite), .in1(1'b0), .out(multiplexer_4_out), .sel(RST));
  Multiplexer #(.select(1), .width(1), .disabled("Z"), .enable("false")) multiplexer_5 (
    .in0(JAL), .in1(1'b0), .out(multiplexer_5_out), .sel(RST));
  Multiplexer #(.select(1), .width(1), .disabled("Z"), .enable("false")) multiplexer_6 (
    .in0(MenToReg), .in1(1'b0), .out(multiplexer_6_out), .sel(RST));
  Multiplexer #(.select(1), .width(1), .disabled("Z"), .enable("false")) multiplexer_7 (
    .in0(MenWrite), .in1(1'b0), .out(multiplexer_7_out), .sel(RST));
  Multiplexer #(.select(1), .width(1), .disabled("Z"), .enable("false")) multiplexer_8 (
    .in0(LUI), .in1(1'b0), .out(multiplexer_8_out), .sel(RST));
  Multiplexer #(.select(1), .width(1), .disabled("Z"), .enable("false")) multiplexer_9 (
    .in0(BLTZ), .in1(1'b0), .out(multiplexer_9_out), .sel(RST));
  Multiplexer #(.select(1), .width(1), .disabled("Z"), .enable("false")) multiplexer_10 (
    .in0(Beq), .in1(1'b0), .out(multiplexer_10_out), .sel(RST));
  Multiplexer #(.select(1), .width(1), .disabled("Z"), .enable("false")) multiplexer_11 (
    .in0(Bne), .in1(1'b0), .out(multiplexer_11_out), .sel(RST));
  Multiplexer #(.select(1), .width(1), .disabled("Z"), .enable("false")) multiplexer_12 (
    .in0(JMP), .in1(1'b0), .out(multiplexer_12_out), .sel(RST));
  Multiplexer #(.select(1), .width(1), .disabled("Z"), .enable("false")) multiplexer_13 (
    .in0(JR), .in1(1'b0), .out(multiplexer_13_out), .sel(RST));
  Multiplexer #(.select(1), .width(4), .disabled("Z"), .enable("false")) multiplexer_14 (
    .in0(AluOP), .in1(4'b0000), .out(multiplexer_14_out), .sel(RST));
  Multiplexer #(.select(1), .width(1), .disabled("Z"), .enable("false")) multiplexer_15 (
    .in0(AluSrcB), .in1(1'b0), .out(multiplexer_15_out), .sel(RST));
  Multiplexer #(.select(1), .width(32), .disabled("Z"), .enable("false")) multiplexer_16 (
    .in0(R1), .in1({32{1'b0}}), .out(multiplexer_16_out), .sel(RST));
  Multiplexer #(.select(1), .width(32), .disabled("Z"), .enable("false")) multiplexer_17 (
    .in0(R2), .in1({32{1'b0}}), .out(multiplexer_17_out), .sel(RST));
  Multiplexer #(.select(1), .width(5), .disabled("Z"), .enable("false")) multiplexer_18 (
    .in0(W), .in1({5{1'b0}}), .out(multiplexer_18_out), .sel(RST));
  Multiplexer #(.select(1), .width(5), .disabled("Z"), .enable("false")) multiplexer_19 (
    .in0(shamt), .in1({5{1'b0}}), .out(multiplexer_19_out), .sel(RST));
  Multiplexer #(.select(1), .width(32), .disabled("Z"), .enable("false")) multiplexer_20 (
    .in0(Imm), .in1({32{1'b0}}), .out(multiplexer_20_out), .sel(RST));
  Multiplexer #(.select(1), .width(32), .disabled("Z"), .enable("false")) multiplexer_21 (
    .in0(Jaddr), .in1({32{1'b0}}), .out(multiplexer_21_out), .sel(RST));
  Multiplexer #(.select(1), .width(32), .disabled("Z"), .enable("false")) multiplexer_22 (
    .in0(PC_4), .in1({32{1'b0}}), .out(multiplexer_22_out), .sel(RST));
  Multiplexer #(.select(1), .width(32), .disabled("Z"), .enable("false")) multiplexer_23 (
    .in0(PC), .in1({32{1'b0}}), .out(multiplexer_23_out), .sel(RST));
  Pull_Resistor #(.pull(0)) pull_resistor_2 (.node(EN));
  Register #(.width(1), .trigger("rising"), .Select("low")) register_1 (
    .D(multiplexer_1_out), .en(EN), .Q(ERET_2), .clk(CLK));  // open: clr
  Register #(.width(1), .trigger("rising"), .Select("low")) register_2 (
    .D(multiplexer_2_out), .en(EN), .Q(LB_2), .clk(CLK));  // open: clr
  Register #(.width(1), .trigger("rising"), .Select("low")) register_3 (
    .D(multiplexer_3_out), .en(EN), .Q(SysCall_2), .clk(CLK));  // open: clr
  Register #(.width(1), .trigger("rising"), .Select("low")) register_4 (
    .D(multiplexer_4_out), .en(EN), .Q(RegWrite_2), .clk(CLK));  // open: clr
  Register #(.width(1), .trigger("rising"), .Select("low")) register_5 (
    .D(multiplexer_5_out), .en(EN), .Q(JAL_2), .clk(CLK));  // open: clr
  Register #(.width(1), .trigger("rising"), .Select("low")) register_6 (
    .D(multiplexer_6_out), .en(EN), .Q(MenToReg_2), .clk(CLK));  // open: clr
  Register #(.width(1), .trigger("rising"), .Select("low")) register_7 (
    .D(multiplexer_7_out), .en(EN), .Q(MenWrite_2), .clk(CLK));  // open: clr
  Register #(.width(1), .trigger("rising"), .Select("low")) register_8 (
    .D(multiplexer_8_out), .en(EN), .Q(LUI_2), .clk(CLK));  // open: clr
  Register #(.width(1), .trigger("rising"), .Select("low")) register_9 (
    .D(multiplexer_9_out), .en(EN), .Q(BLTZ_2), .clk(CLK));  // open: clr
  Register #(.width(1), .trigger("rising"), .Select("low")) register_10 (
    .D(multiplexer_10_out), .en(EN), .Q(Beq_2), .clk(CLK));  // open: clr
  Register #(.width(1), .trigger("rising"), .Select("low")) register_11 (
    .D(multiplexer_11_out), .en(EN), .Q(Bne_2), .clk(CLK));  // open: clr
  Register #(.width(1), .trigger("rising"), .Select("low")) register_12 (
    .D(multiplexer_12_out), .en(EN), .Q(JMP_2), .clk(CLK));  // open: clr
  Register #(.width(1), .trigger("rising"), .Select("low")) register_13 (
    .D(multiplexer_13_out), .en(EN), .Q(JR_2), .clk(CLK));  // open: clr
  Register #(.width(4), .trigger("rising"), .Select("low")) register_14 (
    .D(multiplexer_14_out), .en(EN), .Q(AluOP_2), .clk(CLK));  // open: clr
  Register #(.width(1), .trigger("rising"), .Select("low")) register_15 (
    .D(multiplexer_15_out), .en(EN), .Q(AluSrcB_2), .clk(CLK));  // open: clr
  Register #(.width(32), .trigger("rising"), .Select("low")) register_16 (
    .D(multiplexer_16_out), .en(EN), .Q(R1_2), .clk(CLK));  // open: clr
  Register #(.width(32), .trigger("rising"), .Select("low")) register_17 (
    .D(multiplexer_17_out), .en(EN), .Q(R2_2), .clk(CLK));  // open: clr
  Register #(.width(5), .trigger("rising"), .Select("low")) register_18 (
    .D(multiplexer_18_out), .en(EN), .Q(W_2), .clk(CLK));  // open: clr
  Register #(.width(5), .trigger("rising"), .Select("low")) register_19 (
    .D(multiplexer_19_out), .en(EN), .Q(shamt_2), .clk(CLK));  // open: clr
  Register #(.width(32), .trigger("rising"), .Select("low")) register_20 (
    .D(multiplexer_20_out), .en(EN), .Q(Imm_2), .clk(CLK));  // open: clr
  Register #(.width(32), .trigger("rising"), .Select("low")) register_21 (
    .D(multiplexer_21_out), .en(EN), .Q(Jaddr_2), .clk(CLK));  // open: clr
  Register #(.width(32), .trigger("rising"), .Select("low")) register_22 (
    .D(multiplexer_22_out), .en(EN), .Q(PC_4_2), .clk(CLK));  // open: clr
  Register #(.width(32), .trigger("rising"), .Select("low")) register_23 (
    .D(multiplexer_23_out), .en(EN), .Q(PC_2), .clk(CLK));  // open: clr
endmodule

module EX_MEM (
  input  RST,
  input  EN,
  input  CLK,
  input  ERET,
  input  LB,
  input  SysCall,
  input  RegWrite,
  input  JAL,
  input  MenToReg,
  input  MenWrite,
  input  [31:0] R1,
  input  [31:0] R,
  input  [31:0] R2,
  input  [4:0] W,
  input  [31:0] PC_4,
  input  [31:0] PC,
  output ERET_2,
  output LB_2,
  output SysCall_2,
  output RegWrite_2,
  output JAL_2,
  output MenToReg_2,
  output MenWrite_2,
  output [31:0] R1_2,
  output [31:0] R_2,
  output [31:0] R2_2,
  output [4:0] W_2,
  output [31:0] R2_3,
  output [31:0] PC_4_2,
  output [31:0] PC_2
);

  wire multiplexer_1_out, multiplexer_2_out, multiplexer_3_out, multiplexer_4_out, multiplexer_5_out,
       multiplexer_6_out, multiplexer_7_out;
  wire [4:0] multiplexer_11_out;
  wire [31:0] multiplexer_8_out, multiplexer_9_out, multiplexer_10_out, multiplexer_12_out,
       multiplexer_13_out;

  Pull_Resistor #(.pull(0)) pull_resistor_1 (.node(EN));
  Pull_Resistor #(.pull(0)) pull_resistor_2 (.node(RST));
  Multiplexer #(.select(1), .width(1), .disabled("Z"), .enable("false")) multiplexer_1 (
    .in0(ERET), .in1(1'b0), .out(multiplexer_1_out), .sel(RST));
  Multiplexer #(.select(1), .width(1), .disabled("Z"), .enable("false")) multiplexer_2 (
    .in0(LB), .in1(1'b0), .out(multiplexer_2_out), .sel(RST));
  Multiplexer #(.select(1), .width(1), .disabled("Z"), .enable("false")) multiplexer_3 (
    .in0(SysCall), .in1(1'b0), .out(multiplexer_3_out), .sel(RST));
  Multiplexer #(.select(1), .width(1), .disabled("Z"), .enable("false")) multiplexer_4 (
    .in0(RegWrite), .in1(1'b0), .out(multiplexer_4_out), .sel(RST));
  Multiplexer #(.select(1), .width(1), .disabled("Z"), .enable("false")) multiplexer_5 (
    .in0(JAL), .in1(1'b0), .out(multiplexer_5_out), .sel(RST));
  Multiplexer #(.select(1), .width(1), .disabled("Z"), .enable("false")) multiplexer_6 (
    .in0(MenToReg), .in1(1'b0), .out(multiplexer_6_out), .sel(RST));
  Multiplexer #(.select(1), .width(1), .disabled("Z"), .enable("false")) multiplexer_7 (
    .in0(MenWrite), .in1(1'b0), .out(multiplexer_7_out), .sel(RST));
  Multiplexer #(.select(1), .width(32), .disabled("Z"), .enable("false")) multiplexer_8 (
    .in0(R1), .in1({32{1'b0}}), .out(multiplexer_8_out), .sel(RST));
  Multiplexer #(.select(1), .width(32), .disabled("Z"), .enable("false")) multiplexer_9 (
    .in0(R), .in1({32{1'b0}}), .out(multiplexer_9_out), .sel(RST));
  Multiplexer #(.select(1), .width(32), .disabled("Z"), .enable("false")) multiplexer_10 (
    .in0(R2), .in1({32{1'b0}}), .out(multiplexer_10_out), .sel(RST));
  Multiplexer #(.select(1), .width(5), .disabled("Z"), .enable("false")) multiplexer_11 (
    .in0(W), .in1({5{1'b0}}), .out(multiplexer_11_out), .sel(RST));
  Multiplexer #(.select(1), .width(32), .disabled("Z"), .enable("false")) multiplexer_12 (
    .in0(PC_4), .in1({32{1'b0}}), .out(multiplexer_12_out), .sel(RST));
  Multiplexer #(.select(1), .width(32), .disabled("Z"), .enable("false")) multiplexer_13 (
    .in0(PC), .in1({32{1'b0}}), .out(multiplexer_13_out), .sel(RST));
  Register #(.width(1), .trigger("rising"), .Select("low")) register_1 (
    .D(multiplexer_1_out), .en(EN), .Q(ERET_2), .clk(CLK));  // open: clr
  Register #(.width(1), .trigger("rising"), .Select("low")) register_2 (
    .D(multiplexer_2_out), .en(EN), .Q(LB_2), .clk(CLK));  // open: clr
  Register #(.width(1), .trigger("rising"), .Select("low")) register_3 (
    .D(multiplexer_3_out), .en(EN), .Q(SysCall_2), .clk(CLK));  // open: clr
  Register #(.width(1), .trigger("rising"), .Select("low")) register_4 (
    .D(multiplexer_4_out), .en(EN), .Q(RegWrite_2), .clk(CLK));  // open: clr
  Register #(.width(1), .trigger("rising"), .Select("low")) register_5 (
    .D(multiplexer_5_out), .en(EN), .Q(JAL_2), .clk(CLK));  // open: clr
  Register #(.width(1), .trigger("rising"), .Select("low")) register_6 (
    .D(multiplexer_6_out), .en(EN), .Q(MenToReg_2), .clk(CLK));  // open: clr
  Register #(.width(1), .trigger("rising"), .Select("low")) register_7 (
    .D(multiplexer_7_out), .en(EN), .Q(MenWrite_2), .clk(CLK));  // open: clr
  Register #(.width(32), .trigger("rising"), .Select("low")) register_8 (
    .D(multiplexer_8_out), .en(EN), .Q(R1_2), .clk(CLK));  // open: clr
  Register #(.width(32), .trigger("rising"), .Select("low")) register_9 (
    .D(multiplexer_9_out), .en(EN), .Q(R_2), .clk(CLK));  // open: clr
  Register #(.width(32), .trigger("rising"), .Select("low")) register_10 (
    .D(multiplexer_10_out), .en(EN), .Q(R2_2), .clk(CLK));  // open: clr
  Register #(.width(5), .trigger("rising"), .Select("low")) register_11 (
    .D(multiplexer_11_out), .en(EN), .Q(W_2), .clk(CLK));  // open: clr
  Register #(.width(32), .trigger("rising"), .Select("low")) register_12 (
    .D(multiplexer_13_out), .en(EN), .Q(PC_2), .clk(CLK));  // open: clr
  Register #(.width(32), .trigger("rising"), .Select("low")) register_13 (
    .D(multiplexer_12_out), .en(EN), .Q(PC_4_2), .clk(CLK));  // open: clr

  assign R2_3 = R2_2;
endmodule

module MEM_WB (
  input  RST,
  input  EN,
  input  CLK,
  input  ERET,
  input  LB,
  input  SysCall,
  input  RegWrite,
  input  JAL,
  input  MenToReg,
  input  [31:0] R1,
  input  [31:0] R2,
  input  [31:0] ALU_Data,
  input  [31:0] MEM_ReadData,
  input  [4:0] W,
  input  [1:0] \LB低两位 ,
  input  [31:0] PC_4,
  input  [31:0] PC,
  output ERET_2,
  output LB_2,
  output SysCall_2,
  output RegWrite_2,
  output JAL_2,
  output MenToReg_2,
  output [31:0] R1_2,
  output [31:0] R2_2,
  output [31:0] ALU_Data_2,
  output [31:0] MEM_ReadData_2,
  output [4:0] W_2,
  output [1:0] \LB低两位_2 ,
  output [31:0] PC_4_2,
  output [31:0] PC_2
);

  wire multiplexer_1_out, multiplexer_2_out, multiplexer_3_out, multiplexer_4_out, multiplexer_5_out,
       multiplexer_6_out;
  wire [1:0] multiplexer_12_out;
  wire [4:0] multiplexer_11_out;
  wire [31:0] multiplexer_7_out, multiplexer_8_out, multiplexer_9_out, multiplexer_10_out,
       multiplexer_13_out, multiplexer_14_out;

  Pull_Resistor #(.pull(0)) pull_resistor_1 (.node(EN));
  Pull_Resistor #(.pull(0)) pull_resistor_2 (.node(RST));
  Multiplexer #(.select(1), .width(1), .disabled("Z"), .enable("false")) multiplexer_1 (
    .in0(ERET), .in1(1'b0), .out(multiplexer_1_out), .sel(RST));
  Multiplexer #(.select(1), .width(1), .disabled("Z"), .enable("false")) multiplexer_2 (
    .in0(LB), .in1(1'b0), .out(multiplexer_2_out), .sel(RST));
  Multiplexer #(.select(1), .width(1), .disabled("Z"), .enable("false")) multiplexer_3 (
    .in0(SysCall), .in1(1'b0), .out(multiplexer_3_out), .sel(RST));
  Multiplexer #(.select(1), .width(1), .disabled("Z"), .enable("false")) multiplexer_4 (
    .in0(RegWrite), .in1(1'b0), .out(multiplexer_4_out), .sel(RST));
  Multiplexer #(.select(1), .width(1), .disabled("Z"), .enable("false")) multiplexer_5 (
    .in0(JAL), .in1(1'b0), .out(multiplexer_5_out), .sel(RST));
  Multiplexer #(.select(1), .width(1), .disabled("Z"), .enable("false")) multiplexer_6 (
    .in0(MenToReg), .in1(1'b0), .out(multiplexer_6_out), .sel(RST));
  Multiplexer #(.select(1), .width(32), .disabled("Z"), .enable("false")) multiplexer_7 (
    .in0(R1), .in1({32{1'b0}}), .out(multiplexer_7_out), .sel(RST));
  Multiplexer #(.select(1), .width(32), .disabled("Z"), .enable("false")) multiplexer_8 (
    .in0(R2), .in1({32{1'b0}}), .out(multiplexer_8_out), .sel(RST));
  Multiplexer #(.select(1), .width(32), .disabled("Z"), .enable("false")) multiplexer_9 (
    .in0(ALU_Data), .in1({32{1'b0}}), .out(multiplexer_9_out), .sel(RST));
  Multiplexer #(.select(1), .width(32), .disabled("Z"), .enable("false")) multiplexer_10 (
    .in0(MEM_ReadData), .in1({32{1'b0}}), .out(multiplexer_10_out), .sel(RST));
  Multiplexer #(.select(1), .width(5), .disabled("Z"), .enable("false")) multiplexer_11 (
    .in0(W), .in1({5{1'b0}}), .out(multiplexer_11_out), .sel(RST));
  Multiplexer #(.select(1), .width(2), .disabled("Z"), .enable("false")) multiplexer_12 (
    .in0(\LB低两位 ), .in1(2'b00), .out(multiplexer_12_out), .sel(RST));
  Multiplexer #(.select(1), .width(32), .disabled("Z"), .enable("false")) multiplexer_13 (
    .in0(PC_4), .in1({32{1'b0}}), .out(multiplexer_13_out), .sel(RST));
  Multiplexer #(.select(1), .width(32), .disabled("Z"), .enable("false")) multiplexer_14 (
    .in0(PC), .in1({32{1'b0}}), .out(multiplexer_14_out), .sel(RST));
  Register #(.width(1), .trigger("rising"), .Select("low")) register_1 (
    .D(multiplexer_1_out), .en(EN), .Q(ERET_2), .clk(CLK));  // open: clr
  Register #(.width(1), .trigger("rising"), .Select("low")) register_2 (
    .D(multiplexer_2_out), .en(EN), .Q(LB_2), .clk(CLK));  // open: clr
  Register #(.width(1), .trigger("rising"), .Select("low")) register_3 (
    .D(multiplexer_3_out), .en(EN), .Q(SysCall_2), .clk(CLK));  // open: clr
  Register #(.width(1), .trigger("rising"), .Select("low")) register_4 (
    .D(multiplexer_4_out), .en(EN), .Q(RegWrite_2), .clk(CLK));  // open: clr
  Register #(.width(1), .trigger("rising"), .Select("low")) register_5 (
    .D(multiplexer_5_out), .en(EN), .Q(JAL_2), .clk(CLK));  // open: clr
  Register #(.width(1), .trigger("rising"), .Select("low")) register_6 (
    .D(multiplexer_6_out), .en(EN), .Q(MenToReg_2), .clk(CLK));  // open: clr
  Register #(.width(32), .trigger("rising"), .Select("low")) register_7 (
    .D(multiplexer_7_out), .en(EN), .Q(R1_2), .clk(CLK));  // open: clr
  Register #(.width(32), .trigger("rising"), .Select("low")) register_8 (
    .D(multiplexer_8_out), .en(EN), .Q(R2_2), .clk(CLK));  // open: clr
  Register #(.width(32), .trigger("rising"), .Select("low")) register_9 (
    .D(multiplexer_9_out), .en(EN), .Q(ALU_Data_2), .clk(CLK));  // open: clr
  Register #(.width(32), .trigger("rising"), .Select("low")) register_10 (
    .D(multiplexer_10_out), .en(EN), .Q(MEM_ReadData_2), .clk(CLK));  // open: clr
  Register #(.width(5), .trigger("rising"), .Select("low")) register_11 (
    .D(multiplexer_11_out), .en(EN), .Q(W_2), .clk(CLK));  // open: clr
  Register #(.width(2), .trigger("rising"), .Select("low")) register_12 (
    .D(multiplexer_12_out), .en(EN), .Q(\LB低两位_2 ), .clk(CLK));  // open: clr
  Register #(.width(32), .trigger("rising"), .Select("low")) register_13 (
    .D(multiplexer_13_out), .en(EN), .Q(PC_4_2), .clk(CLK));  // open: clr
  Register #(.width(32), .trigger("rising"), .Select("low")) register_14 (
    .D(multiplexer_14_out), .en(EN), .Q(PC_2), .clk(CLK));  // open: clr
endmodule

module \源寄存器使用情况  (
  input  OP0,
  input  OP1,
  input  OP2,
  input  OP3,
  input  OP4,
  input  OP5,
  input  F0,
  input  F1,
  input  F2,
  input  F3,
  input  F4,
  input  F5,
  output R1_Used,
  output R2_Used
);

  wire and_1_out, and_2_out, and_3_out, and_4_out, and_5_out, and_6_out, and_7_out, and_8_out, and_9_out,
       and_10_out, and_11_out, and_12_out, and_13_out, and_14_out, and_15_out, and_16_out, and_17_out,
       and_18_out, and_19_out, and_20_out, and_21_out, and_22_out, and_23_out, and_24_out, and_25_out,
       and_26_out, and_27_out, and_28_out, and_29_out, and_30_out, and_31_out, and_32_out, and_33_out,
       and_34_out, and_35_out, and_36_out, and_37_out, not_1_out, not_2_out, not_3_out, not_4_out, not_5_out,
       not_6_out, not_7_out, not_8_out, not_9_out, not_10_out, not_11_out, not_12_out, not_13_out,
       not_14_out, not_15_out, not_16_out, not_17_out, not_18_out, not_19_out, not_20_out, not_21_out,
       not_22_out, not_23_out, not_24_out, not_25_out, not_26_out, not_27_out, not_28_out, not_29_out,
       not_30_out, not_31_out, not_32_out, not_33_out, not_34_out, not_35_out, not_36_out, not_37_out,
       not_38_out, not_39_out, not_40_out, not_41_out, not_42_out, not_43_out, not_44_out, not_45_out,
       not_46_out, not_47_out, not_48_out, not_49_out, not_50_out, not_51_out, not_52_out, not_53_out,
       not_54_out, not_55_out, not_56_out, not_57_out, not_58_out, not_59_out, not_60_out, not_61_out,
       not_62_out, not_63_out, not_64_out, not_65_out, not_66_out, not_67_out, not_68_out, not_69_out,
       not_70_out, not_71_out, not_72_out, not_73_out, not_74_out, not_75_out, not_76_out, not_77_out,
       not_78_out, not_79_out, not_80_out, not_81_out, not_82_out, not_83_out, not_84_out, not_85_out,
       not_86_out, not_87_out, not_88_out, not_89_out, not_90_out, not_91_out, not_92_out, not_93_out,
       not_94_out, not_95_out, not_96_out, not_97_out, not_98_out, not_99_out, not_100_out, not_101_out,
       not_102_out, not_103_out, not_104_out, not_105_out, not_106_out, not_107_out, not_108_out,
       not_109_out, not_110_out, not_111_out, not_112_out, not_113_out, not_114_out, not_115_out,
       not_116_out, not_117_out, not_118_out, not_119_out, not_120_out, not_121_out, not_122_out,
       not_123_out, not_124_out, not_125_out, not_126_out, not_127_out, not_128_out, not_129_out,
       not_130_out, not_131_out, not_132_out, not_133_out, not_134_out, not_135_out, not_136_out,
       not_137_out, not_138_out, not_139_out, not_140_out, not_141_out, not_142_out, not_143_out,
       not_144_out, not_145_out, not_146_out, not_147_out, not_148_out, not_149_out, not_150_out,
       not_151_out, not_152_out, not_153_out, not_154_out, not_155_out, not_156_out, not_157_out,
       not_158_out, not_159_out, not_160_out, not_161_out, not_162_out, not_163_out, not_164_out,
       not_165_out, not_166_out, not_167_out, not_168_out, not_169_out, not_170_out, not_171_out,
       not_172_out, not_173_out, not_174_out, not_175_out, not_176_out, not_177_out, not_178_out,
       not_179_out, not_180_out, not_181_out, not_182_out, not_183_out, not_184_out, not_185_out,
       not_186_out, not_187_out, not_188_out, not_189_out, not_190_out, not_191_out, not_192_out,
       not_193_out, not_194_out, not_195_out, not_196_out, not_197_out, not_198_out, not_199_out,
       not_200_out, not_201_out, not_202_out, not_203_out, not_204_out, not_205_out, not_206_out,
       not_207_out, not_208_out, not_209_out, not_210_out, not_211_out, not_212_out, not_213_out,
       not_214_out, not_215_out, not_216_out, not_217_out, not_218_out, not_219_out, not_220_out,
       not_221_out, not_222_out, not_223_out, not_224_out, not_225_out, not_226_out, not_227_out,
       not_228_out, not_229_out, not_230_out, not_231_out, not_232_out, not_233_out, not_234_out,
       not_235_out, not_236_out, not_237_out, not_238_out, not_239_out, not_240_out, not_241_out,
       not_242_out, not_243_out, not_244_out, not_245_out, not_246_out, not_247_out, not_248_out,
       not_249_out, not_250_out, not_251_out, not_252_out, not_253_out, not_254_out, not_255_out,
       not_256_out, not_257_out, not_258_out, not_259_out, not_260_out, not_261_out, not_262_out,
       not_263_out, not_264_out, not_265_out, not_266_out, not_267_out, not_268_out, not_269_out,
       not_270_out, not_271_out, not_272_out;

  not not_1 (not_1_out, OP5);
  not not_2 (not_2_out, OP4);
  not not_3 (not_3_out, OP3);
  not not_4 (not_4_out, OP2);
  not not_5 (not_5_out, OP1);
  not not_6 (not_6_out, OP0);
  not not_7 (not_7_out, F4);
  not not_8 (not_8_out, F3);
  not not_9 (not_9_out, F2);
  not not_10 (not_10_out, F1);
  not not_11 (not_11_out, F0);
  not not_12 (not_12_out, OP5);
  not not_13 (not_13_out, OP4);
  not not_14 (not_14_out, OP3);
  not not_15 (not_15_out, OP2);
  not not_16 (not_16_out, OP1);
  not not_17 (not_17_out, OP0);
  not not_18 (not_18_out, F4);
  not not_19 (not_19_out, F3);
  not not_20 (not_20_out, F2);
  not not_21 (not_21_out, F1);
  not not_22 (not_22_out, OP5);
  not not_23 (not_23_out, OP4);
  not not_24 (not_24_out, OP3);
  not not_25 (not_25_out, OP2);
  not not_26 (not_26_out, OP1);
  not not_27 (not_27_out, OP0);
  not not_28 (not_28_out, F4);
  not not_29 (not_29_out, F3);
  not not_30 (not_30_out, F2);
  not not_31 (not_31_out, F0);
  not not_32 (not_32_out, OP5);
  not not_33 (not_33_out, OP4);
  not not_34 (not_34_out, OP3);
  not not_35 (not_35_out, OP2);
  not not_36 (not_36_out, OP1);
  not not_37 (not_37_out, OP0);
  not not_38 (not_38_out, F4);
  not not_39 (not_39_out, F3);
  not not_40 (not_40_out, F1);
  not not_41 (not_41_out, F0);
  not not_42 (not_42_out, OP5);
  not not_43 (not_43_out, OP4);
  not not_44 (not_44_out, OP3);
  not not_45 (not_45_out, OP2);
  not not_46 (not_46_out, OP1);
  not not_47 (not_47_out, OP0);
  not not_48 (not_48_out, F4);
  not not_49 (not_49_out, F3);
  not not_50 (not_50_out, F1);
  not not_51 (not_51_out, OP5);
  not not_52 (not_52_out, OP4);
  not not_53 (not_53_out, OP3);
  not not_54 (not_54_out, OP2);
  not not_55 (not_55_out, OP1);
  not not_56 (not_56_out, OP0);
  not not_57 (not_57_out, F4);
  not not_58 (not_58_out, F3);
  not not_59 (not_59_out, OP5);
  not not_60 (not_60_out, OP4);
  not not_61 (not_61_out, OP3);
  not not_62 (not_62_out, OP2);
  not not_63 (not_63_out, OP1);
  not not_64 (not_64_out, OP0);
  not not_65 (not_65_out, F4);
  not not_66 (not_66_out, F2);
  not not_67 (not_67_out, F0);
  not not_68 (not_68_out, OP5);
  not not_69 (not_69_out, OP4);
  not not_70 (not_70_out, OP3);
  not not_71 (not_71_out, OP2);
  not not_72 (not_72_out, OP1);
  not not_73 (not_73_out, OP0);
  not not_74 (not_74_out, F4);
  not not_75 (not_75_out, F2);
  not not_76 (not_76_out, OP5);
  not not_77 (not_77_out, OP4);
  not not_78 (not_78_out, OP3);
  not not_79 (not_79_out, OP2);
  not not_80 (not_80_out, OP1);
  not not_81 (not_81_out, OP0);
  not not_82 (not_82_out, F5);
  not not_83 (not_83_out, F4);
  not not_84 (not_84_out, F2);
  not not_85 (not_85_out, F1);
  not not_86 (not_86_out, F0);
  not not_87 (not_87_out, OP5);
  not not_88 (not_88_out, OP4);
  not not_89 (not_89_out, OP3);
  not not_90 (not_90_out, OP2);
  not not_91 (not_91_out, OP1);
  not not_92 (not_92_out, OP0);
  not not_93 (not_93_out, F5);
  not not_94 (not_94_out, F4);
  not not_95 (not_95_out, F1);
  not not_96 (not_96_out, F0);
  not not_97 (not_97_out, OP5);
  not not_98 (not_98_out, OP4);
  not not_99 (not_99_out, OP3);
  not not_100 (not_100_out, OP1);
  not not_101 (not_101_out, OP0);
  not not_102 (not_102_out, OP5);
  not not_103 (not_103_out, OP4);
  not not_104 (not_104_out, OP3);
  not not_105 (not_105_out, OP1);
  not not_106 (not_106_out, OP5);
  not not_107 (not_107_out, OP4);
  not not_108 (not_108_out, OP2);
  not not_109 (not_109_out, OP1);
  not not_110 (not_110_out, OP0);
  not not_111 (not_111_out, OP5);
  not not_112 (not_112_out, OP4);
  not not_113 (not_113_out, OP1);
  not not_114 (not_114_out, OP0);
  not not_115 (not_115_out, OP5);
  not not_116 (not_116_out, OP4);
  not not_117 (not_117_out, OP2);
  not not_118 (not_118_out, OP1);
  not not_119 (not_119_out, OP5);
  not not_120 (not_120_out, OP4);
  not not_121 (not_121_out, OP2);
  not not_122 (not_122_out, OP0);
  not not_123 (not_123_out, OP5);
  not not_124 (not_124_out, OP4);
  not not_125 (not_125_out, OP1);
  not not_126 (not_126_out, OP4);
  not not_127 (not_127_out, OP3);
  not not_128 (not_128_out, OP2);
  not not_129 (not_129_out, OP4);
  not not_130 (not_130_out, OP2);
  not not_131 (not_131_out, OP5);
  not not_132 (not_132_out, OP4);
  not not_133 (not_133_out, OP2);
  not not_134 (not_134_out, OP4);
  not not_135 (not_135_out, OP3);
  not not_136 (not_136_out, OP2);
  not not_137 (not_137_out, OP1);
  not not_138 (not_138_out, OP0);
  not not_139 (not_139_out, OP5);
  not not_140 (not_140_out, OP4);
  not not_141 (not_141_out, OP3);
  not not_142 (not_142_out, OP2);
  not not_143 (not_143_out, OP1);
  not not_144 (not_144_out, OP5);
  not not_145 (not_145_out, OP4);
  not not_146 (not_146_out, OP3);
  not not_147 (not_147_out, OP2);
  not not_148 (not_148_out, OP1);
  not not_149 (not_149_out, OP0);
  not not_150 (not_150_out, F5);
  not not_151 (not_151_out, F4);
  not not_152 (not_152_out, F3);
  not not_153 (not_153_out, F2);
  not not_154 (not_154_out, F1);
  not not_155 (not_155_out, F0);
  not not_156 (not_156_out, OP5);
  not not_157 (not_157_out, OP4);
  not not_158 (not_158_out, OP3);
  not not_159 (not_159_out, OP2);
  not not_160 (not_160_out, OP1);
  not not_161 (not_161_out, OP0);
  not not_162 (not_162_out, F5);
  not not_163 (not_163_out, F4);
  not not_164 (not_164_out, F3);
  not not_165 (not_165_out, F2);
  not not_166 (not_166_out, OP5);
  not not_167 (not_167_out, OP4);
  not not_168 (not_168_out, OP3);
  not not_169 (not_169_out, OP2);
  not not_170 (not_170_out, OP1);
  not not_171 (not_171_out, OP0);
  not not_172 (not_172_out, F5);
  not not_173 (not_173_out, F4);
  not not_174 (not_174_out, F3);
  not not_175 (not_175_out, F2);
  not not_176 (not_176_out, F0);
  not not_177 (not_177_out, OP5);
  not not_178 (not_178_out, OP4);
  not not_179 (not_179_out, OP3);
  not not_180 (not_180_out, OP2);
  not not_181 (not_181_out, OP1);
  not not_182 (not_182_out, OP0);
  not not_183 (not_183_out, F4);
  not not_184 (not_184_out, F3);
  not not_185 (not_185_out, F2);
  not not_186 (not_186_out, F1);
  not not_187 (not_187_out, F0);
  not not_188 (not_188_out, OP5);
  not not_189 (not_189_out, OP4);
  not not_190 (not_190_out, OP3);
  not not_191 (not_191_out, OP2);
  not not_192 (not_192_out, OP1);
  not not_193 (not_193_out, OP0);
  not not_194 (not_194_out, F4);
  not not_195 (not_195_out, F3);
  not not_196 (not_196_out, F2);
  not not_197 (not_197_out, F1);
  not not_198 (not_198_out, OP5);
  not not_199 (not_199_out, OP4);
  not not_200 (not_200_out, OP3);
  not not_201 (not_201_out, OP2);
  not not_202 (not_202_out, OP1);
  not not_203 (not_203_out, OP0);
  not not_204 (not_204_out, F4);
  not not_205 (not_205_out, F3);
  not not_206 (not_206_out, F2);
  not not_207 (not_207_out, F0);
  not not_208 (not_208_out, OP5);
  not not_209 (not_209_out, OP4);
  not not_210 (not_210_out, OP3);
  not not_211 (not_211_out, OP2);
  not not_212 (not_212_out, OP1);
  not not_213 (not_213_out, OP0);
  not not_214 (not_214_out, F4);
  not not_215 (not_215_out, F3);
  not not_216 (not_216_out, F1);
  not not_217 (not_217_out, F0);
  not not_218 (not_218_out, OP5);
  not not_219 (not_219_out, OP4);
  not not_220 (not_220_out, OP3);
  not not_221 (not_221_out, OP2);
  not not_222 (not_222_out, OP1);
  not not_223 (not_223_out, OP0);
  not not_224 (not_224_out, F4);
  not not_225 (not_225_out, F3);
  not not_226 (not_226_out, F1);
  not not_227 (not_227_out, OP5);
  not not_228 (not_228_out, OP4);
  not not_229 (not_229_out, OP3);
  not not_230 (not_230_out, OP2);
  not not_231 (not_231_out, OP1);
  not not_232 (not_232_out, OP0);
  not not_233 (not_233_out, F4);
  not not_234 (not_234_out, F3);
  not not_235 (not_235_out, OP5);
  not not_236 (not_236_out, OP4);
  not not_237 (not_237_out, OP3);
  not not_238 (not_238_out, OP2);
  not not_239 (not_239_out, OP1);
  not not_240 (not_240_out, OP0);
  not not_241 (not_241_out, F4);
  not not_242 (not_242_out, F2);
  not not_243 (not_243_out, F0);
  not not_244 (not_244_out, OP5);
  not not_245 (not_245_out, OP4);
  not not_246 (not_246_out, OP3);
  not not_247 (not_247_out, OP2);
  not not_248 (not_248_out, OP1);
  not not_249 (not_249_out, OP0);
  not not_250 (not_250_out, F4);
  not not_251 (not_251_out, F2);
  not not_252 (not_252_out, OP5);
  not not_253 (not_253_out, OP4);
  not not_254 (not_254_out, OP3);
  not not_255 (not_255_out, OP2);
  not not_256 (not_256_out, OP1);
  not not_257 (not_257_out, OP0);
  not not_258 (not_258_out, F5);
  not not_259 (not_259_out, F4);
  not not_260 (not_260_out, F1);
  not not_261 (not_261_out, F0);
  not not_262 (not_262_out, OP5);
  not not_263 (not_263_out, OP4);
  not not_264 (not_264_out, OP3);
  not not_265 (not_265_out, OP1);
  not not_266 (not_266_out, OP0);
  not not_267 (not_267_out, OP5);
  not not_268 (not_268_out, OP4);
  not not_269 (not_269_out, OP3);
  not not_270 (not_270_out, OP1);
  not not_271 (not_271_out, OP4);
  not not_272 (not_272_out, OP2);
  and and_1 (and_1_out, not_1_out, not_2_out, not_3_out, not_4_out, not_5_out, not_6_out, F5, not_7_out, not_8_out, not_9_out, not_10_out, not_11_out);
  and and_2 (and_2_out, not_12_out, not_13_out, not_14_out, not_15_out, not_16_out, not_17_out, F5, not_18_out, not_19_out, not_20_out, not_21_out, F0);
  and and_3 (and_3_out, not_22_out, not_23_out, not_24_out, not_25_out, not_26_out, not_27_out, F5, not_28_out, not_29_out, not_30_out, F1, not_31_out);
  and and_4 (and_4_out, not_32_out, not_33_out, not_34_out, not_35_out, not_36_out, not_37_out, F5, not_38_out, not_39_out, F2, not_40_out, not_41_out);
  and and_5 (and_5_out, not_42_out, not_43_out, not_44_out, not_45_out, not_46_out, not_47_out, F5, not_48_out, not_49_out, F2, not_50_out, F0);
  and and_6 (and_6_out, not_51_out, not_52_out, not_53_out, not_54_out, not_55_out, not_56_out, F5, not_57_out, not_58_out, F2, F1, F0);
  and and_7 (and_7_out, not_59_out, not_60_out, not_61_out, not_62_out, not_63_out, not_64_out, F5, not_65_out, F3, not_66_out, F1, not_67_out);
  and and_8 (and_8_out, not_68_out, not_69_out, not_70_out, not_71_out, not_72_out, not_73_out, F5, not_74_out, F3, not_75_out, F1, F0);
  and and_9 (and_9_out, not_76_out, not_77_out, not_78_out, not_79_out, not_80_out, not_81_out, not_82_out, not_83_out, F3, not_84_out, not_85_out, not_86_out);
  and and_10 (and_10_out, not_87_out, not_88_out, not_89_out, not_90_out, not_91_out, not_92_out, not_93_out, not_94_out, F3, F2, not_95_out, not_96_out);
  and and_11 (and_11_out, not_97_out, not_98_out, not_99_out, OP2, not_100_out, not_101_out);
  and and_12 (and_12_out, not_102_out, not_103_out, not_104_out, OP2, not_105_out, OP0);
  and and_13 (and_13_out, not_106_out, not_107_out, OP3, not_108_out, not_109_out, not_110_out);
  and and_14 (and_14_out, not_111_out, not_112_out, OP3, OP2, not_113_out, not_114_out);
  and and_15 (and_15_out, not_115_out, not_116_out, OP3, not_117_out, not_118_out, OP0);
  and and_16 (and_16_out, not_119_out, not_120_out, OP3, not_121_out, OP1, not_122_out);
  and and_17 (and_17_out, not_123_out, not_124_out, OP3, OP2, not_125_out, OP0);
  and and_18 (and_18_out, OP5, not_126_out, not_127_out, not_128_out, OP1, OP0);
  and and_19 (and_19_out, OP5, not_129_out, OP3, not_130_out, OP1, OP0);
  and and_20 (and_20_out, not_131_out, not_132_out, OP3, not_133_out, OP1, OP0);
  and and_21 (and_21_out, OP5, not_134_out, not_135_out, not_136_out, not_137_out, not_138_out);
  and and_22 (and_22_out, not_139_out, not_140_out, not_141_out, not_142_out, not_143_out, OP0);
  and and_23 (and_23_out, not_144_out, not_145_out, not_146_out, not_147_out, not_148_out, not_149_out, not_150_out, not_151_out, not_152_out, not_153_out, not_154_out, not_155_out);
  and and_24 (and_24_out, not_156_out, not_157_out, not_158_out, not_159_out, not_160_out, not_161_out, not_162_out, not_163_out, not_164_out, not_165_out, F1, F0);
  and and_25 (and_25_out, not_166_out, not_167_out, not_168_out, not_169_out, not_170_out, not_171_out, not_172_out, not_173_out, not_174_out, not_175_out, F1, not_176_out);
  and and_26 (and_26_out, not_177_out, not_178_out, not_179_out, not_180_out, not_181_out, not_182_out, F5, not_183_out, not_184_out, not_185_out, not_186_out, not_187_out);
  and and_27 (and_27_out, not_188_out, not_189_out, not_190_out, not_191_out, not_192_out, not_193_out, F5, not_194_out, not_195_out, not_196_out, not_197_out, F0);
  and and_28 (and_28_out, not_198_out, not_199_out, not_200_out, not_201_out, not_202_out, not_203_out, F5, not_204_out, not_205_out, not_206_out, F1, not_207_out);
  and and_29 (and_29_out, not_208_out, not_209_out, not_210_out, not_211_out, not_212_out, not_213_out, F5, not_214_out, not_215_out, F2, not_216_out, not_217_out);
  and and_30 (and_30_out, not_218_out, not_219_out, not_220_out, not_221_out, not_222_out, not_223_out, F5, not_224_out, not_225_out, F2, not_226_out, F0);
  and and_31 (and_31_out, not_227_out, not_228_out, not_229_out, not_230_out, not_231_out, not_232_out, F5, not_233_out, not_234_out, F2, F1, F0);
  and and_32 (and_32_out, not_235_out, not_236_out, not_237_out, not_238_out, not_239_out, not_240_out, F5, not_241_out, F3, not_242_out, F1, not_243_out);
  and and_33 (and_33_out, not_244_out, not_245_out, not_246_out, not_247_out, not_248_out, not_249_out, F5, not_250_out, F3, not_251_out, F1, F0);
  and and_34 (and_34_out, not_252_out, not_253_out, not_254_out, not_255_out, not_256_out, not_257_out, not_258_out, not_259_out, F3, F2, not_260_out, not_261_out);
  and and_35 (and_35_out, not_262_out, not_263_out, not_264_out, OP2, not_265_out, not_266_out);
  and and_36 (and_36_out, not_267_out, not_268_out, not_269_out, OP2, not_270_out, OP0);
  and and_37 (and_37_out, OP5, not_271_out, OP3, not_272_out, OP1, OP0);
  or or_1 (R1_Used, and_1_out, and_2_out, and_3_out, and_4_out, and_5_out, and_6_out, and_7_out, and_8_out, and_9_out, and_10_out, and_11_out, and_12_out, and_13_out, and_14_out, and_15_out, and_16_out, and_17_out, and_18_out, and_19_out, and_20_out, and_21_out, and_22_out);
  or or_2 (R2_Used, and_23_out, and_24_out, and_25_out, and_26_out, and_27_out, and_28_out, and_29_out, and_30_out, and_31_out, and_32_out, and_33_out, and_34_out, and_35_out, and_36_out, and_37_out);
endmodule

// 源寄存器使用情况
module \源寄存器使用情况封装电路  (
  input  [5:0] OP,
  input  [5:0] Func,
  output R1_Used,
  output R2_Used
);

  \源寄存器使用情况  \u_源寄存器使用情况_1  (
    .OP0(OP[0]), .OP1(OP[1]), .OP2(OP[2]), .OP3(OP[3]), .OP4(OP[4]), .OP5(OP[5]), .F0(Func[0]), .F1(Func[1]),
    .F2(Func[2]), .F3(Func[3]), .F4(Func[4]), .F5(Func[5]), .R1_Used(R1_Used), .R2_Used(R2_Used));
endmodule

module \数据相关检测  (
  input  MEM_RegWrite,
  input  EX_RegWrite,
  input  [4:0] EX_W_num,
  input  [4:0] MEM_W_num,
  input  R2_Used,
  input  [4:0] R2_num,
  input  R1_Used,
  input  [4:0] R1_num,
  input  Pause,
  input  \转跳插入气泡 ,
  output \ID_EX气泡 ,
  output PC_IF_ID_EN
);

  wire and_1_out, and_2_out, and_3_out, and_4_out, comparator_1_eq, comparator_2_eq, comparator_3_eq,
       comparator_4_eq, comparator_5_eq, comparator_6_eq, comparator_7_eq, comparator_8_eq, not_2_out,
       not_3_out, not_4_out, not_5_out, or_1_out, or_2_out, Pause_EN, \数据冲突 ;

  not not_1 (Pause_EN, Pause);
  Multiplexer #(.select(1), .width(1), .disabled("Z"), .enable("false")) multiplexer_1 (
    .in0(\转跳插入气泡 ), .in1(1'b1), .out(\ID_EX气泡 ), .sel(\数据冲突 ));
  Multiplexer #(.select(1), .width(1), .disabled("Z"), .enable("false")) multiplexer_2 (
    .in0(Pause_EN), .in1(1'b0), .out(PC_IF_ID_EN), .sel(\数据冲突 ));
  Comparator #(.width(5), .mode("unsigned")) comparator_1 (
    .a(R1_num), .b({5{1'b0}}), .eq(comparator_1_eq));  // open: gt, lt
  Comparator #(.width(5), .mode("unsigned")) comparator_2 (
    .a(R1_num), .b(EX_W_num), .eq(comparator_2_eq));  // open: gt, lt
  Comparator #(.width(5), .mode("unsigned")) comparator_3 (
    .a(R2_num), .b({5{1'b0}}), .eq(comparator_3_eq));  // open: gt, lt
  Comparator #(.width(5), .mode("unsigned")) comparator_4 (
    .a(R2_num), .b(EX_W_num), .eq(comparator_4_eq));  // open: gt, lt
  Comparator #(.width(5), .mode("unsigned")) comparator_5 (
    .a(R1_num), .b({5{1'b0}}), .eq(comparator_5_eq));  // open: gt, lt
  Comparator #(.width(5), .mode("unsigned")) comparator_6 (
    .a(R1_num), .b(MEM_W_num), .eq(comparator_6_eq));  // open: gt, lt
  Comparator #(.width(5), .mode("unsigned")) comparator_7 (
    .a(R2_num), .b({5{1'b0}}), .eq(comparator_7_eq));  // open: gt, lt
  Comparator #(.width(5), .mode("unsigned")) comparator_8 (
    .a(R2_num), .b(MEM_W_num), .eq(comparator_8_eq));  // open: gt, lt
  not not_2 (not_2_out, comparator_1_eq);
  not not_3 (not_3_out, comparator_3_eq);
  not not_4 (not_4_out, comparator_5_eq);
  not not_5 (not_5_out, comparator_7_eq);
  and and_1 (and_1_out, not_2_out, comparator_2_eq, EX_RegWrite, R1_Used);
  and and_2 (and_2_out, not_3_out, comparator_4_eq, EX_RegWrite, R2_Used);
  and and_3 (and_3_out, not_4_out, comparator_6_eq, R1_Used, MEM_RegWrite);
  and and_4 (and_4_out, not_5_out, comparator_8_eq, R2_Used, MEM_RegWrite);
  or or_1 (or_1_out, and_1_out, and_2_out);
  or or_2 (or_2_out, and_3_out, and_4_out);
  or or_3 (\数据冲突 , or_1_out, or_2_out);

  // Notes on the sheet:
  //   EN=1时寄存器工作
endmodule

module \重定向数据相关检测  (
  input  EX_MemToReg,
  input  EX_RegWrite,
  input  MEM_MemToReg,
  input  MEM_RegWrite,
  input  [4:0] MEM_W_num,
  input  Pause,
  input  [4:0] EX_W_num,
  input  \转跳插入气泡 ,
  input  [4:0] ID_R1_num,
  input  [4:0] ID_R2_num,
  input  R1_Used,
  input  R2_Used,
  output [1:0] Forward1,
  output \ID_EX气泡 ,
  output PC_IF_ID_EN,
  output [1:0] Forward2
);

  wire and_1_out, and_2_out, and_9_out, and_10_out, comparator_1_eq, comparator_2_eq, comparator_3_eq,
       comparator_4_eq, comparator_5_eq, comparator_6_eq, comparator_7_eq, comparator_8_eq, comparator_9_eq,
       comparator_10_eq, comparator_11_eq, comparator_12_eq, comparator_13_eq, comparator_14_eq,
       comparator_15_eq, comparator_16_eq, Forward1_1, Forward1_2, Forward1_3, Forward2_1, Forward2_2,
       Forward2_3, not_1_out, not_2_out, not_4_out, not_5_out, not_6_out, not_7_out, not_8_out, not_9_out,
       not_10_out, not_11_out, not_12_out, not_13_out, Pause_EN, \气泡 ;

  Comparator #(.width(5), .mode("unsigned")) comparator_1 (
    .a(EX_W_num), .b(ID_R1_num), .eq(comparator_1_eq));  // open: gt, lt
  Comparator #(.width(5), .mode("unsigned")) comparator_2 (
    .a(EX_W_num), .b({5{1'b0}}), .eq(comparator_2_eq));  // open: gt, lt
  Comparator #(.width(5), .mode("unsigned")) comparator_3 (
    .a(EX_W_num), .b(ID_R2_num), .eq(comparator_3_eq));  // open: gt, lt
  Comparator #(.width(5), .mode("unsigned")) comparator_4 (
    .a(EX_W_num), .b({5{1'b0}}), .eq(comparator_4_eq));  // open: gt, lt
  not not_1 (not_1_out, comparator_2_eq);
  not not_2 (not_2_out, comparator_4_eq);
  and and_1 (and_1_out, EX_MemToReg, comparator_1_eq, not_1_out, R1_Used);
  and and_2 (and_2_out, EX_MemToReg, comparator_3_eq, not_2_out, R2_Used);
  not not_3 (Pause_EN, Pause);
  or or_1 (\气泡 , and_1_out, and_2_out);
  Comparator #(.width(5), .mode("unsigned")) comparator_5 (
    .a(MEM_W_num), .b(ID_R1_num), .eq(comparator_5_eq));  // open: gt, lt
  not not_4 (not_4_out, comparator_6_eq);
  Comparator #(.width(5), .mode("unsigned")) comparator_6 (
    .a(MEM_W_num), .b({5{1'b0}}), .eq(comparator_6_eq));  // open: gt, lt
  Comparator #(.width(5), .mode("unsigned")) comparator_7 (
    .a(MEM_W_num), .b(ID_R1_num), .eq(comparator_7_eq));  // open: gt, lt
  Comparator #(.width(5), .mode("unsigned")) comparator_8 (
    .a(MEM_W_num), .b({5{1'b0}}), .eq(comparator_8_eq));  // open: gt, lt
  Comparator #(.width(5), .mode("unsigned")) comparator_9 (
    .a(EX_W_num), .b(ID_R1_num), .eq(comparator_9_eq));  // open: gt, lt
  Comparator #(.width(5), .mode("unsigned")) comparator_10 (
    .a(EX_W_num), .b({5{1'b0}}), .eq(comparator_10_eq));  // open: gt, lt
  not not_5 (not_5_out, MEM_MemToReg);
  not not_6 (not_6_out, comparator_8_eq);
  not not_7 (not_7_out, EX_MemToReg);
  not not_8 (not_8_out, comparator_10_eq);
  and and_3 (Forward1_1, MEM_MemToReg, comparator_5_eq, MEM_RegWrite, not_4_out, R1_Used);
  and and_4 (Forward1_2, not_5_out, comparator_7_eq, MEM_RegWrite, not_6_out, R1_Used);
  and and_5 (Forward1_3, not_7_out, comparator_9_eq, EX_RegWrite, not_8_out, R1_Used);
  Multiplexer #(.select(1), .width(1), .disabled("Z"), .enable("false")) multiplexer_1 (
    .in0(\转跳插入气泡 ), .in1(1'b1), .out(\ID_EX气泡 ), .sel(\气泡 ));
  Comparator #(.width(5), .mode("unsigned")) comparator_11 (
    .a(MEM_W_num), .b(ID_R2_num), .eq(comparator_11_eq));  // open: gt, lt
  Comparator #(.width(5), .mode("unsigned")) comparator_12 (
    .a(MEM_W_num), .b({5{1'b0}}), .eq(comparator_12_eq));  // open: gt, lt
  Comparator #(.width(5), .mode("unsigned")) comparator_13 (
    .a(MEM_W_num), .b(ID_R2_num), .eq(comparator_13_eq));  // open: gt, lt
  Comparator #(.width(5), .mode("unsigned")) comparator_14 (
    .a(MEM_W_num), .b({5{1'b0}}), .eq(comparator_14_eq));  // open: gt, lt
  Comparator #(.width(5), .mode("unsigned")) comparator_15 (
    .a(EX_W_num), .b(ID_R2_num), .eq(comparator_15_eq));  // open: gt, lt
  Comparator #(.width(5), .mode("unsigned")) comparator_16 (
    .a(EX_W_num), .b({5{1'b0}}), .eq(comparator_16_eq));  // open: gt, lt
  not not_9 (not_9_out, comparator_12_eq);
  not not_10 (not_10_out, MEM_MemToReg);
  not not_11 (not_11_out, comparator_14_eq);
  not not_12 (not_12_out, EX_MemToReg);
  not not_13 (not_13_out, comparator_16_eq);
  Multiplexer #(.select(1), .width(1), .disabled("Z"), .enable("false")) multiplexer_2 (
    .in0(Pause_EN), .in1(1'b0), .out(PC_IF_ID_EN), .sel(\气泡 ));
  and and_6 (Forward2_1, MEM_MemToReg, comparator_11_eq, MEM_RegWrite, not_9_out, R2_Used);
  and and_7 (Forward2_2, not_10_out, comparator_13_eq, MEM_RegWrite, not_11_out, R2_Used);
  and and_8 (Forward2_3, not_12_out, comparator_15_eq, EX_RegWrite, not_13_out, R2_Used);
  and and_9 (and_9_out, ~Forward1_3, ~Forward1_2, ~Forward1_1);  // AND_Gate
  and and_10 (and_10_out, ~Forward2_3, ~Forward2_2, ~Forward2_1);  // AND_Gate
  Priority_Encoder #(.select(2), .disabled("Z")) priority_encoder_1 (
    .in0(and_9_out), .in1(Forward1_1), .in2(Forward1_2), .in3(Forward1_3), .out(Forward1));  // open: gs, en_out, en_in
  Priority_Encoder #(.select(2), .disabled("Z")) priority_encoder_2 (
    .in0(and_10_out), .in1(Forward2_1), .in2(Forward2_2), .in3(Forward2_3), .out(Forward2));  // open: gs, en_out, en_in
endmodule

// 写入寄存器数据判断处理器
module \写入寄存器数据判断处理器  (
  input  LB,
  input  WB_JAL,
  input  [31:0] in_3,
  input  [1:0] \LB低两位 ,
  input  [31:0] WB_PC_4,
  output [31:0] out_6
);

  wire [7:0] multiplexer_1_out;
  wire [31:0] bit_extender_1_out, multiplexer_2_out;

  Multiplexer #(.select(2), .width(8), .disabled("Z"), .enable("false")) multiplexer_1 (
    .in0(in_3[7:0]), .in1(in_3[15:8]), .in2(in_3[23:16]), .in3(in_3[31:24]), .out(multiplexer_1_out),
    .sel(\LB低两位 ));
  assign bit_extender_1_out = {{24{multiplexer_1_out[7]}}, multiplexer_1_out};  // Bit_Extender bit_extender_1
  Multiplexer #(.select(1), .width(32), .disabled("Z"), .enable("false")) multiplexer_2 (
    .in0(in_3), .in1(bit_extender_1_out), .out(multiplexer_2_out), .sel(LB));
  Multiplexer #(.select(1), .width(32), .disabled("Z"), .enable("false")) multiplexer_3 (
    .in0(multiplexer_2_out), .in1(WB_PC_4), .out(out_6), .sel(WB_JAL));
endmodule
