// Logisim project 理想流水流水接口部件.circ as structural Verilog
module IF_ID (
  input  CLK,
  input  [31:0] PC_4,
  input  [31:0] IR,
  output [31:0] PC_4_2,
  output [31:0] IR_2
);

  Register #(.width(32), .trigger("rising"), .Select("low")) register_1 (
    .D(PC_4), .Q(PC_4_2), .clk(CLK));  // open: en, clr
  Register #(.width(32), .trigger("rising"), .Select("low")) register_2 (.D(IR), .Q(IR_2), .clk(CLK));  // open: en, clr
endmodule
